// Logisim project cpu21-riscv.circ as structural Verilog: 26 circuits, main circuit ◇单周期RISC-V
module \单周期RISC_V  (
  input  IR1,
  input  IR2,
  input  IR3,
  output RegWrite,
  output MemWrite,
  output [31:0] PC,
  output [31:0] IR,
  output [31:0] RDin,
  output [31:0] MDin,
  output [31:0] LedData
);

  wire ALU_EQU, ALU_LESS, and_1_out, and_2_out, and_3_out, and_5_out, and_6_out, BEQ, BLT, BNE, CLK,
       clock_1_out, comparator_1_eq, comparator_2_eq, comparator_2_lt, d_ff_1_q, ecall, Go, halt, IR1_t,
       IR2_t, IR3_t, IRA, IRB, IRC, JAL, JALR, LB, M2Reg, nand_1_out, not_1_out, not_2_out, not_3_out,
       not_4_out, or_4_out, riscv_probe_1_p2, RST, W1, W2, W3, \单周期硬布线控制器_1_alu_src , \单周期硬布线控制器_1_s_type ;
  wire [1:0] alu_1_result;
  wire [2:0] PC_SRC;
  wire [3:0] \单周期硬布线控制器_1_alu_op ;
  wire [4:0] multiplexer_1_out, multiplexer_3_out;
  wire [7:0] multiplexer_6_out;
  wire [9:0] alu_1_result_2;
  wire [11:0] multiplexer_2_out;
  wire [12:0] CNT_num;
  wire [15:0] \总周期数 ;
  wire [31:0] adder_2_out, adder_3_out, and_4_out, bit_extender_1_out, bit_extender_2_out,
       bit_extender_3_out, bit_extender_4_out, multiplexer_4_out, multiplexer_7_out, multiplexer_8_out,
       NEXT_PC, PC_4, R1, ram_1_data, shifter_1_out, shifter_2_out;
  wire [31:12] alu_1_result_3;

  Button \u_继续运行  (.out(Go));
  Button \u_复位  (.out(RST));
  Button _1 (.out(IRA));
  Button _2 (.out(IRB));
  Button _3 (.out(IRC));
  LED #(.active("true")) led_1 (.in(W1));
  LED #(.active("true")) led_2 (.in(W2));
  LED #(.active("true")) led_3 (.in(W3));
  Hex_Digit_Display hex_digit_display_1 (.value(LedData[31:28]));  // open: dp
  Register #(.width(32), .trigger("rising"), .Select("low")) u_PC (
    .D(NEXT_PC), .en(not_1_out), .Q(PC), .clk(CLK), .clr(RST));
  not not_1 (not_1_out, halt);
  Hex_Digit_Display hex_digit_display_2 (.value(LedData[27:24]));  // open: dp
  Hex_Digit_Display hex_digit_display_3 (.value(LedData[23:20]));  // open: dp
  Hex_Digit_Display hex_digit_display_4 (.value(LedData[19:16]));  // open: dp
  Hex_Digit_Display hex_digit_display_5 (.value(LedData[15:12]));  // open: dp
  // RiscV_Probe riscv_probe_1: pin names not known; wires that end beside it: IR, riscv_probe_1_p2
  Hex_Digit_Display hex_digit_display_6 (.value(LedData[11:8]));  // open: dp
  Hex_Digit_Display hex_digit_display_7 (.value(LedData[7:4]));  // open: dp
  // Probe on \总周期数 
  ROM #(.addrWidth(10), .dataWidth(32), .Select("high")) rom_1 (.addr(PC[11:2]), .data(IR));
  Hex_Digit_Display hex_digit_display_8 (.value(LedData[3:0]));  // open: dp
  \单周期硬布线控制器  \u_单周期硬布线控制器_1  (
    .Funct({IR[30], IR[25], IR[14:12]}), .OP(IR[6:2]), .ALU_OP(\单周期硬布线控制器_1_alu_op ), .MemToReg(M2Reg),
    .MemWrite(MemWrite), .ALU_SRC(\单周期硬布线控制器_1_alu_src ), .RegWrite(RegWrite), .ecall(ecall),
    .S_type(\单周期硬布线控制器_1_s_type ), .Jalr(JALR), .Beq(BEQ), .JAL(JAL), .Bne(BNE), .in_3(IR[21]),
    .uret(riscv_probe_1_p2), .BLT(BLT), .LB(LB));  // open: CSRRSI, CSRRCI
  Multiplexer #(.select(1), .width(5), .disabled("Z"), .enable("false")) multiplexer_1 (
    .in0(IR[19:15]), .in1(5'b01010), .out(multiplexer_1_out), .sel(ecall));
  Multiplexer #(.select(1), .width(12), .disabled("Z"), .enable("false")) multiplexer_2 (
    .in0(IR[31:20]), .in1({IR[31:25], IR[11:7]}), .out(multiplexer_2_out), .sel(\单周期硬布线控制器_1_s_type ));
  or or_1 (IR1_t, IR1, IRA);
  Multiplexer #(.select(1), .width(5), .disabled("Z"), .enable("false")) multiplexer_3 (
    .in0(IR[24:20]), .in1(5'b10001), .out(multiplexer_3_out), .sel(ecall));
  assign bit_extender_1_out = {{20{IR[31]}}, {IR[31], IR[7], IR[30:25], IR[11:8]}};  // Bit_Extender bit_extender_1
  assign bit_extender_2_out = {{12{IR[31]}}, {IR[31], IR[19:12], IR[20], IR[30:21]}};  // Bit_Extender bit_extender_2
  not not_2 (not_2_out, ALU_EQU);
  or or_2 (IR2_t, IR2, IRB);
  Regifile regifile_1 (
    .Din(RDin), .Clk(CLK), .R1(R1), .R2(MDin), .WE(RegWrite), .W_num(IR[11:7]), .R1_num(multiplexer_1_out),
    .R2_num(multiplexer_3_out));
  assign bit_extender_3_out = {{20{multiplexer_2_out[11]}}, multiplexer_2_out};  // Bit_Extender bit_extender_3
  and and_1 (and_1_out, BNE, not_2_out);
  and and_2 (and_2_out, ALU_EQU, BEQ);
  and and_3 (and_3_out, ALU_LESS, BLT);
  Shifter #(.width(32), .shift("ll")) shifter_1 (.in(bit_extender_1_out), .\dist (5'b00001), .out(shifter_1_out));
  Shifter #(.width(32), .shift("ll")) shifter_2 (.in(bit_extender_2_out), .\dist (5'b00001), .out(shifter_2_out));
  or or_3 (IR3_t, IR3, IRC);
  Multiplexer #(.select(1), .width(32), .disabled("Z"), .enable("false")) multiplexer_4 (
    .in0(MDin), .in1(bit_extender_3_out), .out(multiplexer_4_out), .sel(\单周期硬布线控制器_1_alu_src ));
  Adder #(.width(32)) adder_1 (.a(32'h4), .b(PC), .out(PC_4));  // open: cin, cout
  Adder #(.width(32)) adder_2 (.a(shifter_1_out), .b(PC), .out(adder_2_out));  // open: cin, cout
  Adder #(.width(32)) adder_3 (.a(shifter_2_out), .b(PC), .out(adder_3_out));  // open: cin, cout
  ALU alu_1 (
    .X(R1), .Y(multiplexer_4_out), .AluOP(\单周期硬布线控制器_1_alu_op ), .Equal(ALU_EQU),
    .Result({alu_1_result_3, alu_1_result_2, alu_1_result}), .out_6(ALU_LESS));  // open: Result_2, out_4
  assign and_4_out = {alu_1_result_3, alu_1_result_2, alu_1_result} & 32'hfffffffe;  // AND_Gate and_4, 32 bits wide
  Priority_Encoder #(.select(3), .disabled("Z")) priority_encoder_1 (
    .in0(1'b1), .in1(and_1_out), .in2(and_2_out), .in3(JAL), .in4(JALR), .in5(and_3_out), .out(PC_SRC));  // open: in6, in7, gs, en_out, en_in
  RAM #(.addrWidth(10), .dataWidth(32), .bus("separate"), .Select("high")) ram_1 (
    .addr(alu_1_result_2), .din(MDin), .data(ram_1_data), .str(MemWrite), .clk(CLK));  // open: sel, ld, clr
  Multiplexer #(.select(3), .width(32), .disabled("Z"), .enable("false")) multiplexer_5 (
    .in0(PC_4), .in1(adder_2_out), .in2(adder_2_out), .in3(adder_3_out), .in4(and_4_out), .in5(adder_2_out),
    .out(NEXT_PC), .sel(PC_SRC));  // open: in6, in7
  Comparator #(.width(32), .mode("twosComplement")) comparator_1 (
    .a(MDin), .b(32'h22), .eq(comparator_1_eq));  // open: gt, lt
  Multiplexer #(.select(2), .width(8), .disabled("Z"), .enable("false")) multiplexer_6 (
    .in0(ram_1_data[7:0]), .in1(ram_1_data[15:8]), .in2(ram_1_data[23:16]), .in3(ram_1_data[31:24]),
    .out(multiplexer_6_out), .sel(alu_1_result));
  assign bit_extender_4_out = {{24{multiplexer_6_out[7]}}, multiplexer_6_out};  // Bit_Extender bit_extender_4
  D_Flip_Flop #(.trigger("high"), .Pre_Clr_Positions("LEGACY"), .NegatePresetClear("false"), .enable("true"), .NewFFLayout("false")) d_ff_1 (.Q(d_ff_1_q));  // open: clk, D, Qn, preset, en, reset
  // Probe on 13'hc
  and and_5 (and_5_out, ecall, comparator_1_eq);
  Multiplexer #(.select(1), .width(32), .disabled("Z"), .enable("false")) multiplexer_7 (
    .in0(ram_1_data), .in1(bit_extender_4_out), .out(multiplexer_7_out), .sel(LB));
  Comparator #(.width(13), .mode("twosComplement")) comparator_2 (
    .a(CNT_num), .b(13'hc), .eq(comparator_2_eq), .lt(comparator_2_lt));  // open: gt
  Clock #(.highDuration(1), .lowDuration(1)) clock_1 (.out(clock_1_out));
  Register #(.width(32), .trigger("rising"), .Select("low")) register_1 (
    .D(R1), .en(and_5_out), .Q(LedData), .clk(CLK), .clr(RST));
  Counter #(.width(13), .max('h1fff), .ongoal("stay"), .trigger("rising"), .behavior("old")) counter_1 (
    .count(comparator_2_lt), .Q(CNT_num), .clk(clock_1_out));  // open: load, D, carry, clr, preset
  not not_3 (not_3_out, comparator_1_eq);
  Multiplexer #(.select(1), .width(32), .disabled("Z"), .enable("false")) multiplexer_8 (
    .in0({alu_1_result_3, alu_1_result_2, alu_1_result}), .in1(multiplexer_7_out), .out(multiplexer_8_out),
    .sel(M2Reg));
  nand nand_1 (nand_1_out, d_ff_1_q, comparator_2_eq);
  or or_4 (or_4_out, JAL, JALR);
  assign CLK = nand_1_out ? clock_1_out : 1'bz;  // Controlled_Buffer controlled_buffer_1
  Pull_Resistor #(.pull(1)) pull_resistor_1 (.node(CLK));
  and and_6 (and_6_out, ecall, not_3_out);
  Multiplexer #(.select(1), .width(32), .disabled("Z"), .enable("false")) multiplexer_9 (
    .in0(multiplexer_8_out), .in1(PC_4), .out(RDin), .sel(or_4_out));
  not not_4 (not_4_out, halt);
  Counter #(.width(16), .max('hffff), .ongoal("wrap"), .trigger("rising"), .behavior("new")) counter_2 (
    .count(not_4_out), .Q(\总周期数 ), .clk(CLK), .clr(RST));  // open: load, D, carry, preset, down
  Register #(.width(1), .trigger("falling"), .Select("low")) register_2 (
    .D(and_6_out), .en(not_4_out), .Q(halt), .clk(CLK), .clr(Go));

  // Other names for the same wires on the sheet: R2[31:0] = MDin

  // Notes on the sheet:
  //   中断源
  //   中断等待指示
  //   数码管输出应该用寄存器锁存，否则显示数据只能一闪而过
  //   数码管输出
  //   指令探针
  //   指令存储器
  //   指令字
  //   contents of rom_1 (hex, n*v repeats v):
  //   100493 100006f 100493 200913 300993 100006f 100493 200913 300993 100006f 100493 200913 300993
  //   100006f 100493 200913 300993 3cc000ef 100413 100493 1f49493 900533 2200893 73 24d493 48463 fedff06f
  //   900533 2200893 73 100493 249493 900533 2200893 73 48463 fedff06f 100493 1f49493 900533 2200893 73
  //   4034d493 900533 2200893 73 4044d493 900533 2200893 73 4044d493 900533 2200893 73 4044d493 900533
  //   2200893 73 4044d493 900533 2200893 73 4044d493 900533 2200893 73 4044d493 900533 2200893 73 4044d493
  //   900533 2200893 73 100413 1f41993 41f9d993 433 c00913 300b13 140413 f47413 800293 100313 499993
  //   89e9b3 1300533 2200893 73 406282b3 fe0294e3 140413 f00f93 1f47433 1c41413 800293 100313 49d993
  //   89e9b3 1300533 2200893 73 406282b3 fe0294e3 1c45413 406b0b33 b0463 f95ff06f 2b3 fff2c293 829293
  //   ff2e293 500533 2200893 73 fff00413 493 84a023 140413 448493 84a023 140413 448493 84a023 140413
  //   448493 84a023 140413 448493 84a023 140413 448493 84a023 140413 448493 84a023 140413 448493 84a023
  //   140413 448493 84a023 140413 448493 84a023 140413 448493 84a023 140413 448493 84a023 140413 448493
  //   84a023 140413 448493 84a023 140413 448493 84a023 140413 448493 84a023 140413 448493 140413 433
  //   3c00493 42983 4aa03 149a2b3 28663 134a023 1442023 ffc48493 fe9412e3 800533 2200893 73 440413 3c00493
  //   fc9416e3 3200893 73 100293 300313 800493 849493 7648493 1449493 900533 2200893 73 800e13 4054d4b3
  //   4064d4b3 900533 2200893 73 fffe0e13 fe0e14e3 a00893 73 fff00293 7700493 849493 7748493 900533
  //   2200893 73 1000e13 54c4b3 900533 2200893 73 fffe0e13 fe0e16e3 a00893 73 313 1000e13 13 8400493
  //   849493 8348493 400913 891913 490913 849493 8248493 849493 8148493 891913 490913 891913 490913 932023
  //   12484b3 430313 fffe0e13 fe0e18e3 2000e13 313 30483 900533 2200893 73 130313 fffe0e13 fe0e14e3 a00893
  //   73 ff100493 900533 2200893 73 148493 fe04c8e3 a00893 73 413 140413 800533 2200893 73 240413 800533
  //   2200893 73 340413 800533 2200893 73 440413 800533 2200893 73 540413 800533 2200893 73 640413 800533
  //   2200893 73 740413 800533 2200893 73 840413 800533 2200893 2200893 73 8067
  //   JAL
  //   JALR
  //   URET
  //   R1
  //   a0
  //   R2
  //   I 指令
  //   S 指令
  //   B 指令
  //   J 指令
  //   Beq
  //   Bne
  //   MemToReg
  //   MemWrite
  //   AluOP
  //   AluSrcB
  //   RegWrite
  //   a7
  //   数据存储器
  //   为方便自动评测，需要输出PC，IR，寄存器堆写如数据RDin
  //   RAM写使能MemWrite、RAM写入数据MDin等信号
  //   控制位
  //   暂停节拍，不能为0
  //   戳工具置1进入计数暂停模式，ctrl+k时钟自动运行到对应节拍暂停
  //   ctrl+k关闭时钟连续运行，将控制位置零，进入单步调试模式调试
  //   用这个时钟源需要去掉电路中的其他时钟源
  //   可计数暂停的时钟源
endmodule

// 单周期硬布线控制器
module \单周期硬布线控制器  (
  input  [4:0] OP,
  input  [4:0] Funct,
  input  in_3,
  output [3:0] ALU_OP,
  output uret,
  output MemToReg,
  output ecall,
  output MemWrite,
  output ALU_SRC,
  output RegWrite,
  output S_type,
  output Beq,
  output Bne,
  output Jalr,
  output JAL,
  output LB,
  output BLT,
  output CSRRSI,
  output CSRRCI
);

  wire \控制信号自动生成_1_ecall ;

  \运算控制器自动生成  \u_运算控制器自动生成_1  (
    .OP2(OP[0]), .OP3(OP[1]), .OP4(OP[2]), .OP5(OP[3]), .OP6(OP[4]), .F12(Funct[0]), .F13(Funct[1]),
    .F14(Funct[2]), .F25(Funct[3]), .F30(Funct[4]), .S0(ALU_OP[0]), .S1(ALU_OP[1]), .S2(ALU_OP[2]),
    .S3(ALU_OP[3]));
  \控制信号自动生成  \u_控制信号自动生成_1  (
    .OP2(OP[0]), .OP3(OP[1]), .OP4(OP[2]), .OP5(OP[3]), .MemToReg(MemToReg), .OP6(OP[4]), .F12(Funct[0]),
    .F13(Funct[1]), .F14(Funct[2]), .F25(Funct[3]), .F30(Funct[4]), .CSRRSI(CSRRSI), .CSRRCI(CSRRCI),
    .MemWrite(MemWrite), .ALU_SRC(ALU_SRC), .RegWrite(RegWrite), .ecall(\控制信号自动生成_1_ecall ), .S_Type(S_type),
    .BEQ(Beq), .BNE(Bne), .JALR(Jalr), .JAL(JAL), .LB(LB), .BLT(BLT));
  and and_1 (uret, in_3, \控制信号自动生成_1_ecall );
  and and_2 (ecall, ~in_3, \控制信号自动生成_1_ecall );  // AND_Gate

  // Other names for the same wires on the sheet: IR21 = in_3; OP_CODE[4:0] = OP

  // Notes on the sheet:
  //   运算器控制器，根据指令生成运算器功能选择信号
  //   控制信号生成，产生数据通路需要的其他控制信号
endmodule

// 运算器控制器
module \运算控制器自动生成  (
  input  OP2,
  input  OP3,
  input  OP4,
  input  OP5,
  input  OP6,
  input  F12,
  input  F13,
  input  F14,
  input  F25,
  input  F30,
  output S0,
  output S1,
  output S2,
  output S3
);

  wire and_1_out, and_2_out, and_3_out, and_4_out, and_5_out, and_6_out, and_7_out, and_8_out, and_9_out,
       and_10_out, and_11_out, and_12_out, and_13_out, and_14_out, and_15_out, and_16_out, and_17_out,
       and_18_out, and_19_out, and_20_out, and_21_out, and_22_out, and_23_out, and_24_out, and_25_out,
       and_26_out, and_27_out, and_28_out, and_29_out, and_30_out, and_31_out, and_32_out, and_33_out,
       and_34_out, and_35_out, and_36_out, and_37_out, and_38_out, not_1_out, not_2_out, not_3_out,
       not_4_out, not_5_out, not_6_out, not_7_out, not_8_out, not_9_out, not_10_out, not_11_out, not_12_out,
       not_13_out, not_14_out, not_15_out, not_16_out, not_17_out, not_18_out, not_19_out, not_20_out,
       not_21_out, not_22_out, not_23_out, not_24_out, not_25_out, not_26_out, not_27_out, not_28_out,
       not_29_out, not_30_out, not_31_out, not_32_out, not_33_out, not_34_out, not_35_out, not_36_out,
       not_37_out, not_38_out, not_39_out, not_40_out, not_41_out, not_42_out, not_43_out, not_44_out,
       not_45_out, not_46_out, not_47_out, not_48_out, not_49_out, not_50_out, not_51_out, not_52_out,
       not_53_out, not_54_out, not_55_out, not_56_out, not_57_out, not_58_out, not_59_out, not_60_out,
       not_61_out, not_62_out, not_63_out, not_64_out, not_65_out, not_66_out, not_67_out, not_68_out,
       not_69_out, not_70_out, not_71_out, not_72_out, not_73_out, not_74_out, not_75_out, not_76_out,
       not_77_out, not_78_out, not_79_out, not_80_out, not_81_out, not_82_out, not_83_out, not_84_out,
       not_85_out, not_86_out, not_87_out, not_88_out, not_89_out, not_90_out, not_91_out, not_92_out,
       not_93_out, not_94_out, not_95_out, not_96_out, not_97_out, not_98_out, not_99_out, not_100_out,
       not_101_out, not_102_out, not_103_out, not_104_out, not_105_out, not_106_out, not_107_out,
       not_108_out, not_109_out, not_110_out, not_111_out, not_112_out, not_113_out, not_114_out,
       not_115_out, not_116_out, not_117_out, not_118_out, not_119_out, not_120_out, not_121_out,
       not_122_out, not_123_out, not_124_out, not_125_out, not_126_out, not_127_out, not_128_out,
       not_129_out, not_130_out, not_131_out, not_132_out, not_133_out, not_134_out, not_135_out,
       not_136_out, not_137_out, not_138_out, not_139_out, not_140_out, not_141_out, not_142_out,
       not_143_out, not_144_out, not_145_out, not_146_out, not_147_out, not_148_out, not_149_out,
       not_150_out, not_151_out, not_152_out, not_153_out, not_154_out, not_155_out, not_156_out,
       not_157_out, not_158_out, not_159_out, not_160_out, not_161_out, not_162_out, not_163_out,
       not_164_out, not_165_out, not_166_out, not_167_out, not_168_out, not_169_out, not_170_out,
       not_171_out, not_172_out, not_173_out, not_174_out, not_175_out, not_176_out, not_177_out,
       not_178_out, not_179_out, not_180_out, not_181_out, not_182_out, not_183_out, not_184_out,
       not_185_out, not_186_out, not_187_out, not_188_out, not_189_out, not_190_out, not_191_out,
       not_192_out, not_193_out, not_194_out, not_195_out, not_196_out, not_197_out, not_198_out,
       not_199_out, not_200_out, not_201_out, not_202_out, not_203_out, not_204_out, not_205_out,
       not_206_out, not_207_out, not_208_out, not_209_out, not_210_out, not_211_out, not_212_out,
       not_213_out, not_214_out, not_215_out, not_216_out, not_217_out, not_218_out, not_219_out,
       not_220_out, not_221_out, not_222_out, not_223_out, not_224_out, not_225_out, not_226_out,
       not_227_out, not_228_out, not_229_out, not_230_out, not_231_out, not_232_out, not_233_out, not_234_out;

  not not_1 (not_1_out, F30);
  not not_2 (not_2_out, F25);
  not not_3 (not_3_out, F14);
  not not_4 (not_4_out, F13);
  not not_5 (not_5_out, F12);
  not not_6 (not_6_out, OP6);
  not not_7 (not_7_out, OP3);
  not not_8 (not_8_out, OP2);
  not not_9 (not_9_out, F30);
  not not_10 (not_10_out, F25);
  not not_11 (not_11_out, OP6);
  not not_12 (not_12_out, OP3);
  not not_13 (not_13_out, OP2);
  not not_14 (not_14_out, F30);
  not not_15 (not_15_out, F25);
  not not_16 (not_16_out, F14);
  not not_17 (not_17_out, F12);
  not not_18 (not_18_out, OP6);
  not not_19 (not_19_out, OP3);
  not not_20 (not_20_out, OP2);
  not not_21 (not_21_out, F14);
  not not_22 (not_22_out, F13);
  not not_23 (not_23_out, F12);
  not not_24 (not_24_out, OP6);
  not not_25 (not_25_out, OP5);
  not not_26 (not_26_out, OP3);
  not not_27 (not_27_out, OP2);
  not not_28 (not_28_out, OP6);
  not not_29 (not_29_out, OP5);
  not not_30 (not_30_out, OP3);
  not not_31 (not_31_out, OP2);
  not not_32 (not_32_out, F13);
  not not_33 (not_33_out, F12);
  not not_34 (not_34_out, OP6);
  not not_35 (not_35_out, OP5);
  not not_36 (not_36_out, OP3);
  not not_37 (not_37_out, OP2);
  not not_38 (not_38_out, F14);
  not not_39 (not_39_out, F12);
  not not_40 (not_40_out, OP6);
  not not_41 (not_41_out, OP5);
  not not_42 (not_42_out, OP3);
  not not_43 (not_43_out, OP2);
  not not_44 (not_44_out, F25);
  not not_45 (not_45_out, F13);
  not not_46 (not_46_out, OP6);
  not not_47 (not_47_out, OP5);
  not not_48 (not_48_out, OP3);
  not not_49 (not_49_out, OP2);
  not not_50 (not_50_out, F14);
  not not_51 (not_51_out, F12);
  not not_52 (not_52_out, OP6);
  not not_53 (not_53_out, OP5);
  not not_54 (not_54_out, OP4);
  not not_55 (not_55_out, OP3);
  not not_56 (not_56_out, OP2);
  not not_57 (not_57_out, F14);
  not not_58 (not_58_out, F12);
  not not_59 (not_59_out, OP6);
  not not_60 (not_60_out, OP4);
  not not_61 (not_61_out, OP3);
  not not_62 (not_62_out, OP2);
  not not_63 (not_63_out, F25);
  not not_64 (not_64_out, F13);
  not not_65 (not_65_out, OP6);
  not not_66 (not_66_out, OP3);
  not not_67 (not_67_out, OP2);
  not not_68 (not_68_out, F30);
  not not_69 (not_69_out, F25);
  not not_70 (not_70_out, F13);
  not not_71 (not_71_out, F12);
  not not_72 (not_72_out, OP6);
  not not_73 (not_73_out, OP3);
  not not_74 (not_74_out, OP2);
  not not_75 (not_75_out, F14);
  not not_76 (not_76_out, F13);
  not not_77 (not_77_out, F12);
  not not_78 (not_78_out, OP6);
  not not_79 (not_79_out, OP5);
  not not_80 (not_80_out, OP4);
  not not_81 (not_81_out, OP3);
  not not_82 (not_82_out, OP2);
  not not_83 (not_83_out, F13);
  not not_84 (not_84_out, F12);
  not not_85 (not_85_out, OP4);
  not not_86 (not_86_out, OP3);
  not not_87 (not_87_out, OP2);
  not not_88 (not_88_out, F25);
  not not_89 (not_89_out, F14);
  not not_90 (not_90_out, F13);
  not not_91 (not_91_out, F12);
  not not_92 (not_92_out, OP6);
  not not_93 (not_93_out, OP3);
  not not_94 (not_94_out, OP2);
  not not_95 (not_95_out, F30);
  not not_96 (not_96_out, F25);
  not not_97 (not_97_out, OP6);
  not not_98 (not_98_out, OP3);
  not not_99 (not_99_out, OP2);
  not not_100 (not_100_out, F30);
  not not_101 (not_101_out, F25);
  not not_102 (not_102_out, F14);
  not not_103 (not_103_out, F12);
  not not_104 (not_104_out, OP6);
  not not_105 (not_105_out, OP3);
  not not_106 (not_106_out, OP2);
  not not_107 (not_107_out, OP6);
  not not_108 (not_108_out, OP5);
  not not_109 (not_109_out, OP3);
  not not_110 (not_110_out, OP2);
  not not_111 (not_111_out, F14);
  not not_112 (not_112_out, F12);
  not not_113 (not_113_out, OP6);
  not not_114 (not_114_out, OP5);
  not not_115 (not_115_out, OP3);
  not not_116 (not_116_out, OP2);
  not not_117 (not_117_out, F30);
  not not_118 (not_118_out, F25);
  not not_119 (not_119_out, F13);
  not not_120 (not_120_out, OP6);
  not not_121 (not_121_out, OP5);
  not not_122 (not_122_out, OP3);
  not not_123 (not_123_out, OP2);
  not not_124 (not_124_out, F13);
  not not_125 (not_125_out, F12);
  not not_126 (not_126_out, OP4);
  not not_127 (not_127_out, OP3);
  not not_128 (not_128_out, OP2);
  not not_129 (not_129_out, F30);
  not not_130 (not_130_out, F25);
  not not_131 (not_131_out, F14);
  not not_132 (not_132_out, F13);
  not not_133 (not_133_out, F12);
  not not_134 (not_134_out, OP6);
  not not_135 (not_135_out, OP3);
  not not_136 (not_136_out, OP2);
  not not_137 (not_137_out, F25);
  not not_138 (not_138_out, F14);
  not not_139 (not_139_out, F13);
  not not_140 (not_140_out, F12);
  not not_141 (not_141_out, OP6);
  not not_142 (not_142_out, OP3);
  not not_143 (not_143_out, OP2);
  not not_144 (not_144_out, F30);
  not not_145 (not_145_out, F25);
  not not_146 (not_146_out, OP6);
  not not_147 (not_147_out, OP3);
  not not_148 (not_148_out, OP2);
  not not_149 (not_149_out, F30);
  not not_150 (not_150_out, F25);
  not not_151 (not_151_out, F14);
  not not_152 (not_152_out, OP6);
  not not_153 (not_153_out, OP3);
  not not_154 (not_154_out, OP2);
  not not_155 (not_155_out, F14);
  not not_156 (not_156_out, F13);
  not not_157 (not_157_out, F12);
  not not_158 (not_158_out, OP6);
  not not_159 (not_159_out, OP5);
  not not_160 (not_160_out, OP3);
  not not_161 (not_161_out, OP2);
  not not_162 (not_162_out, OP6);
  not not_163 (not_163_out, OP5);
  not not_164 (not_164_out, OP3);
  not not_165 (not_165_out, OP2);
  not not_166 (not_166_out, F14);
  not not_167 (not_167_out, F12);
  not not_168 (not_168_out, OP6);
  not not_169 (not_169_out, OP5);
  not not_170 (not_170_out, OP4);
  not not_171 (not_171_out, OP3);
  not not_172 (not_172_out, OP2);
  not not_173 (not_173_out, F14);
  not not_174 (not_174_out, F12);
  not not_175 (not_175_out, OP6);
  not not_176 (not_176_out, OP4);
  not not_177 (not_177_out, OP3);
  not not_178 (not_178_out, OP2);
  not not_179 (not_179_out, F14);
  not not_180 (not_180_out, F13);
  not not_181 (not_181_out, F12);
  not not_182 (not_182_out, OP6);
  not not_183 (not_183_out, OP5);
  not not_184 (not_184_out, OP4);
  not not_185 (not_185_out, OP3);
  not not_186 (not_186_out, OP2);
  not not_187 (not_187_out, F30);
  not not_188 (not_188_out, F25);
  not not_189 (not_189_out, F12);
  not not_190 (not_190_out, OP6);
  not not_191 (not_191_out, OP3);
  not not_192 (not_192_out, OP2);
  not not_193 (not_193_out, F30);
  not not_194 (not_194_out, F25);
  not not_195 (not_195_out, F14);
  not not_196 (not_196_out, F12);
  not not_197 (not_197_out, OP6);
  not not_198 (not_198_out, OP3);
  not not_199 (not_199_out, OP2);
  not not_200 (not_200_out, F30);
  not not_201 (not_201_out, F25);
  not not_202 (not_202_out, F14);
  not not_203 (not_203_out, OP6);
  not not_204 (not_204_out, OP3);
  not not_205 (not_205_out, OP2);
  not not_206 (not_206_out, F12);
  not not_207 (not_207_out, OP6);
  not not_208 (not_208_out, OP5);
  not not_209 (not_209_out, OP3);
  not not_210 (not_210_out, OP2);
  not not_211 (not_211_out, F13);
  not not_212 (not_212_out, F12);
  not not_213 (not_213_out, OP6);
  not not_214 (not_214_out, OP5);
  not not_215 (not_215_out, OP3);
  not not_216 (not_216_out, OP2);
  not not_217 (not_217_out, F14);
  not not_218 (not_218_out, F12);
  not not_219 (not_219_out, OP6);
  not not_220 (not_220_out, OP5);
  not not_221 (not_221_out, OP3);
  not not_222 (not_222_out, OP2);
  not not_223 (not_223_out, F30);
  not not_224 (not_224_out, F25);
  not not_225 (not_225_out, F13);
  not not_226 (not_226_out, F12);
  not not_227 (not_227_out, OP6);
  not not_228 (not_228_out, OP3);
  not not_229 (not_229_out, OP2);
  not not_230 (not_230_out, F13);
  not not_231 (not_231_out, F12);
  not not_232 (not_232_out, OP4);
  not not_233 (not_233_out, OP3);
  not not_234 (not_234_out, OP2);
  and and_1 (and_1_out, not_1_out, not_2_out, not_3_out, not_4_out, not_5_out, not_6_out, OP5, OP4, not_7_out, not_8_out);
  and and_2 (and_2_out, not_9_out, not_10_out, F14, F13, F12, not_11_out, OP5, OP4, not_12_out, not_13_out);
  and and_3 (and_3_out, not_14_out, not_15_out, not_16_out, F13, not_17_out, not_18_out, OP5, OP4, not_19_out, not_20_out);
  and and_4 (and_4_out, not_21_out, not_22_out, not_23_out, not_24_out, not_25_out, OP4, not_26_out, not_27_out);
  and and_5 (and_5_out, F14, F13, F12, not_28_out, not_29_out, OP4, not_30_out, not_31_out);
  and and_6 (and_6_out, F14, not_32_out, not_33_out, not_34_out, not_35_out, OP4, not_36_out, not_37_out);
  and and_7 (and_7_out, not_38_out, F13, not_39_out, not_40_out, not_41_out, OP4, not_42_out, not_43_out);
  and and_8 (and_8_out, F30, not_44_out, F14, not_45_out, F12, not_46_out, not_47_out, OP4, not_48_out, not_49_out);
  and and_9 (and_9_out, not_50_out, F13, not_51_out, not_52_out, not_53_out, not_54_out, not_55_out, not_56_out);
  and and_10 (and_10_out, not_57_out, F13, not_58_out, not_59_out, OP5, not_60_out, not_61_out, not_62_out);
  and and_11 (and_11_out, F30, not_63_out, F14, not_64_out, F12, not_65_out, OP5, OP4, not_66_out, not_67_out);
  and and_12 (and_12_out, not_68_out, not_69_out, F14, not_70_out, not_71_out, not_72_out, OP5, OP4, not_73_out, not_74_out);
  and and_13 (and_13_out, not_75_out, not_76_out, not_77_out, not_78_out, not_79_out, not_80_out, not_81_out, not_82_out);
  and and_14 (and_14_out, F14, not_83_out, not_84_out, OP6, OP5, not_85_out, not_86_out, not_87_out);
  and and_15 (and_15_out, F30, not_88_out, not_89_out, not_90_out, not_91_out, not_92_out, OP5, OP4, not_93_out, not_94_out);
  and and_16 (and_16_out, not_95_out, not_96_out, F14, F13, F12, not_97_out, OP5, OP4, not_98_out, not_99_out);
  and and_17 (and_17_out, not_100_out, not_101_out, not_102_out, F13, not_103_out, not_104_out, OP5, OP4, not_105_out, not_106_out);
  and and_18 (and_18_out, F14, F13, F12, not_107_out, not_108_out, OP4, not_109_out, not_110_out);
  and and_19 (and_19_out, not_111_out, F13, not_112_out, not_113_out, not_114_out, OP4, not_115_out, not_116_out);
  and and_20 (and_20_out, not_117_out, not_118_out, F14, not_119_out, F12, not_120_out, not_121_out, OP4, not_122_out, not_123_out);
  and and_21 (and_21_out, F14, not_124_out, not_125_out, OP6, OP5, not_126_out, not_127_out, not_128_out);
  and and_22 (and_22_out, not_129_out, not_130_out, not_131_out, not_132_out, not_133_out, not_134_out, OP5, OP4, not_135_out, not_136_out);
  and and_23 (and_23_out, F30, not_137_out, not_138_out, not_139_out, not_140_out, not_141_out, OP5, OP4, not_142_out, not_143_out);
  and and_24 (and_24_out, not_144_out, not_145_out, F14, F13, F12, not_146_out, OP5, OP4, not_147_out, not_148_out);
  and and_25 (and_25_out, not_149_out, not_150_out, not_151_out, F13, F12, not_152_out, OP5, OP4, not_153_out, not_154_out);
  and and_26 (and_26_out, not_155_out, not_156_out, not_157_out, not_158_out, not_159_out, OP4, not_160_out, not_161_out);
  and and_27 (and_27_out, F14, F13, F12, not_162_out, not_163_out, OP4, not_164_out, not_165_out);
  and and_28 (and_28_out, not_166_out, F13, not_167_out, not_168_out, not_169_out, not_170_out, not_171_out, not_172_out);
  and and_29 (and_29_out, not_173_out, F13, not_174_out, not_175_out, OP5, not_176_out, not_177_out, not_178_out);
  and and_30 (and_30_out, not_179_out, not_180_out, not_181_out, not_182_out, not_183_out, not_184_out, not_185_out, not_186_out);
  and and_31 (and_31_out, not_187_out, not_188_out, F14, F13, not_189_out, not_190_out, OP5, OP4, not_191_out, not_192_out);
  and and_32 (and_32_out, not_193_out, not_194_out, not_195_out, F13, not_196_out, not_197_out, OP5, OP4, not_198_out, not_199_out);
  and and_33 (and_33_out, not_200_out, not_201_out, not_202_out, F13, F12, not_203_out, OP5, OP4, not_204_out, not_205_out);
  and and_34 (and_34_out, F14, F13, not_206_out, not_207_out, not_208_out, OP4, not_209_out, not_210_out);
  and and_35 (and_35_out, F14, not_211_out, not_212_out, not_213_out, not_214_out, OP4, not_215_out, not_216_out);
  and and_36 (and_36_out, not_217_out, F13, not_218_out, not_219_out, not_220_out, OP4, not_221_out, not_222_out);
  and and_37 (and_37_out, not_223_out, not_224_out, F14, not_225_out, not_226_out, not_227_out, OP5, OP4, not_228_out, not_229_out);
  and and_38 (and_38_out, F14, not_230_out, not_231_out, OP6, OP5, not_232_out, not_233_out, not_234_out);
  or or_1 (S0, and_1_out, and_2_out, and_3_out, and_4_out, and_5_out, and_6_out, and_7_out, and_8_out, and_9_out, and_10_out, and_11_out, and_12_out, and_13_out, and_14_out);
  or or_2 (S1, and_15_out, and_16_out, and_17_out, and_18_out, and_19_out, and_20_out, and_21_out);
  or or_3 (S2, and_22_out, and_23_out, and_24_out, and_25_out, and_26_out, and_27_out, and_28_out, and_29_out, and_30_out);
  or or_4 (S3, and_31_out, and_32_out, and_33_out, and_34_out, and_35_out, and_36_out, and_37_out, and_38_out);
endmodule

// 控制信号生成
module \控制信号自动生成  (
  input  OP2,
  input  OP3,
  input  OP4,
  input  OP5,
  input  OP6,
  input  F12,
  input  F13,
  input  F14,
  input  F25,
  input  F30,
  output MemToReg,
  output CSRRSI,
  output CSRRCI,
  output MemWrite,
  output ALU_SRC,
  output RegWrite,
  output ecall,
  output S_Type,
  output BEQ,
  output BNE,
  output JALR,
  output JAL,
  output LB,
  output BLT
);

  wire and_1_out, and_2_out, and_6_out, and_7_out, and_8_out, and_9_out, and_10_out, and_11_out, and_12_out,
       and_13_out, and_14_out, and_15_out, and_16_out, and_17_out, and_18_out, and_19_out, and_20_out,
       and_21_out, and_22_out, and_23_out, and_24_out, and_25_out, and_26_out, not_1_out, not_2_out,
       not_3_out, not_4_out, not_5_out, not_6_out, not_7_out, not_8_out, not_9_out, not_10_out, not_11_out,
       not_12_out, not_13_out, not_14_out, not_15_out, not_16_out, not_17_out, not_18_out, not_19_out,
       not_20_out, not_21_out, not_22_out, not_23_out, not_24_out, not_25_out, not_26_out, not_27_out,
       not_28_out, not_29_out, not_30_out, not_31_out, not_32_out, not_33_out, not_34_out, not_35_out,
       not_36_out, not_37_out, not_38_out, not_39_out, not_40_out, not_41_out, not_42_out, not_43_out,
       not_44_out, not_45_out, not_46_out, not_47_out, not_48_out, not_49_out, not_50_out, not_51_out,
       not_52_out, not_53_out, not_54_out, not_55_out, not_56_out, not_57_out, not_58_out, not_59_out,
       not_60_out, not_61_out, not_62_out, not_63_out, not_64_out, not_65_out, not_66_out, not_67_out,
       not_68_out, not_69_out, not_70_out, not_71_out, not_72_out, not_73_out, not_74_out, not_75_out,
       not_76_out, not_77_out, not_78_out, not_79_out, not_80_out, not_81_out, not_82_out, not_83_out,
       not_84_out, not_85_out, not_86_out, not_87_out, not_88_out, not_89_out, not_90_out, not_91_out,
       not_92_out, not_93_out, not_94_out, not_95_out, not_96_out, not_97_out, not_98_out, not_99_out,
       not_100_out, not_101_out, not_102_out, not_103_out, not_104_out, not_105_out, not_106_out,
       not_107_out, not_108_out, not_109_out, not_110_out, not_111_out, not_112_out, not_113_out,
       not_114_out, not_115_out, not_116_out, not_117_out, not_118_out, not_119_out, not_120_out,
       not_121_out, not_122_out, not_123_out, not_124_out, not_125_out, not_126_out, not_127_out,
       not_128_out, not_129_out, not_130_out, not_131_out, not_132_out, not_133_out, not_134_out,
       not_135_out, not_136_out, not_137_out, not_138_out, not_139_out, not_140_out, not_141_out,
       not_142_out, not_143_out, not_144_out, not_145_out, not_146_out, not_147_out, not_148_out,
       not_149_out, not_150_out, not_151_out, not_152_out, not_153_out, not_154_out, not_155_out,
       not_156_out, not_157_out, not_158_out, not_159_out, not_160_out, not_161_out, not_162_out,
       not_163_out, not_164_out, not_165_out, not_166_out, not_167_out, not_168_out, not_169_out,
       not_170_out, not_171_out, not_172_out, not_173_out, not_174_out, not_175_out, not_176_out,
       not_177_out, not_178_out, not_179_out, not_180_out, not_181_out, not_182_out, not_183_out,
       not_184_out, not_185_out, not_186_out, not_187_out, not_188_out, not_189_out;

  not not_1 (not_1_out, F14);
  not not_2 (not_2_out, F12);
  not not_3 (not_3_out, OP6);
  not not_4 (not_4_out, OP5);
  not not_5 (not_5_out, OP4);
  not not_6 (not_6_out, OP3);
  not not_7 (not_7_out, OP2);
  not not_8 (not_8_out, F14);
  not not_9 (not_9_out, F13);
  not not_10 (not_10_out, F12);
  not not_11 (not_11_out, OP6);
  not not_12 (not_12_out, OP5);
  not not_13 (not_13_out, OP4);
  not not_14 (not_14_out, OP3);
  not not_15 (not_15_out, OP2);
  not not_16 (not_16_out, F12);
  not not_17 (not_17_out, OP3);
  not not_18 (not_18_out, OP2);
  not not_19 (not_19_out, OP3);
  not not_20 (not_20_out, OP2);
  not not_21 (not_21_out, F14);
  not not_22 (not_22_out, F12);
  not not_23 (not_23_out, OP6);
  not not_24 (not_24_out, OP4);
  not not_25 (not_25_out, OP3);
  not not_26 (not_26_out, OP2);
  not not_27 (not_27_out, F14);
  not not_28 (not_28_out, F13);
  not not_29 (not_29_out, F12);
  not not_30 (not_30_out, OP6);
  not not_31 (not_31_out, OP5);
  not not_32 (not_32_out, OP3);
  not not_33 (not_33_out, OP2);
  not not_34 (not_34_out, OP6);
  not not_35 (not_35_out, OP5);
  not not_36 (not_36_out, OP3);
  not not_37 (not_37_out, OP2);
  not not_38 (not_38_out, F12);
  not not_39 (not_39_out, OP6);
  not not_40 (not_40_out, OP5);
  not not_41 (not_41_out, OP3);
  not not_42 (not_42_out, OP2);
  not not_43 (not_43_out, F13);
  not not_44 (not_44_out, F12);
  not not_45 (not_45_out, OP6);
  not not_46 (not_46_out, OP5);
  not not_47 (not_47_out, OP3);
  not not_48 (not_48_out, OP2);
  not not_49 (not_49_out, F14);
  not not_50 (not_50_out, F12);
  not not_51 (not_51_out, OP6);
  not not_52 (not_52_out, OP5);
  not not_53 (not_53_out, OP3);
  not not_54 (not_54_out, OP2);
  not not_55 (not_55_out, F30);
  not not_56 (not_56_out, F25);
  not not_57 (not_57_out, F14);
  not not_58 (not_58_out, F13);
  not not_59 (not_59_out, OP6);
  not not_60 (not_60_out, OP5);
  not not_61 (not_61_out, OP3);
  not not_62 (not_62_out, OP2);
  not not_63 (not_63_out, F30);
  not not_64 (not_64_out, F25);
  not not_65 (not_65_out, F13);
  not not_66 (not_66_out, OP6);
  not not_67 (not_67_out, OP5);
  not not_68 (not_68_out, OP3);
  not not_69 (not_69_out, OP2);
  not not_70 (not_70_out, F25);
  not not_71 (not_71_out, F13);
  not not_72 (not_72_out, OP6);
  not not_73 (not_73_out, OP5);
  not not_74 (not_74_out, OP3);
  not not_75 (not_75_out, OP2);
  not not_76 (not_76_out, F14);
  not not_77 (not_77_out, F12);
  not not_78 (not_78_out, OP6);
  not not_79 (not_79_out, OP5);
  not not_80 (not_80_out, OP4);
  not not_81 (not_81_out, OP3);
  not not_82 (not_82_out, OP2);
  not not_83 (not_83_out, F14);
  not not_84 (not_84_out, F12);
  not not_85 (not_85_out, OP6);
  not not_86 (not_86_out, OP4);
  not not_87 (not_87_out, OP3);
  not not_88 (not_88_out, OP2);
  not not_89 (not_89_out, F14);
  not not_90 (not_90_out, F13);
  not not_91 (not_91_out, F12);
  not not_92 (not_92_out, OP6);
  not not_93 (not_93_out, OP5);
  not not_94 (not_94_out, OP4);
  not not_95 (not_95_out, OP3);
  not not_96 (not_96_out, OP2);
  not not_97 (not_97_out, OP2);
  not not_98 (not_98_out, OP3);
  not not_99 (not_99_out, OP5);
  not not_100 (not_100_out, OP6);
  not not_101 (not_101_out, F12);
  not not_102 (not_102_out, F14);
  not not_103 (not_103_out, OP2);
  not not_104 (not_104_out, OP3);
  not not_105 (not_105_out, OP5);
  not not_106 (not_106_out, OP6);
  not not_107 (not_107_out, F12);
  not not_108 (not_108_out, OP2);
  not not_109 (not_109_out, OP3);
  not not_110 (not_110_out, OP5);
  not not_111 (not_111_out, OP6);
  not not_112 (not_112_out, F13);
  not not_113 (not_113_out, F25);
  not not_114 (not_114_out, F30);
  not not_115 (not_115_out, OP2);
  not not_116 (not_116_out, OP3);
  not not_117 (not_117_out, OP6);
  not not_118 (not_118_out, F12);
  not not_119 (not_119_out, F13);
  not not_120 (not_120_out, F14);
  not not_121 (not_121_out, F25);
  not not_122 (not_122_out, OP2);
  not not_123 (not_123_out, OP3);
  not not_124 (not_124_out, OP6);
  not not_125 (not_125_out, F12);
  not not_126 (not_126_out, F25);
  not not_127 (not_127_out, F30);
  not not_128 (not_128_out, OP2);
  not not_129 (not_129_out, OP3);
  not not_130 (not_130_out, OP5);
  not not_131 (not_131_out, OP6);
  not not_132 (not_132_out, OP2);
  not not_133 (not_133_out, OP3);
  not not_134 (not_134_out, OP6);
  not not_135 (not_135_out, F13);
  not not_136 (not_136_out, F25);
  not not_137 (not_137_out, OP2);
  not not_138 (not_138_out, OP3);
  not not_139 (not_139_out, OP6);
  not not_140 (not_140_out, F25);
  not not_141 (not_141_out, F30);
  not not_142 (not_142_out, OP4);
  not not_143 (not_143_out, F12);
  not not_144 (not_144_out, F13);
  not not_145 (not_145_out, F14);
  not not_146 (not_146_out, OP4);
  not not_147 (not_147_out, F30);
  not not_148 (not_148_out, F25);
  not not_149 (not_149_out, F14);
  not not_150 (not_150_out, F13);
  not not_151 (not_151_out, F12);
  not not_152 (not_152_out, OP3);
  not not_153 (not_153_out, OP2);
  not not_154 (not_154_out, F14);
  not not_155 (not_155_out, F12);
  not not_156 (not_156_out, OP6);
  not not_157 (not_157_out, OP4);
  not not_158 (not_158_out, OP3);
  not not_159 (not_159_out, OP2);
  not not_160 (not_160_out, F14);
  not not_161 (not_161_out, F13);
  not not_162 (not_162_out, F12);
  not not_163 (not_163_out, OP4);
  not not_164 (not_164_out, OP3);
  not not_165 (not_165_out, OP2);
  not not_166 (not_166_out, F14);
  not not_167 (not_167_out, F13);
  not not_168 (not_168_out, OP4);
  not not_169 (not_169_out, OP3);
  not not_170 (not_170_out, OP2);
  not not_171 (not_171_out, F14);
  not not_172 (not_172_out, F13);
  not not_173 (not_173_out, F12);
  not not_174 (not_174_out, OP4);
  not not_175 (not_175_out, OP3);
  not not_176 (not_176_out, OP4);
  not not_177 (not_177_out, F14);
  not not_178 (not_178_out, F13);
  not not_179 (not_179_out, F12);
  not not_180 (not_180_out, OP6);
  not not_181 (not_181_out, OP5);
  not not_182 (not_182_out, OP4);
  not not_183 (not_183_out, OP3);
  not not_184 (not_184_out, OP2);
  not not_185 (not_185_out, F13);
  not not_186 (not_186_out, F12);
  not not_187 (not_187_out, OP4);
  not not_188 (not_188_out, OP3);
  not not_189 (not_189_out, OP2);
  and and_1 (and_1_out, not_1_out, F13, not_2_out, not_3_out, not_4_out, not_5_out, not_6_out, not_7_out);
  and and_2 (and_2_out, not_8_out, not_9_out, not_10_out, not_11_out, not_12_out, not_13_out, not_14_out, not_15_out);
  and and_3 (CSRRSI, F14, F13, not_16_out, OP6, OP5, OP4, not_17_out, not_18_out);
  and and_4 (CSRRCI, F14, F13, F12, OP6, OP5, OP4, not_19_out, not_20_out);
  and and_5 (MemWrite, not_21_out, F13, not_22_out, not_23_out, OP5, not_24_out, not_25_out, not_26_out);
  and and_6 (and_6_out, not_27_out, not_28_out, not_29_out, not_30_out, not_31_out, OP4, not_32_out, not_33_out);
  and and_7 (and_7_out, F14, F13, F12, not_34_out, not_35_out, OP4, not_36_out, not_37_out);
  and and_8 (and_8_out, F14, F13, not_38_out, not_39_out, not_40_out, OP4, not_41_out, not_42_out);
  and and_9 (and_9_out, F14, not_43_out, not_44_out, not_45_out, not_46_out, OP4, not_47_out, not_48_out);
  and and_10 (and_10_out, not_49_out, F13, not_50_out, not_51_out, not_52_out, OP4, not_53_out, not_54_out);
  and and_11 (and_11_out, not_55_out, not_56_out, not_57_out, not_58_out, F12, not_59_out, not_60_out, OP4, not_61_out, not_62_out);
  and and_12 (and_12_out, not_63_out, not_64_out, F14, not_65_out, F12, not_66_out, not_67_out, OP4, not_68_out, not_69_out);
  and and_13 (and_13_out, F30, not_70_out, F14, not_71_out, F12, not_72_out, not_73_out, OP4, not_74_out, not_75_out);
  and and_14 (and_14_out, not_76_out, F13, not_77_out, not_78_out, not_79_out, not_80_out, not_81_out, not_82_out);
  and and_15 (and_15_out, not_83_out, F13, not_84_out, not_85_out, OP5, not_86_out, not_87_out, not_88_out);
  and and_16 (and_16_out, not_89_out, not_90_out, not_91_out, not_92_out, not_93_out, not_94_out, not_95_out, not_96_out);
  and and_17 (and_17_out, not_97_out, not_98_out, not_99_out, not_100_out, not_101_out, not_102_out);
  and and_18 (and_18_out, not_103_out, not_104_out, OP4, not_105_out, not_106_out, not_107_out);
  and and_19 (and_19_out, not_108_out, not_109_out, OP4, not_110_out, not_111_out, not_112_out, not_113_out, not_114_out);
  and and_20 (and_20_out, not_115_out, not_116_out, OP4, not_117_out, not_118_out, not_119_out, not_120_out, not_121_out);
  and and_21 (and_21_out, not_122_out, not_123_out, OP4, not_124_out, not_125_out, not_126_out, not_127_out);
  and and_22 (and_22_out, not_128_out, not_129_out, OP4, not_130_out, not_131_out, F13, F14);
  and and_23 (and_23_out, not_132_out, not_133_out, OP4, not_134_out, F12, not_135_out, F14, not_136_out, F30);
  and and_24 (and_24_out, not_137_out, not_138_out, OP4, OP5, not_139_out, F13, not_140_out, not_141_out);
  and and_25 (and_25_out, OP2, not_142_out, OP5, OP6, not_143_out, not_144_out, not_145_out);
  and and_26 (and_26_out, OP2, OP3, not_146_out, OP5, OP6);
  and and_27 (ecall, not_147_out, not_148_out, not_149_out, not_150_out, not_151_out, OP6, OP5, OP4, not_152_out, not_153_out);
  and and_28 (S_Type, not_154_out, F13, not_155_out, not_156_out, OP5, not_157_out, not_158_out, not_159_out);
  and and_29 (BEQ, not_160_out, not_161_out, not_162_out, OP6, OP5, not_163_out, not_164_out, not_165_out);
  and and_30 (BNE, not_166_out, not_167_out, F12, OP6, OP5, not_168_out, not_169_out, not_170_out);
  and and_31 (JALR, not_171_out, not_172_out, not_173_out, OP6, OP5, not_174_out, not_175_out, OP2);
  and and_32 (JAL, OP6, OP5, not_176_out, OP3, OP2);
  and and_33 (LB, not_177_out, not_178_out, not_179_out, not_180_out, not_181_out, not_182_out, not_183_out, not_184_out);
  and and_34 (BLT, F14, not_185_out, not_186_out, OP6, OP5, not_187_out, not_188_out, not_189_out);
  or or_1 (MemToReg, and_1_out, and_2_out);
  or or_2 (ALU_SRC, and_6_out, and_7_out, and_8_out, and_9_out, and_10_out, and_11_out, and_12_out, and_13_out, and_14_out, and_15_out, and_16_out);
  or or_3 (RegWrite, and_17_out, and_18_out, and_19_out, and_20_out, and_21_out, and_22_out, and_23_out, and_24_out, and_25_out, and_26_out);
endmodule

// ALU
module ALU (
  input  [31:0] X,
  input  [31:0] Y,
  input  [3:0] AluOP,
  output out_4,
  output Equal,
  output out_6,
  output [31:0] Result,
  output [31:0] Result_2
);

  wire [0:0] comparator_1_lt, comparator_2_lt;
  wire [31:0] adder_1_out, AND_out, divider_1_out, divider_1_rem, multiplier_1_cout, multiplier_1_out,
       NOR_out, OR_out, shifter_1_out, shifter_2_out, shifter_3_out, subtractor_1_out, XOR_out;

  assign AND_out = X & Y;  // AND_Gate AND, 32 bits wide
  assign OR_out = X | Y;  // OR_Gate OR, 32 bits wide
  Shifter #(.width(32), .shift("ll")) shifter_1 (.in(X), .\dist (Y[4:0]), .out(shifter_1_out));
  Shifter #(.width(32), .shift("ar")) shifter_2 (.in(X), .\dist (Y[4:0]), .out(shifter_2_out));
  Shifter #(.width(32), .shift("lr")) shifter_3 (.in(X), .\dist (Y[4:0]), .out(shifter_3_out));
  Multiplier #(.width(32)) multiplier_1 (.a(X), .b(Y), .out(multiplier_1_out), .cout(multiplier_1_cout));  // open: cin
  Divider #(.width(32)) divider_1 (.a(X), .b(Y), .out(divider_1_out), .rem(divider_1_rem));  // open: upper
  Adder #(.width(32)) adder_1 (.a(X), .b(Y), .out(adder_1_out));  // open: cin, cout
  Subtractor #(.width(32)) subtractor_1 (.a(X), .b(Y), .out(subtractor_1_out));  // open: bin, bout
  assign XOR_out = X ^ Y;  // XOR_Gate XOR, 32 bits wide
  assign NOR_out = ~(X | Y);  // NOR_Gate NOR, 32 bits wide
  Comparator #(.width(32), .mode("twosComplement")) comparator_1 (
    .a(X), .b(Y), .eq(Equal), .lt(comparator_1_lt[0]));  // open: gt
  Comparator #(.width(32), .mode("unsigned")) comparator_2 (.a(X), .b(Y), .lt(comparator_2_lt[0]));  // open: gt, eq
  Multiplexer #(.select(4), .width(32), .disabled("Z"), .enable("false")) multiplexer_1 (
    .in0(shifter_1_out), .in1(shifter_2_out), .in2(shifter_3_out), .in3(multiplier_1_out),
    .in4(divider_1_out), .in5(adder_1_out), .in6(subtractor_1_out), .in7(AND_out), .in8(OR_out),
    .in9(XOR_out), .in10(NOR_out), .in11({{31{1'b0}}, comparator_1_lt[0]}),
    .in12({{31{1'b0}}, comparator_2_lt[0]}), .in13({32{1'b0}}), .in14({32{1'b0}}), .in15({32{1'b0}}),
    .out(Result), .sel(AluOP));
  Multiplexer #(.select(4), .width(32), .disabled("Z"), .enable("false")) multiplexer_2 (
    .in0({32{1'b0}}), .in1({32{1'b0}}), .in2({32{1'b0}}), .in3(multiplier_1_cout), .in4(divider_1_rem),
    .in5({32{1'b0}}), .in6({32{1'b0}}), .in7({32{1'b0}}), .in8({32{1'b0}}), .in9({32{1'b0}}),
    .in10({32{1'b0}}), .in11({32{1'b0}}), .in12({32{1'b0}}), .in13({32{1'b0}}), .in14({32{1'b0}}),
    .in15({32{1'b0}}), .out(Result_2), .sel(AluOP));
  Multiplexer #(.select(4), .width(1), .disabled("Z"), .enable("false")) multiplexer_3 (
    .in0(1'b0), .in1(1'b0), .in2(1'b0), .in3(1'b0), .in4(1'b0), .in5(1'b0), .in6(1'b0), .in7(1'b0),
    .in8(1'b0), .in9(1'b0), .in10(1'b0), .in11(comparator_1_lt[0]), .in12(comparator_2_lt[0]), .in13(1'b0),
    .in14(1'b0), .in15(1'b0), .out(out_6), .sel(AluOP));
  not not_1 (out_4, out_6);

  // Other names for the same wires on the sheet: Result2[31:0] = Result_2; S[3:0] = AluOP; tunnel = out_6;
  //   tunnel_t = out_4

  // Notes on the sheet:
  //   不要改变此引脚区域内容，也不要改变ALU封装形式
  //   输入引脚
  //   输出引脚
endmodule

module Regifile (
  input  [31:0] Din,
  input  Clk,
  input  WE,
  input  [4:0] R1_num,
  input  [4:0] W_num,
  input  [4:0] R2_num,
  output [31:0] R1,
  output [31:0] R2
);

  // RegisterFile registerfile_1: pin names not known; wires that end beside it: Din, Clk, WE, W_num, R1_num, R2_num, R1, R2
endmodule

module Regifile4Bubble (
  input  [31:0] Din,
  input  Clk,
  input  WE,
  input  [4:0] R1_num,
  input  [4:0] W_num,
  input  [4:0] R2_num,
  output [31:0] R1,
  output [31:0] R2
);

  // RegisterFile registerfile_1: pin names not known; wires that end beside it: Din, Clk, WE, W_num, R1_num, R2_num, R1, R2
endmodule

module \理想流水线  (
  output RegWrite,
  output MemWrite,
  output [31:0] IF_PC,
  output [31:0] ID_PC,
  output [31:0] EX_PC,
  output [31:0] M_PC,
  output [31:0] WB_PC,
  output [31:0] RDin,
  output [31:0] MDin,
  output [31:0] LedData
);

  wire ALU_EQU, ALU_LESS, and_1_out, and_2_out, and_3_out, and_4_out, and_6_out, BEQ, BLT, BNE, CLK,
       clock_1_out, comparator_1_eq, comparator_1_lt, comparator_2_eq, comparator_2_gt, comparator_3_eq,
       d_ff_1_q, ecall, ex_mem_1_bltout, ex_mem_1_haltout, ex_mem_1_jalout, ex_mem_1_jalrout, ex_mem_1_lbout,
       ex_mem_1_memtoregout, ex_mem_1_regwriteout, Go, halt, haltsign, id_ex_1_alusrcbout, id_ex_1_lbout,
       id_ex_1_memtoregout, id_ex_1_memwriteout, id_ex_1_regwriteout, IR1, IR2, IR3, JAL, JALR,
       mem_wb_1_jalout, mem_wb_1_jalrout, mem_wb_1_lbout, mem_wb_1_memtoregout, nand_1_out, nor_1_out,
       not_1_out, not_2_out, not_3_out, not_4_out, not_5_out, or_1_out, or_2_out, RST, W1, W2, W3,
       \单周期硬布线控制器_1_alu_src , \单周期硬布线控制器_1_beq , \单周期硬布线控制器_1_blt , \单周期硬布线控制器_1_bne , \单周期硬布线控制器_1_ecall ,
       \单周期硬布线控制器_1_jal , \单周期硬布线控制器_1_jalr , \单周期硬布线控制器_1_lb , \单周期硬布线控制器_1_memtoreg ,
       \单周期硬布线控制器_1_memwrite , \单周期硬布线控制器_1_regwrite , \单周期硬布线控制器_1_s_type , \单周期硬布线控制器_1_uret ;
  wire [1:0] mem_wb_1_aluresulthighout;
  wire [2:0] PC_SRC;
  wire [3:0] id_ex_1_aluopout, \单周期硬布线控制器_1_alu_op ;
  wire [4:0] ex_mem_1_regwritedestout, id_ex_1_writedest_out, multiplexer_1_out, multiplexer_2_out,
       RegWriteDest;
  wire [7:0] multiplexer_6_out;
  wire [11:0] multiplexer_3_out;
  wire [12:0] CNT_num;
  wire [15:0] \总周期数 ;
  wire [31:0] adder_1_out, adder_2_out, adder_3_out, adder_4_out, alu_1_result, and_5_out,
       bit_extender_1_out, bit_extender_2_out, bit_extender_3_out, bit_extender_4_out, EX_IR,
       ex_mem_1_aluresultout, id_ex_1_immbout, id_ex_1_immjout, id_ex_1_immout, ID_IR, IF_IR, MEM_IR,
       mem_wb_1_aluresultout, mem_wb_1_memdataout, multiplexer_4_out, multiplexer_7_out, multiplexer_8_out,
       NEXT_PC, R1, R2, ram_1_data, regifile_1_r1, regifile_1_r2, shifter_1_out, shifter_2_out, WB_IR;

  Button \u_总复位  (.out(RST));
  Button _1 (.out(IR1));
  Button _2 (.out(IR2));
  Button _3 (.out(IR3));
  // Probe on \总周期数 
  // Probe on \总周期数 
  Button \u_继续运行  (.out(Go));
  LED #(.active("true")) led_1 (.in(W1));
  LED #(.active("true")) led_2 (.in(W2));
  LED #(.active("true")) led_3 (.in(W3));
  or or_1 (or_1_out, Go, not_1_out);
  Hex_Digit_Display hex_digit_display_1 (.value(LedData[31:28]));  // open: dp
  // Probe on IF_PC[19:0]
  // RiscV_Probe riscv_probe_1: pin names not known; wires that end beside it: IF_IR
  Counter #(.width(16), .max('hffff), .ongoal("wrap"), .trigger("rising"), .behavior("new")) counter_1 (
    .count(or_1_out), .Q(\总周期数 ), .clk(CLK), .clr(RST));  // open: load, D, carry, preset, down
  not not_1 (not_1_out, halt);
  Hex_Digit_Display hex_digit_display_2 (.value(LedData[27:24]));  // open: dp
  Hex_Digit_Display hex_digit_display_3 (.value(LedData[23:20]));  // open: dp
  // Probe on ID_PC[19:0]
  // RiscV_Probe riscv_probe_2: pin names not known; wires that end beside it: ID_IR
  Register #(.width(32), .trigger("rising"), .Select("low")) PC (
    .D(NEXT_PC), .en(or_1_out), .Q(IF_PC), .clk(CLK), .clr(RST));
  Hex_Digit_Display hex_digit_display_4 (.value(LedData[15:12]));  // open: dp
  Hex_Digit_Display hex_digit_display_5 (.value(LedData[19:16]));  // open: dp
  not not_2 (not_2_out, halt);
  Hex_Digit_Display hex_digit_display_6 (.value(LedData[11:8]));  // open: dp
  Hex_Digit_Display hex_digit_display_7 (.value(LedData[7:4]));  // open: dp
  // Probe on EX_PC[19:0]
  // RiscV_Probe riscv_probe_3: pin names not known; wires that end beside it: EX_IR
  nor nor_1 (nor_1_out, Go, not_2_out);
  Hex_Digit_Display hex_digit_display_8 (.value(LedData[3:0]));  // open: dp
  ROM #(.addrWidth(10), .dataWidth(32), .Select("low")) rom_1 (.addr(IF_PC[11:2]), .data(IF_IR));
  // Probe on \总周期数 
  // Probe on M_PC[19:0]
  // RiscV_Probe riscv_probe_4: pin names not known; wires that end beside it: MEM_IR
  IF_ID if_id_1 (
    .IR(IF_IR), .PC(IF_PC), .IRout(ID_IR), .PCout(ID_PC), .bubble(1'b0), .EN(nor_1_out), .CLK(CLK),
    .RESET(RST));  // open: PREDICT_JUMP, PREDICT_JUMPout
  // Probe on \总周期数 
  // Probe on {16{1'b0}}
  // Probe on {16{1'b0}}
  // Probe on {16{1'b0}}
  // Probe on {16{1'b0}}
  // Probe on IF_PC[11:0]
  // Probe on WB_PC[19:0]
  // RiscV_Probe riscv_probe_5: pin names not known; wires that end beside it: WB_IR
  // Probe on EX_PC[11:0]
  // Probe on ID_PC[11:0]
  \单周期硬布线控制器  \u_单周期硬布线控制器_1  (
    .Funct({ID_IR[30], ID_IR[25], ID_IR[14:12]}), .OP(ID_IR[6:2]), .ALU_OP(\单周期硬布线控制器_1_alu_op ),
    .MemToReg(\单周期硬布线控制器_1_memtoreg ), .MemWrite(\单周期硬布线控制器_1_memwrite ), .ALU_SRC(\单周期硬布线控制器_1_alu_src ),
    .RegWrite(\单周期硬布线控制器_1_regwrite ), .ecall(\单周期硬布线控制器_1_ecall ), .S_type(\单周期硬布线控制器_1_s_type ),
    .Jalr(\单周期硬布线控制器_1_jalr ), .Beq(\单周期硬布线控制器_1_beq ), .JAL(\单周期硬布线控制器_1_jal ), .Bne(\单周期硬布线控制器_1_bne ),
    .in_3(ID_IR[21]), .uret(\单周期硬布线控制器_1_uret ), .BLT(\单周期硬布线控制器_1_blt ), .LB(\单周期硬布线控制器_1_lb ));  // open: CSRRSI, CSRRCI
  Multiplexer #(.select(1), .width(5), .disabled("Z"), .enable("false")) multiplexer_1 (
    .in0(ID_IR[19:15]), .in1(5'b01010), .out(multiplexer_1_out), .sel(\单周期硬布线控制器_1_ecall ));
  Multiplexer #(.select(1), .width(5), .disabled("Z"), .enable("false")) multiplexer_2 (
    .in0(ID_IR[24:20]), .in1(5'b10001), .out(multiplexer_2_out), .sel(\单周期硬布线控制器_1_ecall ));
  Multiplexer #(.select(1), .width(12), .disabled("Z"), .enable("false")) multiplexer_3 (
    .in0(ID_IR[31:20]), .in1({ID_IR[31:25], ID_IR[11:7]}), .out(multiplexer_3_out), .sel(\单周期硬布线控制器_1_s_type ));
  // Probe on M_PC[11:0]
  D_Flip_Flop #(.trigger("high"), .Pre_Clr_Positions("LEGACY"), .NegatePresetClear("false"), .enable("true"), .NewFFLayout("false")) d_ff_1 (.Q(d_ff_1_q));  // open: clk, D, Qn, preset, en, reset
  // Probe on 13'hc
  assign bit_extender_1_out = {{20{multiplexer_3_out[11]}}, multiplexer_3_out};  // Bit_Extender bit_extender_1
  assign bit_extender_2_out = {{20{ID_IR[31]}}, {ID_IR[31], ID_IR[7], ID_IR[30:25], ID_IR[11:8]}};  // Bit_Extender bit_extender_2
  assign bit_extender_3_out = {{12{ID_IR[31]}}, {ID_IR[31], ID_IR[19:12], ID_IR[20], ID_IR[30:21]}};  // Bit_Extender bit_extender_3
  // Probe on WB_PC[11:0]
  Comparator #(.width(13), .mode("twosComplement")) comparator_1 (
    .a(CNT_num), .b(13'hc), .eq(comparator_1_eq), .lt(comparator_1_lt));  // open: gt
  Clock #(.highDuration(1), .lowDuration(1)) clock_1 (.out(clock_1_out));
  nand nand_1 (nand_1_out, d_ff_1_q, comparator_1_eq);
  Counter #(.width(13), .max('h1fff), .ongoal("stay"), .trigger("rising"), .behavior("old")) counter_2 (
    .count(comparator_1_lt), .Q(CNT_num), .clk(clock_1_out));  // open: load, D, carry, clr, preset
  Comparator #(.width(32), .mode("twosComplement")) comparator_2 (
    .a({32{1'b0}}), .b(ID_IR), .gt(comparator_2_gt), .eq(comparator_2_eq));  // open: lt
  Regifile regifile_1 (
    .Din(RDin), .Clk(CLK), .R1(regifile_1_r1), .R2(regifile_1_r2), .WE(RegWrite), .W_num(RegWriteDest),
    .R1_num(multiplexer_1_out), .R2_num(multiplexer_2_out));
  assign CLK = nand_1_out ? clock_1_out : 1'bz;  // Controlled_Buffer controlled_buffer_1
  and and_1 (and_1_out, \单周期硬布线控制器_1_regwrite , not_3_out);
  not not_3 (not_3_out, comparator_2_eq);
  Pull_Resistor #(.pull(1)) pull_resistor_1 (.node(CLK));
  ID_EX id_ex_1 (
    .JAL(\单周期硬布线控制器_1_jal ), .BLT(\单周期硬布线控制器_1_blt ), .JALR(\单周期硬布线控制器_1_jalr ), .LB(\单周期硬布线控制器_1_lb ),
    .URET(\单周期硬布线控制器_1_uret ), .BEQ(\单周期硬布线控制器_1_beq ), .BNE(\单周期硬布线控制器_1_bne ),
    .MemToReg(\单周期硬布线控制器_1_memtoreg ), .MemWrite(\单周期硬布线控制器_1_memwrite ), .AluOP(\单周期硬布线控制器_1_alu_op ),
    .AluSrcB(\单周期硬布线控制器_1_alu_src ), .RegWrite(and_1_out), .R1(regifile_1_r1), .R2(regifile_1_r2),
    .Imm(bit_extender_1_out), .IR(ID_IR), .PC(ID_PC), .bubble(1'b0), .EN(nor_1_out), .CLK(CLK), .JALout(JAL),
    .BLTout(BLT), .JALRout(JALR), .LBout(id_ex_1_lbout), .BEQout(BEQ), .BNEout(BNE),
    .MemToRegout(id_ex_1_memtoregout), .MemWriteout(id_ex_1_memwriteout), .AluOPout(id_ex_1_aluopout),
    .AluSrcBout(id_ex_1_alusrcbout), .RegWriteout(id_ex_1_regwriteout), .R1out(R1), .R2out(R2),
    .Immout(id_ex_1_immout), .IRout(EX_IR), .PCout(EX_PC), .RESET(RST), .ecallout(ecall),
    .ecall(\单周期硬布线控制器_1_ecall ), .ImmB(bit_extender_2_out), .ImmJ(bit_extender_3_out),
    .ImmBout(id_ex_1_immbout), .ImmJout(id_ex_1_immjout), .WriteDest_num(ID_IR[11:7]),
    .WriteDest_out(id_ex_1_writedest_out));  // open: URETout, R1_Forword, R2_Forword, R1_Forwordout, R2_Forwordout, PREDICT_JUMP, PREDICT_JUMPout
  not not_4 (not_4_out, ALU_EQU);
  and and_2 (and_2_out, BNE, not_4_out);
  and and_3 (and_3_out, ALU_EQU, BEQ);
  and and_4 (and_4_out, BLT, ALU_LESS);
  Multiplexer #(.select(1), .width(32), .disabled("Z"), .enable("false")) multiplexer_4 (
    .in0(R2), .in1(id_ex_1_immout), .out(multiplexer_4_out), .sel(id_ex_1_alusrcbout));
  Shifter #(.width(32), .shift("ll")) shifter_1 (.in(id_ex_1_immbout), .\dist (5'b00001), .out(shifter_1_out));
  Shifter #(.width(32), .shift("ll")) shifter_2 (.in(id_ex_1_immjout), .\dist (5'b00001), .out(shifter_2_out));
  Adder #(.width(32)) adder_1 (.a(shifter_1_out), .b(EX_PC), .out(adder_1_out));  // open: cin, cout
  Adder #(.width(32)) adder_2 (.a(shifter_2_out), .b(EX_PC), .out(adder_2_out));  // open: cin, cout
  Adder #(.width(32)) adder_3 (.a(IF_PC), .b(32'h4), .out(adder_3_out));  // open: cin, cout
  Priority_Encoder #(.select(3), .disabled("Z")) priority_encoder_1 (
    .in0(1'b1), .in1(and_2_out), .in2(and_3_out), .in3(JAL), .in4(JALR), .in5(and_4_out), .out(PC_SRC));  // open: in6, in7, gs, en_out, en_in
  ALU alu_1 (
    .X(R1), .Y(multiplexer_4_out), .AluOP(id_ex_1_aluopout), .Equal(ALU_EQU), .Result(alu_1_result),
    .out_6(ALU_LESS));  // open: Result_2, out_4
  assign and_5_out = alu_1_result & 32'hfffffffe;  // AND_Gate and_5, 32 bits wide
  EX_MEM ex_mem_1 (
    .JAL(JAL), .JALR(JALR), .LB(id_ex_1_lbout), .MemToReg(id_ex_1_memtoregout),
    .MemWrite(id_ex_1_memwriteout), .RegWrite(id_ex_1_regwriteout), .ALUResult(alu_1_result), .R2(R2),
    .RegWriteDest(id_ex_1_writedest_out), .IR(EX_IR), .PC(EX_PC), .JALout(ex_mem_1_jalout),
    .JALRout(ex_mem_1_jalrout), .LBout(ex_mem_1_lbout), .MemToRegout(ex_mem_1_memtoregout),
    .MemWriteout(MemWrite), .RegWriteout(ex_mem_1_regwriteout), .ALUResultout(ex_mem_1_aluresultout),
    .R2out(MDin), .RegWriteDestout(ex_mem_1_regwritedestout), .IRout(MEM_IR), .PCout(M_PC), .RESET(RST),
    .bubble(1'b0), .EN(nor_1_out), .CLK(CLK), .BLT(BLT), .BLTout(ex_mem_1_bltout), .halt(haltsign),
    .haltout(ex_mem_1_haltout));
  Multiplexer #(.select(3), .width(32), .disabled("Z"), .enable("false")) multiplexer_5 (
    .in0(adder_3_out), .in1(adder_1_out), .in2(adder_1_out), .in3(adder_2_out), .in4(and_5_out),
    .in5(adder_1_out), .out(NEXT_PC), .sel(PC_SRC));  // open: in6, in7
  RAM #(.addrWidth(10), .dataWidth(32), .bus("separate"), .Select("high")) ram_1 (
    .addr(ex_mem_1_aluresultout[11:2]), .din(MDin), .data(ram_1_data), .str(MemWrite), .clk(CLK));  // open: sel, ld, clr
  MEM_WB mem_wb_1 (
    .JAL(ex_mem_1_jalout), .JALR(ex_mem_1_jalrout), .LB(ex_mem_1_lbout), .MemToReg(ex_mem_1_memtoregout),
    .RegWrite(ex_mem_1_regwriteout), .ALUResult(ex_mem_1_aluresultout),
    .RegWriteDest(ex_mem_1_regwritedestout), .IR(MEM_IR), .PC(M_PC), .JALout(mem_wb_1_jalout),
    .JALRout(mem_wb_1_jalrout), .LBout(mem_wb_1_lbout), .MemToRegout(mem_wb_1_memtoregout),
    .RegWriteout(RegWrite), .ALUResultout(mem_wb_1_aluresultout), .RegWriteDestout(RegWriteDest),
    .MemDataout(mem_wb_1_memdataout), .IRout(WB_IR), .PCout(WB_PC), .RESET(RST), .bubble(1'b0),
    .EN(nor_1_out), .CLK(CLK), .BLT(ex_mem_1_bltout), .ALUResultHigh(ex_mem_1_aluresultout[1:0]),
    .ALUResultHighout(mem_wb_1_aluresulthighout), .MemData(ram_1_data), .halt(ex_mem_1_haltout),
    .haltout(halt));  // open: BLTout
  Comparator #(.width(32), .mode("twosComplement")) comparator_3 (
    .a(R2), .b(32'h22), .eq(comparator_3_eq));  // open: gt, lt
  Multiplexer #(.select(2), .width(8), .disabled("Z"), .enable("false")) multiplexer_6 (
    .in0(mem_wb_1_memdataout[7:0]), .in1(mem_wb_1_memdataout[15:8]), .in2(mem_wb_1_memdataout[23:16]),
    .in3(mem_wb_1_memdataout[31:24]), .out(multiplexer_6_out), .sel(mem_wb_1_aluresulthighout));
  and and_6 (and_6_out, ecall, comparator_3_eq);
  assign bit_extender_4_out = {{24{multiplexer_6_out[7]}}, multiplexer_6_out};  // Bit_Extender bit_extender_4
  Register #(.width(32), .trigger("rising"), .Select("low")) register_1 (
    .D(R1), .en(and_6_out), .Q(LedData), .clk(CLK), .clr(RST));
  Multiplexer #(.select(1), .width(32), .disabled("Z"), .enable("false")) multiplexer_7 (
    .in0(mem_wb_1_memdataout), .in1(bit_extender_4_out), .out(multiplexer_7_out), .sel(mem_wb_1_lbout));
  not not_5 (not_5_out, comparator_3_eq);
  Multiplexer #(.select(1), .width(32), .disabled("Z"), .enable("false")) multiplexer_8 (
    .in0(mem_wb_1_aluresultout), .in1(multiplexer_7_out), .out(multiplexer_8_out), .sel(mem_wb_1_memtoregout));
  and and_7 (haltsign, ecall, not_5_out);
  or or_2 (or_2_out, mem_wb_1_jalout, mem_wb_1_jalrout);
  Adder #(.width(32)) adder_4 (.a(WB_PC), .b(32'h4), .out(adder_4_out));  // open: cin, cout
  Multiplexer #(.select(1), .width(32), .disabled("Z"), .enable("false")) multiplexer_9 (
    .in0(multiplexer_8_out), .in1(adder_4_out), .out(RDin), .sel(or_2_out));

  // Other names for the same wires on the sheet: MEM_PC[31:0] = M_PC

  // Notes on the sheet:
  //   中断源
  //   时空图监测，可删除
  //   中断等待指示
  //   数码管输出
  //   contents of rom_1 (hex, n*v repeats v):
  //   413 493 913 993 46413 14e493 296913 39e993 842023 942223 1242423 1342623 a00893 493 913 993 73
  //   R1
  //   R2
  //   WriteReg#
  //   I
  //   S
  //   B
  //   J
  //   控制位
  //   流水调试日志用
  //   暂停节拍，不能为0
  //   戳工具置1进入计数暂停模式，ctrl+k时钟自动运行到对应节拍暂停
  //   ctrl+k关闭时钟连续运行，将控制位置零，进入单步调试模式调试
  //   用这个时钟源需要去掉电路中的其他时钟源
  //   可计数暂停的时钟源
  //   特判流水钱前几个周期，防止控制器初始值干扰
  //   为方便自动评测，需要输出流水线各段保存的PC值，注意是PC不是PC+4，另外ID段寄存器写入信息，Mem段内存写入信息也要输出
endmodule

module \气泡流水线  (
  output RegWrite,
  output MemWrite,
  output [31:0] IF_PC,
  output [31:0] ID_PC,
  output [31:0] EX_PC,
  output [31:0] M_PC,
  output [31:0] WB_PC,
  output [31:0] RDin,
  output [31:0] MDin,
  output [31:0] LedData
);

  wire ALU_EQU, ALU_LESS, and_1_out, and_2_out, and_3_out, and_4_out, and_5_out, and_7_out, BEQ, BLT, BNE,
       Branch_Success, CLK, clock_1_out, comparator_1_eq, comparator_1_lt, comparator_2_eq, comparator_2_gt,
       comparator_3_eq, d_ff_1_q, ecall, ex_mem_1_bltout, ex_mem_1_haltout, ex_mem_1_jalout,
       ex_mem_1_jalrout, ex_mem_1_lbout, ex_mem_1_memtoregout, EX_RegWrite, Go, halt, haltsign,
       id_ex_1_alusrcbout, id_ex_1_lbout, id_ex_1_memtoregout, id_ex_1_memwriteout, InBranch, IR1, IR2, IR3,
       IR_ecall, JAL, JALR, MEM_RegWrite, mem_wb_1_jalout, mem_wb_1_jalrout, mem_wb_1_lbout,
       mem_wb_1_memtoregout, nand_1_out, nor_1_out, nor_2_out, nor_3_out, not_1_out, not_2_out, not_3_out,
       not_4_out, not_5_out, not_6_out, not_7_out, not_8_out, or_1_out, or_2_out, or_3_out, or_5_out,
       or_7_out, RST, stall, W1, W2, W3, \单周期硬布线控制器_1_alu_src , \单周期硬布线控制器_1_beq , \单周期硬布线控制器_1_blt ,
       \单周期硬布线控制器_1_bne , \单周期硬布线控制器_1_jal , \单周期硬布线控制器_1_jalr , \单周期硬布线控制器_1_lb , \单周期硬布线控制器_1_memtoreg ,
       \单周期硬布线控制器_1_memwrite , \单周期硬布线控制器_1_regwrite , \单周期硬布线控制器_1_s_type , \单周期硬布线控制器_1_uret ;
  wire [1:0] mem_wb_1_aluresulthighout;
  wire [2:0] PC_SRC;
  wire [3:0] id_ex_1_aluopout, \单周期硬布线控制器_1_alu_op ;
  wire [4:0] EX_RegWriteDest_num, MEM_RegWriteDest_num, multiplexer_1_out, multiplexer_2_out, RegWriteDest;
  wire [7:0] multiplexer_6_out;
  wire [11:0] multiplexer_3_out;
  wire [12:0] CNT_num;
  wire [15:0] \总周期数 , \插入气泡数 , \无条件分支数 , \条件分支成功数 ;
  wire [31:0] adder_1_out, adder_2_out, adder_3_out, adder_4_out, alu_1_result, and_6_out,
       bit_extender_1_out, bit_extender_2_out, bit_extender_3_out, bit_extender_4_out, EX_IR,
       ex_mem_1_aluresultout, id_ex_1_immbout, id_ex_1_immjout, id_ex_1_immout, ID_IR, IF_IR, MEM_IR,
       mem_wb_1_aluresultout, mem_wb_1_memdataout, multiplexer_4_out, multiplexer_7_out, multiplexer_8_out,
       NEXT_PC, R1, R2, ram_1_data, regifile4bubble_1_r1, regifile4bubble_1_r2, shifter_1_out, shifter_2_out,
       WB_IR;

  Button \u_总复位  (.out(RST));
  Button _1 (.out(IR1));
  Button _2 (.out(IR2));
  Button _3 (.out(IR3));
  // Probe on \总周期数 
  // Probe on \总周期数 
  Button \u_继续运行  (.out(Go));
  LED #(.active("true")) led_1 (.in(W1));
  LED #(.active("true")) led_2 (.in(W2));
  LED #(.active("true")) led_3 (.in(W3));
  or or_1 (or_1_out, Go, not_1_out);
  not not_1 (not_1_out, halt);
  Hex_Digit_Display hex_digit_display_1 (.value(LedData[31:28]));  // open: dp
  // Probe on IF_PC[19:0]
  // RiscV_Probe riscv_probe_1: pin names not known; wires that end beside it: IF_IR
  Counter #(.width(16), .max('hffff), .ongoal("wrap"), .trigger("rising"), .behavior("new")) counter_1 (
    .count(or_1_out), .Q(\总周期数 ), .clk(CLK), .clr(RST));  // open: load, D, carry, preset, down
  and and_1 (and_1_out, or_1_out, not_2_out);
  not not_2 (not_2_out, stall);
  Hex_Digit_Display hex_digit_display_2 (.value(LedData[23:20]));  // open: dp
  Hex_Digit_Display hex_digit_display_3 (.value(LedData[27:24]));  // open: dp
  // Probe on ID_PC[19:0]
  // RiscV_Probe riscv_probe_2: pin names not known; wires that end beside it: ID_IR
  Register #(.width(32), .trigger("rising"), .Select("low")) PC (
    .D(NEXT_PC), .en(and_1_out), .Q(IF_PC), .clk(CLK), .clr(RST));
  Hex_Digit_Display hex_digit_display_4 (.value(LedData[19:16]));  // open: dp
  Hex_Digit_Display hex_digit_display_5 (.value(LedData[15:12]));  // open: dp
  not not_3 (not_3_out, halt);
  Hex_Digit_Display hex_digit_display_6 (.value(LedData[11:8]));  // open: dp
  Hex_Digit_Display hex_digit_display_7 (.value(LedData[7:4]));  // open: dp
  // Probe on EX_PC[19:0]
  // RiscV_Probe riscv_probe_3: pin names not known; wires that end beside it: EX_IR
  nor nor_1 (nor_1_out, Go, not_3_out);
  Hex_Digit_Display hex_digit_display_8 (.value(LedData[3:0]));  // open: dp
  ROM #(.addrWidth(10), .dataWidth(32), .Select("low")) rom_1 (.addr(IF_PC[11:2]), .data(IF_IR));
  // Probe on \总周期数 
  // Probe on M_PC[19:0]
  // RiscV_Probe riscv_probe_4: pin names not known; wires that end beside it: MEM_IR
  IF_ID if_id_1 (
    .IR(IF_IR), .PC(IF_PC), .IRout(ID_IR), .PCout(ID_PC), .bubble(InBranch), .EN(or_2_out), .CLK(CLK),
    .RESET(RST));  // open: PREDICT_JUMP, PREDICT_JUMPout
  // Probe on \总周期数 
  // Probe on \无条件分支数 
  // Probe on \条件分支成功数 
  // Probe on \插入气泡数 
  // Probe on {16{1'b0}}
  Counter #(.width(16), .max('hffff), .ongoal("wrap"), .trigger("rising"), .behavior("new")) counter_2 (
    .count(stall), .Q(\插入气泡数 ), .clk(CLK), .clr(RST));  // open: load, D, carry, preset, down
  or or_2 (or_2_out, nor_1_out, stall);
  \流水冲突检测器4气泡  \u_流水冲突检测器4气泡_1  (
    .EX_RegWrite(EX_RegWrite), .MEM_RegWrite(MEM_RegWrite), .EX_RegWriteDest_num(EX_RegWriteDest_num),
    .MEM_RegWriteDest_num(MEM_RegWriteDest_num), .IR(ID_IR), .ecall(IR_ecall), .stall(stall));
  // Probe on IF_PC[11:0]
  // Probe on WB_PC[19:0]
  // RiscV_Probe riscv_probe_5: pin names not known; wires that end beside it: WB_IR
  // Probe on ID_PC[11:0]
  // Probe on EX_PC[11:0]
  \单周期硬布线控制器  \u_单周期硬布线控制器_1  (
    .Funct({ID_IR[30], ID_IR[25], ID_IR[14:12]}), .OP(ID_IR[6:2]), .ALU_OP(\单周期硬布线控制器_1_alu_op ),
    .MemToReg(\单周期硬布线控制器_1_memtoreg ), .MemWrite(\单周期硬布线控制器_1_memwrite ), .ALU_SRC(\单周期硬布线控制器_1_alu_src ),
    .RegWrite(\单周期硬布线控制器_1_regwrite ), .ecall(IR_ecall), .S_type(\单周期硬布线控制器_1_s_type ),
    .Jalr(\单周期硬布线控制器_1_jalr ), .Beq(\单周期硬布线控制器_1_beq ), .JAL(\单周期硬布线控制器_1_jal ), .Bne(\单周期硬布线控制器_1_bne ),
    .in_3(ID_IR[21]), .uret(\单周期硬布线控制器_1_uret ), .BLT(\单周期硬布线控制器_1_blt ), .LB(\单周期硬布线控制器_1_lb ));  // open: CSRRSI, CSRRCI
  Multiplexer #(.select(1), .width(5), .disabled("Z"), .enable("false")) multiplexer_1 (
    .in0(ID_IR[19:15]), .in1(5'b01010), .out(multiplexer_1_out), .sel(IR_ecall));
  Multiplexer #(.select(1), .width(5), .disabled("Z"), .enable("false")) multiplexer_2 (
    .in0(ID_IR[24:20]), .in1(5'b10001), .out(multiplexer_2_out), .sel(IR_ecall));
  Multiplexer #(.select(1), .width(12), .disabled("Z"), .enable("false")) multiplexer_3 (
    .in0(ID_IR[31:20]), .in1({ID_IR[31:25], ID_IR[11:7]}), .out(multiplexer_3_out), .sel(\单周期硬布线控制器_1_s_type ));
  // Probe on M_PC[11:0]
  D_Flip_Flop #(.trigger("high"), .Pre_Clr_Positions("LEGACY"), .NegatePresetClear("false"), .enable("true"), .NewFFLayout("false")) d_ff_1 (.Q(d_ff_1_q));  // open: clk, D, Qn, preset, en, reset
  // Probe on 13'hc
  assign bit_extender_1_out = {{20{multiplexer_3_out[11]}}, multiplexer_3_out};  // Bit_Extender bit_extender_1
  assign bit_extender_2_out = {{20{ID_IR[31]}}, {ID_IR[31], ID_IR[7], ID_IR[30:25], ID_IR[11:8]}};  // Bit_Extender bit_extender_2
  assign bit_extender_3_out = {{12{ID_IR[31]}}, {ID_IR[31], ID_IR[19:12], ID_IR[20], ID_IR[30:21]}};  // Bit_Extender bit_extender_3
  // Probe on WB_PC[11:0]
  Comparator #(.width(13), .mode("twosComplement")) comparator_1 (
    .a(CNT_num), .b(13'hc), .eq(comparator_1_eq), .lt(comparator_1_lt));  // open: gt
  Clock #(.highDuration(1), .lowDuration(1)) clock_1 (.out(clock_1_out));
  nand nand_1 (nand_1_out, d_ff_1_q, comparator_1_eq);
  Counter #(.width(13), .max('h1fff), .ongoal("stay"), .trigger("rising"), .behavior("old")) counter_3 (
    .count(comparator_1_lt), .Q(CNT_num), .clk(clock_1_out));  // open: load, D, carry, clr, preset
  Comparator #(.width(32), .mode("twosComplement")) comparator_2 (
    .a({32{1'b0}}), .b(ID_IR), .gt(comparator_2_gt), .eq(comparator_2_eq));  // open: lt
  Regifile4Bubble regifile4bubble_1 (
    .Din(RDin), .Clk(CLK), .R1(regifile4bubble_1_r1), .R2(regifile4bubble_1_r2), .WE(RegWrite),
    .W_num(RegWriteDest), .R1_num(multiplexer_1_out), .R2_num(multiplexer_2_out));
  not not_4 (not_4_out, halt);
  assign CLK = nand_1_out ? clock_1_out : 1'bz;  // Controlled_Buffer controlled_buffer_1
  and and_2 (and_2_out, \单周期硬布线控制器_1_regwrite , not_5_out);
  not not_5 (not_5_out, comparator_2_eq);
  nor nor_2 (nor_2_out, Go, not_4_out);
  Pull_Resistor #(.pull(1)) pull_resistor_1 (.node(CLK));
  ID_EX id_ex_1 (
    .JAL(\单周期硬布线控制器_1_jal ), .BLT(\单周期硬布线控制器_1_blt ), .JALR(\单周期硬布线控制器_1_jalr ), .LB(\单周期硬布线控制器_1_lb ),
    .URET(\单周期硬布线控制器_1_uret ), .BEQ(\单周期硬布线控制器_1_beq ), .BNE(\单周期硬布线控制器_1_bne ),
    .MemToReg(\单周期硬布线控制器_1_memtoreg ), .MemWrite(\单周期硬布线控制器_1_memwrite ), .AluOP(\单周期硬布线控制器_1_alu_op ),
    .AluSrcB(\单周期硬布线控制器_1_alu_src ), .RegWrite(and_2_out), .R1(regifile4bubble_1_r1),
    .R2(regifile4bubble_1_r2), .Imm(bit_extender_1_out), .IR(ID_IR), .PC(ID_PC), .bubble(or_3_out),
    .EN(nor_2_out), .CLK(CLK), .JALout(JAL), .BLTout(BLT), .JALRout(JALR), .LBout(id_ex_1_lbout),
    .BEQout(BEQ), .BNEout(BNE), .MemToRegout(id_ex_1_memtoregout), .MemWriteout(id_ex_1_memwriteout),
    .AluOPout(id_ex_1_aluopout), .AluSrcBout(id_ex_1_alusrcbout), .RegWriteout(EX_RegWrite), .R1out(R1),
    .R2out(R2), .Immout(id_ex_1_immout), .IRout(EX_IR), .PCout(EX_PC), .RESET(RST), .ecallout(ecall),
    .ecall(IR_ecall), .ImmB(bit_extender_2_out), .ImmJ(bit_extender_3_out), .ImmBout(id_ex_1_immbout),
    .ImmJout(id_ex_1_immjout), .WriteDest_num(ID_IR[11:7]), .WriteDest_out(EX_RegWriteDest_num));  // open: URETout, R1_Forword, R2_Forword, R1_Forwordout, R2_Forwordout, PREDICT_JUMP, PREDICT_JUMPout
  or or_3 (or_3_out, InBranch, stall);
  not not_6 (not_6_out, ALU_EQU);
  and and_3 (and_3_out, BNE, not_6_out);
  and and_4 (and_4_out, ALU_EQU, BEQ);
  and and_5 (and_5_out, BLT, ALU_LESS);
  Multiplexer #(.select(1), .width(32), .disabled("Z"), .enable("false")) multiplexer_4 (
    .in0(R2), .in1(id_ex_1_immout), .out(multiplexer_4_out), .sel(id_ex_1_alusrcbout));
  Shifter #(.width(32), .shift("ll")) shifter_1 (.in(id_ex_1_immbout), .\dist (5'b00001), .out(shifter_1_out));
  Shifter #(.width(32), .shift("ll")) shifter_2 (.in(id_ex_1_immjout), .\dist (5'b00001), .out(shifter_2_out));
  Adder #(.width(32)) adder_1 (.a(shifter_1_out), .b(EX_PC), .out(adder_1_out));  // open: cin, cout
  Adder #(.width(32)) adder_2 (.a(shifter_2_out), .b(EX_PC), .out(adder_2_out));  // open: cin, cout
  Adder #(.width(32)) adder_3 (.a(IF_PC), .b(32'h4), .out(adder_3_out));  // open: cin, cout
  Priority_Encoder #(.select(3), .disabled("Z")) priority_encoder_1 (
    .in0(1'b1), .in1(and_3_out), .in2(and_4_out), .in3(JAL), .in4(JALR), .in5(and_5_out), .out(PC_SRC));  // open: in6, in7, gs, en_out, en_in
  or or_4 (InBranch, JAL, JALR, Branch_Success);
  or or_5 (or_5_out, JALR, JAL);
  ALU alu_1 (
    .X(R1), .Y(multiplexer_4_out), .AluOP(id_ex_1_aluopout), .Equal(ALU_EQU), .Result(alu_1_result),
    .out_6(ALU_LESS));  // open: Result_2, out_4
  or or_6 (Branch_Success, and_4_out, and_3_out, and_5_out);
  Counter #(.width(16), .max('hffff), .ongoal("wrap"), .trigger("rising"), .behavior("new")) counter_4 (
    .count(or_5_out), .Q(\无条件分支数 ), .clk(CLK), .clr(RST));  // open: load, D, carry, preset, down
  assign and_6_out = alu_1_result & 32'hfffffffe;  // AND_Gate and_6, 32 bits wide
  EX_MEM ex_mem_1 (
    .JAL(JAL), .JALR(JALR), .LB(id_ex_1_lbout), .MemToReg(id_ex_1_memtoregout),
    .MemWrite(id_ex_1_memwriteout), .RegWrite(EX_RegWrite), .ALUResult(alu_1_result), .R2(R2),
    .RegWriteDest(EX_RegWriteDest_num), .IR(EX_IR), .PC(EX_PC), .JALout(ex_mem_1_jalout),
    .JALRout(ex_mem_1_jalrout), .LBout(ex_mem_1_lbout), .MemToRegout(ex_mem_1_memtoregout),
    .MemWriteout(MemWrite), .RegWriteout(MEM_RegWrite), .ALUResultout(ex_mem_1_aluresultout), .R2out(MDin),
    .RegWriteDestout(MEM_RegWriteDest_num), .IRout(MEM_IR), .PCout(M_PC), .RESET(RST), .bubble(1'b0),
    .EN(nor_3_out), .CLK(CLK), .BLT(BLT), .BLTout(ex_mem_1_bltout), .halt(haltsign),
    .haltout(ex_mem_1_haltout));
  Multiplexer #(.select(3), .width(32), .disabled("Z"), .enable("false")) multiplexer_5 (
    .in0(adder_3_out), .in1(adder_1_out), .in2(adder_1_out), .in3(adder_2_out), .in4(and_6_out),
    .in5(adder_1_out), .out(NEXT_PC), .sel(PC_SRC));  // open: in6, in7
  Counter #(.width(16), .max('hffff), .ongoal("wrap"), .trigger("rising"), .behavior("new")) counter_5 (
    .count(Branch_Success), .Q(\条件分支成功数 ), .clk(CLK), .clr(RST));  // open: load, D, carry, preset, down
  RAM #(.addrWidth(10), .dataWidth(32), .bus("separate"), .Select("high")) ram_1 (
    .addr(ex_mem_1_aluresultout[11:2]), .din(MDin), .data(ram_1_data), .str(MemWrite), .clk(CLK));  // open: sel, ld, clr
  not not_7 (not_7_out, halt);
  nor nor_3 (nor_3_out, Go, not_7_out);
  MEM_WB mem_wb_1 (
    .JAL(ex_mem_1_jalout), .JALR(ex_mem_1_jalrout), .LB(ex_mem_1_lbout), .MemToReg(ex_mem_1_memtoregout),
    .RegWrite(MEM_RegWrite), .ALUResult(ex_mem_1_aluresultout), .RegWriteDest(MEM_RegWriteDest_num),
    .IR(MEM_IR), .PC(M_PC), .JALout(mem_wb_1_jalout), .JALRout(mem_wb_1_jalrout), .LBout(mem_wb_1_lbout),
    .MemToRegout(mem_wb_1_memtoregout), .RegWriteout(RegWrite), .ALUResultout(mem_wb_1_aluresultout),
    .RegWriteDestout(RegWriteDest), .MemDataout(mem_wb_1_memdataout), .IRout(WB_IR), .PCout(WB_PC),
    .RESET(RST), .bubble(1'b0), .EN(nor_3_out), .CLK(CLK), .BLT(ex_mem_1_bltout),
    .ALUResultHigh(ex_mem_1_aluresultout[1:0]), .ALUResultHighout(mem_wb_1_aluresulthighout),
    .MemData(ram_1_data), .halt(ex_mem_1_haltout), .haltout(halt));  // open: BLTout
  Comparator #(.width(32), .mode("twosComplement")) comparator_3 (
    .a(R2), .b(32'h22), .eq(comparator_3_eq));  // open: gt, lt
  Multiplexer #(.select(2), .width(8), .disabled("Z"), .enable("false")) multiplexer_6 (
    .in0(mem_wb_1_memdataout[7:0]), .in1(mem_wb_1_memdataout[15:8]), .in2(mem_wb_1_memdataout[23:16]),
    .in3(mem_wb_1_memdataout[31:24]), .out(multiplexer_6_out), .sel(mem_wb_1_aluresulthighout));
  and and_7 (and_7_out, ecall, comparator_3_eq);
  assign bit_extender_4_out = {{24{multiplexer_6_out[7]}}, multiplexer_6_out};  // Bit_Extender bit_extender_4
  Register #(.width(32), .trigger("rising"), .Select("low")) register_1 (
    .D(R1), .en(and_7_out), .Q(LedData), .clk(CLK), .clr(RST));
  Multiplexer #(.select(1), .width(32), .disabled("Z"), .enable("false")) multiplexer_7 (
    .in0(mem_wb_1_memdataout), .in1(bit_extender_4_out), .out(multiplexer_7_out), .sel(mem_wb_1_lbout));
  not not_8 (not_8_out, comparator_3_eq);
  Multiplexer #(.select(1), .width(32), .disabled("Z"), .enable("false")) multiplexer_8 (
    .in0(mem_wb_1_aluresultout), .in1(multiplexer_7_out), .out(multiplexer_8_out), .sel(mem_wb_1_memtoregout));
  and and_8 (haltsign, ecall, not_8_out);
  or or_7 (or_7_out, mem_wb_1_jalout, mem_wb_1_jalrout);
  Adder #(.width(32)) adder_4 (.a(WB_PC), .b(32'h4), .out(adder_4_out));  // open: cin, cout
  Multiplexer #(.select(1), .width(32), .disabled("Z"), .enable("false")) multiplexer_9 (
    .in0(multiplexer_8_out), .in1(adder_4_out), .out(RDin), .sel(or_7_out));

  // Other names for the same wires on the sheet: MEM_PC[31:0] = M_PC

  // Notes on the sheet:
  //   中断源
  //   时空图监测，可删除
  //   中断等待指示
  //   数码管输出
  //   contents of rom_1 (hex, n*v repeats v):
  //   100493 100006f 100493 200913 300993 100006f 100493 200913 300993 100006f 100493 200913 300993
  //   100006f 100493 200913 300993 29c000ef 100413 100493 1f49493 900533 2200893 73 24d493 48463 fedff06f
  //   900533 2200893 73 100493 249493 900533 2200893 73 48463 fedff06f 100493 1f49493 900533 2200893 73
  //   4034d493 900533 2200893 73 4044d493 900533 2200893 73 4044d493 900533 2200893 73 4044d493 900533
  //   2200893 73 4044d493 900533 2200893 73 4044d493 900533 2200893 73 4044d493 900533 2200893 73 4044d493
  //   900533 2200893 73 100413 1f41993 41f9d993 433 c00913 300b13 140413 f47413 800293 100313 499993
  //   89e9b3 1300533 2200893 73 406282b3 fe0294e3 140413 f00f93 1f47433 1c41413 800293 100313 49d993
  //   89e9b3 1300533 2200893 73 406282b3 fe0294e3 1c45413 406b0b33 b0463 f95ff06f 2b3 fff2c293 829293
  //   ff2e293 500533 2200893 73 fff00413 493 84a023 140413 448493 84a023 140413 448493 84a023 140413
  //   448493 84a023 140413 448493 84a023 140413 448493 84a023 140413 448493 84a023 140413 448493 84a023
  //   140413 448493 84a023 140413 448493 84a023 140413 448493 84a023 140413 448493 84a023 140413 448493
  //   84a023 140413 448493 84a023 140413 448493 84a023 140413 448493 84a023 140413 448493 140413 433
  //   3c00493 42983 4aa03 149a2b3 28663 134a023 1442023 ffc48493 fe9412e3 800533 2200893 73 440413 3c00493
  //   fc9416e3 a00893 73 413 140413 800533 2200893 73 240413 800533 2200893 73 340413 800533 2200893 73
  //   440413 800533 2200893 73 540413 800533 2200893 73 640413 800533 2200893 73 740413 800533 2200893 73
  //   840413 800533 2200893 2200893 73 8067
  //   R1
  //   R2
  //   WriteReg#
  //   I
  //   S
  //   B
  //   J
  //   控制位
  //   流水调试日志用
  //   暂停节拍，不能为0
  //   戳工具置1进入计数暂停模式，ctrl+k时钟自动运行到对应节拍暂停
  //   ctrl+k关闭时钟连续运行，将控制位置零，进入单步调试模式调试
  //   用这个时钟源需要去掉电路中的其他时钟源
  //   可计数暂停的时钟源
  //   为方便自动评测，需要输出流水线各段保存的PC值，注意是PC不是PC+4，另外ID段寄存器写入信息，Mem段内存写入信息也要输出
endmodule

module \重定向流水线  (
  output RegWrite,
  output MemWrite,
  output [31:0] IF_PC,
  output [31:0] ID_PC,
  output [31:0] EX_PC,
  output [31:0] M_PC,
  output [31:0] WB_PC,
  output [31:0] RDin,
  output [31:0] MDin,
  output [31:0] LedData
);

  wire ALU_EQU, ALU_LESS, and_1_out, and_2_out, and_3_out, and_4_out, and_5_out, and_7_out, BEQ, BLT, BNE,
       Branch_Success, CLK, clock_1_out, comparator_1_eq, comparator_1_lt, comparator_2_eq, comparator_2_gt,
       comparator_3_eq, d_ff_1_q, ecall, ex_mem_1_bltout, ex_mem_1_haltout, ex_mem_1_jalout,
       ex_mem_1_jalrout, ex_mem_1_lbout, ex_mem_1_memtoregout, EX_MemToReg, EX_RegWrite, Go, halt, haltsign,
       id_ex_1_alusrcbout, id_ex_1_lbout, id_ex_1_memwriteout, InBranch, IR1, IR2, IR3, IR_ecall, JAL, JALR,
       load_use, MEM_RegWrite, mem_wb_1_jalout, mem_wb_1_jalrout, mem_wb_1_lbout, mem_wb_1_memtoregout,
       nand_1_out, nor_1_out, nor_2_out, nor_3_out, not_1_out, not_2_out, not_3_out, not_4_out, not_5_out,
       not_6_out, not_7_out, not_8_out, or_1_out, or_2_out, or_3_out, or_5_out, or_7_out, or_8_out, RST, W1,
       W2, W3, \单周期硬布线控制器_1_alu_src , \单周期硬布线控制器_1_beq , \单周期硬布线控制器_1_blt , \单周期硬布线控制器_1_bne ,
       \单周期硬布线控制器_1_jal , \单周期硬布线控制器_1_jalr , \单周期硬布线控制器_1_lb , \单周期硬布线控制器_1_memtoreg ,
       \单周期硬布线控制器_1_memwrite , \单周期硬布线控制器_1_regwrite , \单周期硬布线控制器_1_s_type , \单周期硬布线控制器_1_uret ;
  wire [1:0] EX_R1Forword, EX_R2Forword, MEM_ALUHIGH, mem_wb_1_aluresulthighout, R1_Forword, R2_Forword;
  wire [2:0] PC_SRC;
  wire [3:0] id_ex_1_aluopout, \单周期硬布线控制器_1_alu_op ;
  wire [4:0] EX_RegWriteDest_num, MEM_RegWriteDest_num, multiplexer_3_out, multiplexer_4_out, RegWriteDest;
  wire [7:0] multiplexer_8_out, multiplexer_12_out;
  wire [11:0] multiplexer_5_out;
  wire [12:0] CNT_num;
  wire [15:0] \LoadUse次数 , \总周期数 , \无条件分支数 , \条件分支成功数 ;
  wire [31:0] adder_1_out, adder_2_out, adder_3_out, adder_4_out, adder_5_out, alu_1_result, and_6_out,
       bit_extender_1_out, bit_extender_2_out, bit_extender_3_out, bit_extender_4_out, bit_extender_5_out,
       EX_IR, EX_R1, EX_R2, id_ex_1_immbout, id_ex_1_immjout, id_ex_1_immout, ID_IR, IF_IR, MEM_DATAOUT,
       MEM_IR, MEM_ReadData, mem_wb_1_aluresultout, mem_wb_1_memdataout, multiplexer_6_out,
       multiplexer_9_out, multiplexer_10_out, multiplexer_13_out, multiplexer_14_out, NEXT_PC, R1, R2,
       regifile4bubble_1_r1, regifile4bubble_1_r2, shifter_1_out, shifter_2_out, WB_IR;
  wire [31:2] ex_mem_1_aluresultout;

  Button \u_总复位  (.out(RST));
  Button _1 (.out(IR1));
  Button _2 (.out(IR2));
  Button _3 (.out(IR3));
  // Probe on \总周期数 
  // Probe on \总周期数 
  Button \u_继续运行  (.out(Go));
  LED #(.active("true")) led_1 (.in(W1));
  LED #(.active("true")) led_2 (.in(W2));
  LED #(.active("true")) led_3 (.in(W3));
  or or_1 (or_1_out, Go, not_1_out);
  not not_1 (not_1_out, halt);
  Hex_Digit_Display hex_digit_display_1 (.value(LedData[31:28]));  // open: dp
  // Probe on IF_PC[19:0]
  // RiscV_Probe riscv_probe_1: pin names not known; wires that end beside it: IF_IR
  Counter #(.width(16), .max('hffff), .ongoal("wrap"), .trigger("rising"), .behavior("new")) counter_1 (
    .count(or_1_out), .Q(\总周期数 ), .clk(CLK), .clr(RST));  // open: load, D, carry, preset, down
  and and_1 (and_1_out, or_1_out, not_2_out);
  not not_2 (not_2_out, load_use);
  Hex_Digit_Display hex_digit_display_2 (.value(LedData[27:24]));  // open: dp
  Hex_Digit_Display hex_digit_display_3 (.value(LedData[23:20]));  // open: dp
  // Probe on ID_PC[19:0]
  // RiscV_Probe riscv_probe_2: pin names not known; wires that end beside it: ID_IR
  Register #(.width(32), .trigger("rising"), .Select("low")) PC (
    .D(NEXT_PC), .en(and_1_out), .Q(IF_PC), .clk(CLK), .clr(RST));
  Hex_Digit_Display hex_digit_display_4 (.value(LedData[19:16]));  // open: dp
  Hex_Digit_Display hex_digit_display_5 (.value(LedData[15:12]));  // open: dp
  not not_3 (not_3_out, halt);
  Hex_Digit_Display hex_digit_display_6 (.value(LedData[11:8]));  // open: dp
  Hex_Digit_Display hex_digit_display_7 (.value(LedData[7:4]));  // open: dp
  // Probe on EX_PC[19:0]
  // RiscV_Probe riscv_probe_3: pin names not known; wires that end beside it: EX_IR
  nor nor_1 (nor_1_out, Go, not_3_out);
  Hex_Digit_Display hex_digit_display_8 (.value(LedData[3:0]));  // open: dp
  ROM #(.addrWidth(10), .dataWidth(32), .Select("low")) rom_1 (.addr(IF_PC[11:2]), .data(IF_IR));
  // Probe on \总周期数 
  // Probe on M_PC[19:0]
  // RiscV_Probe riscv_probe_4: pin names not known; wires that end beside it: MEM_IR
  IF_ID if_id_1 (
    .IR(IF_IR), .PC(IF_PC), .IRout(ID_IR), .PCout(ID_PC), .bubble(InBranch), .EN(or_2_out), .CLK(CLK),
    .RESET(RST));  // open: PREDICT_JUMP, PREDICT_JUMPout
  // Probe on \总周期数 
  // Probe on \无条件分支数 
  // Probe on \条件分支成功数 
  // Probe on \LoadUse次数 
  // Probe on \LoadUse次数 
  Counter #(.width(16), .max('hffff), .ongoal("wrap"), .trigger("rising"), .behavior("new")) counter_2 (
    .count(load_use), .Q(\LoadUse次数 ), .clk(CLK), .clr(RST));  // open: load, D, carry, preset, down
  or or_2 (or_2_out, nor_1_out, load_use);
  // Probe on IF_PC[11:0]
  // Probe on WB_PC[19:0]
  // RiscV_Probe riscv_probe_5: pin names not known; wires that end beside it: WB_IR
  \流水冲突检测器4重定向  \u_流水冲突检测器4重定向_1  (
    .EX_RegWrite(EX_RegWrite), .MEM_RegWrite(MEM_RegWrite), .EX_RegWriteDest_num(EX_RegWriteDest_num),
    .MEM_RegWriteDest_num(MEM_RegWriteDest_num), .IR(ID_IR), .ecall(IR_ecall), .load_use(load_use),
    .EX_MEMToReg(EX_MemToReg), .R1_Forword(R1_Forword), .R2_Forword(R2_Forword));
  Multiplexer #(.select(2), .width(32), .disabled("Z"), .enable("false")) multiplexer_1 (
    .in0(EX_R1), .in1(RDin), .in2(MEM_DATAOUT), .in3(MEM_DATAOUT), .out(R1), .sel(EX_R1Forword));
  Multiplexer #(.select(2), .width(32), .disabled("Z"), .enable("false")) multiplexer_2 (
    .in0(EX_R2), .in1(RDin), .in2(MEM_DATAOUT), .in3(MEM_DATAOUT), .out(R2), .sel(EX_R2Forword));
  // Probe on ID_PC[11:0]
  // Probe on EX_PC[11:0]
  \单周期硬布线控制器  \u_单周期硬布线控制器_1  (
    .Funct({ID_IR[30], ID_IR[25], ID_IR[14:12]}), .OP(ID_IR[6:2]), .ALU_OP(\单周期硬布线控制器_1_alu_op ),
    .MemToReg(\单周期硬布线控制器_1_memtoreg ), .MemWrite(\单周期硬布线控制器_1_memwrite ), .ALU_SRC(\单周期硬布线控制器_1_alu_src ),
    .RegWrite(\单周期硬布线控制器_1_regwrite ), .ecall(IR_ecall), .S_type(\单周期硬布线控制器_1_s_type ),
    .Jalr(\单周期硬布线控制器_1_jalr ), .Beq(\单周期硬布线控制器_1_beq ), .JAL(\单周期硬布线控制器_1_jal ), .Bne(\单周期硬布线控制器_1_bne ),
    .in_3(ID_IR[21]), .uret(\单周期硬布线控制器_1_uret ), .BLT(\单周期硬布线控制器_1_blt ), .LB(\单周期硬布线控制器_1_lb ));  // open: CSRRSI, CSRRCI
  Multiplexer #(.select(1), .width(5), .disabled("Z"), .enable("false")) multiplexer_3 (
    .in0(ID_IR[19:15]), .in1(5'b01010), .out(multiplexer_3_out), .sel(IR_ecall));
  Multiplexer #(.select(1), .width(5), .disabled("Z"), .enable("false")) multiplexer_4 (
    .in0(ID_IR[24:20]), .in1(5'b10001), .out(multiplexer_4_out), .sel(IR_ecall));
  Multiplexer #(.select(1), .width(12), .disabled("Z"), .enable("false")) multiplexer_5 (
    .in0(ID_IR[31:20]), .in1({ID_IR[31:25], ID_IR[11:7]}), .out(multiplexer_5_out), .sel(\单周期硬布线控制器_1_s_type ));
  // Probe on M_PC[11:0]
  D_Flip_Flop #(.trigger("high"), .Pre_Clr_Positions("LEGACY"), .NegatePresetClear("false"), .enable("true"), .NewFFLayout("false")) d_ff_1 (.Q(d_ff_1_q));  // open: clk, D, Qn, preset, en, reset
  // Probe on 13'h373
  assign bit_extender_1_out = {{20{multiplexer_5_out[11]}}, multiplexer_5_out};  // Bit_Extender bit_extender_1
  assign bit_extender_2_out = {{20{ID_IR[31]}}, {ID_IR[31], ID_IR[7], ID_IR[30:25], ID_IR[11:8]}};  // Bit_Extender bit_extender_2
  assign bit_extender_3_out = {{12{ID_IR[31]}}, {ID_IR[31], ID_IR[19:12], ID_IR[20], ID_IR[30:21]}};  // Bit_Extender bit_extender_3
  // Probe on WB_PC[11:0]
  Comparator #(.width(13), .mode("twosComplement")) comparator_1 (
    .a(CNT_num), .b(13'h373), .eq(comparator_1_eq), .lt(comparator_1_lt));  // open: gt
  Clock #(.highDuration(1), .lowDuration(1)) clock_1 (.out(clock_1_out));
  nand nand_1 (nand_1_out, d_ff_1_q, comparator_1_eq);
  Counter #(.width(13), .max('h1fff), .ongoal("stay"), .trigger("rising"), .behavior("old")) counter_3 (
    .count(comparator_1_lt), .Q(CNT_num), .clk(clock_1_out));  // open: load, D, carry, clr, preset
  Comparator #(.width(32), .mode("twosComplement")) comparator_2 (
    .a({32{1'b0}}), .b(ID_IR), .gt(comparator_2_gt), .eq(comparator_2_eq));  // open: lt
  Regifile4Bubble regifile4bubble_1 (
    .Din(RDin), .Clk(CLK), .R1(regifile4bubble_1_r1), .R2(regifile4bubble_1_r2), .WE(RegWrite),
    .W_num(RegWriteDest), .R1_num(multiplexer_3_out), .R2_num(multiplexer_4_out));
  not not_4 (not_4_out, halt);
  assign CLK = nand_1_out ? clock_1_out : 1'bz;  // Controlled_Buffer controlled_buffer_1
  and and_2 (and_2_out, \单周期硬布线控制器_1_regwrite , not_5_out);
  not not_5 (not_5_out, comparator_2_eq);
  nor nor_2 (nor_2_out, Go, not_4_out);
  Pull_Resistor #(.pull(1)) pull_resistor_1 (.node(CLK));
  ID_EX id_ex_1 (
    .JAL(\单周期硬布线控制器_1_jal ), .BLT(\单周期硬布线控制器_1_blt ), .JALR(\单周期硬布线控制器_1_jalr ), .LB(\单周期硬布线控制器_1_lb ),
    .URET(\单周期硬布线控制器_1_uret ), .BEQ(\单周期硬布线控制器_1_beq ), .BNE(\单周期硬布线控制器_1_bne ),
    .MemToReg(\单周期硬布线控制器_1_memtoreg ), .MemWrite(\单周期硬布线控制器_1_memwrite ), .AluOP(\单周期硬布线控制器_1_alu_op ),
    .AluSrcB(\单周期硬布线控制器_1_alu_src ), .RegWrite(and_2_out), .R1(regifile4bubble_1_r1),
    .R2(regifile4bubble_1_r2), .Imm(bit_extender_1_out), .IR(ID_IR), .PC(ID_PC), .bubble(or_3_out),
    .EN(nor_2_out), .CLK(CLK), .JALout(JAL), .BLTout(BLT), .JALRout(JALR), .LBout(id_ex_1_lbout),
    .BEQout(BEQ), .BNEout(BNE), .MemToRegout(EX_MemToReg), .MemWriteout(id_ex_1_memwriteout),
    .AluOPout(id_ex_1_aluopout), .AluSrcBout(id_ex_1_alusrcbout), .RegWriteout(EX_RegWrite), .R1out(EX_R1),
    .R2out(EX_R2), .Immout(id_ex_1_immout), .IRout(EX_IR), .PCout(EX_PC), .RESET(RST), .ecallout(ecall),
    .ecall(IR_ecall), .ImmB(bit_extender_2_out), .ImmJ(bit_extender_3_out), .ImmBout(id_ex_1_immbout),
    .ImmJout(id_ex_1_immjout), .WriteDest_num(ID_IR[11:7]), .WriteDest_out(EX_RegWriteDest_num),
    .R1_Forword(R1_Forword), .R2_Forword(R2_Forword), .R1_Forwordout(EX_R1Forword),
    .R2_Forwordout(EX_R2Forword));  // open: URETout, PREDICT_JUMP, PREDICT_JUMPout
  or or_3 (or_3_out, InBranch, load_use);
  not not_6 (not_6_out, ALU_EQU);
  and and_3 (and_3_out, BNE, not_6_out);
  and and_4 (and_4_out, ALU_EQU, BEQ);
  and and_5 (and_5_out, BLT, ALU_LESS);
  Multiplexer #(.select(1), .width(32), .disabled("Z"), .enable("false")) multiplexer_6 (
    .in0(R2), .in1(id_ex_1_immout), .out(multiplexer_6_out), .sel(id_ex_1_alusrcbout));
  Shifter #(.width(32), .shift("ll")) shifter_1 (.in(id_ex_1_immbout), .\dist (5'b00001), .out(shifter_1_out));
  Shifter #(.width(32), .shift("ll")) shifter_2 (.in(id_ex_1_immjout), .\dist (5'b00001), .out(shifter_2_out));
  Adder #(.width(32)) adder_1 (.a(shifter_1_out), .b(EX_PC), .out(adder_1_out));  // open: cin, cout
  Adder #(.width(32)) adder_2 (.a(shifter_2_out), .b(EX_PC), .out(adder_2_out));  // open: cin, cout
  Adder #(.width(32)) adder_3 (.a(IF_PC), .b(32'h4), .out(adder_3_out));  // open: cin, cout
  Priority_Encoder #(.select(3), .disabled("Z")) priority_encoder_1 (
    .in0(1'b1), .in1(and_3_out), .in2(and_4_out), .in3(JAL), .in4(JALR), .in5(and_5_out), .out(PC_SRC));  // open: in6, in7, gs, en_out, en_in
  or or_4 (InBranch, JAL, JALR, Branch_Success);
  or or_5 (or_5_out, JALR, JAL);
  ALU alu_1 (
    .X(R1), .Y(multiplexer_6_out), .AluOP(id_ex_1_aluopout), .Equal(ALU_EQU), .Result(alu_1_result),
    .out_6(ALU_LESS));  // open: Result_2, out_4
  or or_6 (Branch_Success, and_4_out, and_3_out, and_5_out);
  Counter #(.width(16), .max('hffff), .ongoal("wrap"), .trigger("rising"), .behavior("new")) counter_4 (
    .count(or_5_out), .Q(\无条件分支数 ), .clk(CLK), .clr(RST));  // open: load, D, carry, preset, down
  assign and_6_out = alu_1_result & 32'hfffffffe;  // AND_Gate and_6, 32 bits wide
  EX_MEM ex_mem_1 (
    .JAL(JAL), .JALR(JALR), .LB(id_ex_1_lbout), .MemToReg(EX_MemToReg), .MemWrite(id_ex_1_memwriteout),
    .RegWrite(EX_RegWrite), .ALUResult(alu_1_result), .R2(R2), .RegWriteDest(EX_RegWriteDest_num),
    .IR(EX_IR), .PC(EX_PC), .JALout(ex_mem_1_jalout), .JALRout(ex_mem_1_jalrout), .LBout(ex_mem_1_lbout),
    .MemToRegout(ex_mem_1_memtoregout), .MemWriteout(MemWrite), .RegWriteout(MEM_RegWrite),
    .ALUResultout({ex_mem_1_aluresultout, MEM_ALUHIGH}), .R2out(MDin),
    .RegWriteDestout(MEM_RegWriteDest_num), .IRout(MEM_IR), .PCout(M_PC), .RESET(RST), .bubble(1'b0),
    .EN(nor_3_out), .CLK(CLK), .BLT(BLT), .BLTout(ex_mem_1_bltout), .halt(haltsign),
    .haltout(ex_mem_1_haltout));
  Multiplexer #(.select(3), .width(32), .disabled("Z"), .enable("false")) multiplexer_7 (
    .in0(adder_3_out), .in1(adder_1_out), .in2(adder_1_out), .in3(adder_2_out), .in4(and_6_out),
    .in5(adder_1_out), .out(NEXT_PC), .sel(PC_SRC));  // open: in6, in7
  Multiplexer #(.select(2), .width(8), .disabled("Z"), .enable("false")) multiplexer_8 (
    .in0(MEM_ReadData[7:0]), .in1(MEM_ReadData[15:8]), .in2(MEM_ReadData[23:16]), .in3(MEM_ReadData[31:24]),
    .out(multiplexer_8_out), .sel(MEM_ALUHIGH));
  assign bit_extender_4_out = {{24{multiplexer_8_out[7]}}, multiplexer_8_out};  // Bit_Extender bit_extender_4
  Counter #(.width(16), .max('hffff), .ongoal("wrap"), .trigger("rising"), .behavior("new")) counter_5 (
    .count(Branch_Success), .Q(\条件分支成功数 ), .clk(CLK), .clr(RST));  // open: load, D, carry, preset, down
  Multiplexer #(.select(1), .width(32), .disabled("Z"), .enable("false")) multiplexer_9 (
    .in0(MEM_ReadData), .in1(bit_extender_4_out), .out(multiplexer_9_out), .sel(ex_mem_1_lbout));
  or or_7 (or_7_out, ex_mem_1_jalrout, ex_mem_1_jalout);
  Multiplexer #(.select(1), .width(32), .disabled("Z"), .enable("false")) multiplexer_10 (
    .in0({ex_mem_1_aluresultout, MEM_ALUHIGH}), .in1(multiplexer_9_out), .out(multiplexer_10_out),
    .sel(ex_mem_1_memtoregout));
  Multiplexer #(.select(1), .width(32), .disabled("Z"), .enable("false")) multiplexer_11 (
    .in0(multiplexer_10_out), .in1(adder_4_out), .out(MEM_DATAOUT), .sel(or_7_out));
  Adder #(.width(32)) adder_4 (.a(32'h4), .b(M_PC), .out(adder_4_out));  // open: cin, cout
  RAM #(.addrWidth(10), .dataWidth(32), .bus("separate"), .Select("high")) ram_1 (
    .addr(ex_mem_1_aluresultout[11:2]), .din(MDin), .data(MEM_ReadData), .str(MemWrite), .clk(CLK));  // open: sel, ld, clr
  not not_7 (not_7_out, halt);
  nor nor_3 (nor_3_out, Go, not_7_out);
  MEM_WB mem_wb_1 (
    .JAL(ex_mem_1_jalout), .JALR(ex_mem_1_jalrout), .LB(ex_mem_1_lbout), .MemToReg(ex_mem_1_memtoregout),
    .RegWrite(MEM_RegWrite), .ALUResult({ex_mem_1_aluresultout, MEM_ALUHIGH}),
    .RegWriteDest(MEM_RegWriteDest_num), .IR(MEM_IR), .PC(M_PC), .JALout(mem_wb_1_jalout),
    .JALRout(mem_wb_1_jalrout), .LBout(mem_wb_1_lbout), .MemToRegout(mem_wb_1_memtoregout),
    .RegWriteout(RegWrite), .ALUResultout(mem_wb_1_aluresultout), .RegWriteDestout(RegWriteDest),
    .MemDataout(mem_wb_1_memdataout), .IRout(WB_IR), .PCout(WB_PC), .RESET(RST), .bubble(1'b0),
    .EN(nor_3_out), .CLK(CLK), .BLT(ex_mem_1_bltout), .ALUResultHigh(MEM_ALUHIGH),
    .ALUResultHighout(mem_wb_1_aluresulthighout), .MemData(MEM_ReadData), .halt(ex_mem_1_haltout),
    .haltout(halt));  // open: BLTout
  Comparator #(.width(32), .mode("twosComplement")) comparator_3 (
    .a(R2), .b(32'h22), .eq(comparator_3_eq));  // open: gt, lt
  Multiplexer #(.select(2), .width(8), .disabled("Z"), .enable("false")) multiplexer_12 (
    .in0(mem_wb_1_memdataout[7:0]), .in1(mem_wb_1_memdataout[15:8]), .in2(mem_wb_1_memdataout[23:16]),
    .in3(mem_wb_1_memdataout[31:24]), .out(multiplexer_12_out), .sel(mem_wb_1_aluresulthighout));
  and and_7 (and_7_out, ecall, comparator_3_eq);
  assign bit_extender_5_out = {{24{multiplexer_12_out[7]}}, multiplexer_12_out};  // Bit_Extender bit_extender_5
  Register #(.width(32), .trigger("rising"), .Select("low")) register_1 (
    .D(R1), .en(and_7_out), .Q(LedData), .clk(CLK), .clr(RST));
  Multiplexer #(.select(1), .width(32), .disabled("Z"), .enable("false")) multiplexer_13 (
    .in0(mem_wb_1_memdataout), .in1(bit_extender_5_out), .out(multiplexer_13_out), .sel(mem_wb_1_lbout));
  not not_8 (not_8_out, comparator_3_eq);
  Multiplexer #(.select(1), .width(32), .disabled("Z"), .enable("false")) multiplexer_14 (
    .in0(mem_wb_1_aluresultout), .in1(multiplexer_13_out), .out(multiplexer_14_out),
    .sel(mem_wb_1_memtoregout));
  and and_8 (haltsign, ecall, not_8_out);
  or or_8 (or_8_out, mem_wb_1_jalout, mem_wb_1_jalrout);
  Adder #(.width(32)) adder_5 (.a(WB_PC), .b(32'h4), .out(adder_5_out));  // open: cin, cout
  Multiplexer #(.select(1), .width(32), .disabled("Z"), .enable("false")) multiplexer_15 (
    .in0(multiplexer_14_out), .in1(adder_5_out), .out(RDin), .sel(or_8_out));

  // Other names for the same wires on the sheet: MEM_PC[31:0] = M_PC; 插入气泡数[15:0] = \LoadUse次数 

  // Notes on the sheet:
  //   中断源
  //   时空图监测，可删除
  //   中断等待指示
  //   数码管输出
  //   contents of rom_1 (hex, n*v repeats v):
  //   100493 100006f 100493 200913 300993 100006f 100493 200913 300993 100006f 100493 200913 300993
  //   100006f 100493 200913 300993 3cc000ef 100413 100493 1f49493 900533 2200893 73 24d493 48463 fedff06f
  //   900533 2200893 73 100493 249493 900533 2200893 73 48463 fedff06f 100493 1f49493 900533 2200893 73
  //   4034d493 900533 2200893 73 4044d493 900533 2200893 73 4044d493 900533 2200893 73 4044d493 900533
  //   2200893 73 4044d493 900533 2200893 73 4044d493 900533 2200893 73 4044d493 900533 2200893 73 4044d493
  //   900533 2200893 73 100413 1f41993 41f9d993 433 c00913 300b13 140413 f47413 800293 100313 499993
  //   89e9b3 1300533 2200893 73 406282b3 fe0294e3 140413 f00f93 1f47433 1c41413 800293 100313 49d993
  //   89e9b3 1300533 2200893 73 406282b3 fe0294e3 1c45413 406b0b33 b0463 f95ff06f 2b3 fff2c293 829293
  //   ff2e293 500533 2200893 73 fff00413 493 84a023 140413 448493 84a023 140413 448493 84a023 140413
  //   448493 84a023 140413 448493 84a023 140413 448493 84a023 140413 448493 84a023 140413 448493 84a023
  //   140413 448493 84a023 140413 448493 84a023 140413 448493 84a023 140413 448493 84a023 140413 448493
  //   84a023 140413 448493 84a023 140413 448493 84a023 140413 448493 84a023 140413 448493 140413 433
  //   3c00493 42983 4aa03 149a2b3 28663 134a023 1442023 ffc48493 fe9412e3 800533 2200893 73 440413 3c00493
  //   fc9416e3 3200893 73 100293 300313 800493 849493 7648493 1449493 900533 2200893 73 800e13 4054d4b3
  //   4064d4b3 900533 2200893 73 fffe0e13 fe0e14e3 a00893 73 fff00293 7700493 849493 7748493 900533
  //   2200893 73 1000e13 54c4b3 900533 2200893 73 fffe0e13 fe0e16e3 a00893 73 313 1000e13 13 8400493
  //   849493 8348493 400913 891913 490913 849493 8248493 849493 8148493 891913 490913 891913 490913 932023
  //   12484b3 430313 fffe0e13 fe0e18e3 2000e13 313 30483 900533 2200893 73 130313 fffe0e13 fe0e14e3 a00893
  //   73 ff100493 900533 2200893 73 148493 fe04c8e3 a00893 73 413 140413 800533 2200893 73 240413 800533
  //   2200893 73 340413 800533 2200893 73 440413 800533 2200893 73 540413 800533 2200893 73 640413 800533
  //   2200893 73 740413 800533 2200893 73 840413 800533 2200893 2200893 73 8067
  //   MEM段写寄存器，将写回数据先返回
  //   EX段写寄存器，将MEM段数据提前返回
  //   R1
  //   R2
  //   WriteReg#
  //   I
  //   S
  //   B
  //   J
  //   流水调试日志用
  //   暂停节拍，不能为0
  //   戳工具置1进入计数暂停模式，ctrl+k时钟自动运行到对应节拍暂停
  //   ctrl+k关闭时钟连续运行，将控制位置零，进入单步调试模式调试
  //   用这个时钟源需要去掉电路中的其他时钟源
  //   可计数暂停的时钟源
  //   为方便自动评测，需要输出流水线各段保存的PC值，注意是PC不是PC+4，另外ID段寄存器写入信息，Mem段内存写入信息也要输出
endmodule

module \中断按键参考电路  (
  input  \同步清零信号 ,
  output \与中断屏蔽位与 
);

  wire \_1号中断_out , and_1_out, clock_1_out, d_ff_1_q, or_1_out, or_2_out;

  Clock #(.highDuration(1), .lowDuration(1)) clock_1 (.out(clock_1_out));
  Button \_1号中断  (.out(\_1号中断_out ));
  LED #(.active("true")) \_1号中断等待指示灯  (.in(or_1_out));
  or or_1 (or_1_out, \与中断屏蔽位与 , d_ff_1_q);
  D_Flip_Flop #(.trigger("rising"), .Pre_Clr_Positions("LEGACY"), .NegatePresetClear("false"), .enable("true"), .NewFFLayout("false")) d_ff_1 (
    .clk(\_1号中断_out ), .D(1'b1), .Q(d_ff_1_q), .reset(\与中断屏蔽位与 ));  // open: Qn, preset, en
  or or_2 (or_2_out, d_ff_1_q, \与中断屏蔽位与 );
  and and_1 (and_1_out, or_2_out, ~\同步清零信号 );  // AND_Gate
  D_Flip_Flop #(.trigger("rising"), .Pre_Clr_Positions("LEGACY"), .NegatePresetClear("false"), .enable("true"), .NewFFLayout("false")) IR1 (
    .clk(clock_1_out), .D(and_1_out), .Q(\与中断屏蔽位与 ));  // open: Qn, preset, en, reset

  // Notes on the sheet:
  //   中断信号采样参考电路
  //   Reset 
endmodule
module \单周期_单级中断  (
  input  IR1,
  input  IR2,
  input  IR3,
  output RegWrite,
  output MemWrite,
  output [31:0] PC,
  output [31:0] IR,
  output [31:0] RDin,
  output [31:0] MDin,
  output [31:0] LedData
);

  wire ALU_EQU, ALU_LESS, and_2_out, and_3_out, and_4_out, and_6_out, and_7_out, BEQ, BLT, BNE, CLK,
       clock_1_out, CLRA, CLRB, CLRC, comparator_1_eq, comparator_2_eq, comparator_3_eq, comparator_4_eq,
       comparator_5_eq, comparator_6_eq, comparator_6_lt, d_ff_1_q, ecall, Go, halt, IE, INTR, INTRA, INTRB,
       INTRC, IR1_t, IR2_t, IR3_t, IRA, IRB, IRC, JAL, JALR, LB, M2Reg, nand_1_out, not_1_out, not_2_out,
       not_3_out, not_4_out, not_5_out, or_1_out, or_2_out, or_4_out, or_10_out, or_11_out, or_12_out,
       or_13_out, register_5_q, register_6_q, register_7_q, RST, URET, W1, W2, W3, \单周期硬布线控制器_1_alu_src ,
       \单周期硬布线控制器_1_s_type ;
  wire [1:0] priority_encoder_2_out, priority_encoder_3_out, register_2_q;
  wire [2:0] PC_SRC;
  wire [3:0] \单周期硬布线控制器_1_alu_op ;
  wire [4:0] multiplexer_1_out, multiplexer_2_out;
  wire [7:0] multiplexer_7_out;
  wire [11:0] multiplexer_3_out;
  wire [12:0] CNT_num;
  wire [15:0] \总周期数 ;
  wire [31:0] adder_2_out, adder_3_out, alu_1_result, and_5_out, bit_extender_1_out, bit_extender_2_out,
       bit_extender_3_out, bit_extender_4_out, EPC, INTR_PC, multiplexer_4_out, multiplexer_6_out,
       multiplexer_8_out, multiplexer_10_out, NEXT_PC, PC_4, R1, ram_1_data, shifter_1_out, shifter_2_out;

  Button \u_继续运行  (.out(Go));
  Button \u_复位  (.out(RST));
  Button _1 ();  // open: out
  Button _2 ();  // open: out
  Button _3 ();  // open: out
  LED #(.active("true")) led_1 (.in(W1));
  LED #(.active("true")) led_2 (.in(W2));
  LED #(.active("true")) led_3 (.in(W3));
  Hex_Digit_Display hex_digit_display_1 (.value(LedData[31:28]));  // open: dp
  Comparator #(.width(16), .mode("twosComplement")) comparator_1 (
    .a(16'h23b), .b(\总周期数 ), .eq(comparator_1_eq));  // open: gt, lt
  Comparator #(.width(16), .mode("twosComplement")) comparator_2 (
    .a(\总周期数 ), .b(16'h1), .eq(comparator_2_eq));  // open: gt, lt
  Comparator #(.width(16), .mode("twosComplement")) comparator_3 (
    .a(\总周期数 ), .b(16'h4), .eq(comparator_3_eq));  // open: gt, lt
  Comparator #(.width(16), .mode("twosComplement")) comparator_4 (
    .a(\总周期数 ), .b(16'h7), .eq(comparator_4_eq));  // open: gt, lt
  Register #(.width(32), .trigger("rising"), .Select("low")) u_PC (
    .D(NEXT_PC), .en(not_1_out), .Q(PC), .clk(CLK), .clr(RST));
  not not_1 (not_1_out, halt);
  Hex_Digit_Display hex_digit_display_2 (.value(LedData[23:20]));  // open: dp
  Hex_Digit_Display hex_digit_display_3 (.value(LedData[27:24]));  // open: dp
  or or_1 (or_1_out, comparator_1_eq, comparator_2_eq);
  Pull_Resistor #(.pull(0)) pull_resistor_1 (.node(IRA));
  assign IRA = or_1_out ? ~CLK : 1'bz;  // Controlled_Inverter controlled_inverter_1
  Pull_Resistor #(.pull(0)) pull_resistor_2 (.node(IRB));
  assign IRB = comparator_3_eq ? ~CLK : 1'bz;  // Controlled_Inverter controlled_inverter_2
  Pull_Resistor #(.pull(0)) pull_resistor_3 (.node(IRC));
  assign IRC = comparator_4_eq ? ~CLK : 1'bz;  // Controlled_Inverter controlled_inverter_3
  Hex_Digit_Display hex_digit_display_4 (.value(LedData[19:16]));  // open: dp
  Hex_Digit_Display hex_digit_display_5 (.value(LedData[15:12]));  // open: dp
  Hex_Digit_Display hex_digit_display_6 (.value(LedData[7:4]));  // open: dp
  Hex_Digit_Display hex_digit_display_7 (.value(LedData[11:8]));  // open: dp
  // Probe on \总周期数 
  // Probe on \总周期数 
  // RiscV_Probe riscv_probe_1: pin names not known; wires that end beside it: IR
  ROM #(.addrWidth(10), .dataWidth(32), .Select("high")) rom_1 (.addr(PC[11:2]), .data(IR));
  Hex_Digit_Display hex_digit_display_8 (.value(LedData[3:0]));  // open: dp
  or or_2 (or_2_out, INTRA, INTRB, INTRC);
  not not_2 (not_2_out, or_2_out);
  \单周期硬布线控制器  \u_单周期硬布线控制器_1  (
    .Funct({IR[30], IR[25], IR[14:12]}), .OP(IR[6:2]), .ALU_OP(\单周期硬布线控制器_1_alu_op ), .MemToReg(M2Reg),
    .MemWrite(MemWrite), .ALU_SRC(\单周期硬布线控制器_1_alu_src ), .RegWrite(RegWrite), .ecall(ecall),
    .S_type(\单周期硬布线控制器_1_s_type ), .Jalr(JALR), .Beq(BEQ), .JAL(JAL), .Bne(BNE), .in_3(IR[21]), .uret(URET),
    .BLT(BLT), .LB(LB));  // open: CSRRSI, CSRRCI
  Multiplexer #(.select(1), .width(5), .disabled("Z"), .enable("false")) multiplexer_1 (
    .in0(IR[19:15]), .in1(5'b01010), .out(multiplexer_1_out), .sel(ecall));
  or or_3 (IR1_t, IR1, IRA);
  and and_1 (INTR, IE, or_2_out);
  or or_4 (or_4_out, not_2_out, URET);
  Multiplexer #(.select(1), .width(5), .disabled("Z"), .enable("false")) multiplexer_2 (
    .in0(IR[24:20]), .in1(5'b10001), .out(multiplexer_2_out), .sel(ecall));
  Multiplexer #(.select(1), .width(12), .disabled("Z"), .enable("false")) multiplexer_3 (
    .in0(IR[31:20]), .in1({IR[31:25], IR[11:7]}), .out(multiplexer_3_out), .sel(\单周期硬布线控制器_1_s_type ));
  or or_5 (IR2_t, IR2, IRB);
  Register #(.width(1), .trigger("rising"), .Select("low")) register_1 (
    .D(or_4_out), .Q(IE), .clk(CLK));  // open: en, clr
  assign bit_extender_1_out = {{20{multiplexer_3_out[11]}}, multiplexer_3_out};  // Bit_Extender bit_extender_1
  assign bit_extender_2_out = {{20{IR[31]}}, {IR[31], IR[7], IR[30:25], IR[11:8]}};  // Bit_Extender bit_extender_2
  assign bit_extender_3_out = {{12{IR[31]}}, {IR[31], IR[19:12], IR[20], IR[30:21]}};  // Bit_Extender bit_extender_3
  and and_2 (and_2_out, BNE, not_3_out);
  not not_3 (not_3_out, ALU_EQU);
  and and_3 (and_3_out, ALU_EQU, BEQ);
  and and_4 (and_4_out, ALU_LESS, BLT);
  Regifile regifile_1 (
    .Din(RDin), .Clk(CLK), .R1(R1), .R2(MDin), .WE(RegWrite), .W_num(IR[11:7]), .R1_num(multiplexer_1_out),
    .R2_num(multiplexer_2_out));
  Shifter #(.width(32), .shift("ll")) shifter_1 (.in(bit_extender_2_out), .\dist (5'b00001), .out(shifter_1_out));
  Shifter #(.width(32), .shift("ll")) shifter_2 (.in(bit_extender_3_out), .\dist (5'b00001), .out(shifter_2_out));
  or or_6 (IR3_t, IR3, IRC);
  Multiplexer #(.select(1), .width(32), .disabled("Z"), .enable("false")) multiplexer_4 (
    .in0(MDin), .in1(bit_extender_1_out), .out(multiplexer_4_out), .sel(\单周期硬布线控制器_1_alu_src ));
  Adder #(.width(32)) adder_1 (.a(32'h4), .b(PC), .out(PC_4));  // open: cin, cout
  Adder #(.width(32)) adder_2 (.a(shifter_1_out), .b(PC), .out(adder_2_out));  // open: cin, cout
  Adder #(.width(32)) adder_3 (.a(shifter_2_out), .b(PC), .out(adder_3_out));  // open: cin, cout
  ALU alu_1 (
    .X(R1), .Y(multiplexer_4_out), .AluOP(\单周期硬布线控制器_1_alu_op ), .Equal(ALU_EQU), .Result(alu_1_result),
    .out_6(ALU_LESS));  // open: Result_2, out_4
  assign and_5_out = alu_1_result & 32'hfffffffe;  // AND_Gate and_5, 32 bits wide
  Priority_Encoder #(.select(3), .disabled("Z")) priority_encoder_1 (
    .in0(1'b1), .in1(and_2_out), .in2(and_3_out), .in3(JAL), .in4(JALR), .in5(and_4_out), .out(PC_SRC));  // open: in6, in7, gs, en_out, en_in
  Priority_Encoder #(.select(2), .disabled("Z")) priority_encoder_2 (
    .in0(INTRA), .in1(INTRB), .in2(INTRC), .out(priority_encoder_2_out));  // open: in3, gs, en_out, en_in
  Multiplexer #(.select(2), .width(32), .disabled("Z"), .enable("false")) multiplexer_5 (
    .in0(32'h30ac), .in1(32'h3150), .in2(32'h31f4), .out(INTR_PC), .sel(priority_encoder_2_out));  // open: in3
  RAM #(.addrWidth(10), .dataWidth(32), .bus("separate"), .Select("high")) ram_1 (
    .addr(alu_1_result[11:2]), .din(MDin), .data(ram_1_data), .str(MemWrite), .clk(CLK));  // open: sel, ld, clr
  Multiplexer #(.select(3), .width(32), .disabled("Z"), .enable("false")) multiplexer_6 (
    .in0(PC_4), .in1(adder_2_out), .in2(adder_2_out), .in3(adder_3_out), .in4(and_5_out), .in5(adder_2_out),
    .out(multiplexer_6_out), .sel(PC_SRC));  // open: in6, in7
  Register #(.width(2), .trigger("rising"), .Select("low")) register_2 (
    .D(priority_encoder_2_out), .en(INTR), .Q(register_2_q), .clk(CLK));  // open: clr
  Multiplexer #(.select(2), .width(8), .disabled("Z"), .enable("false")) multiplexer_7 (
    .in0(ram_1_data[7:0]), .in1(ram_1_data[15:8]), .in2(ram_1_data[23:16]), .in3(ram_1_data[31:24]),
    .out(multiplexer_7_out), .sel(alu_1_result[1:0]));
  Demultiplexer #(.select(2), .width(1), .tristate("false"), .disabled("Z"), .enable("false")) demultiplexer_1 (
    .out0(CLRA), .out1(CLRB), .out2(CLRC), .in(URET), .sel(register_2_q));  // open: out3
  Comparator #(.width(32), .mode("twosComplement")) comparator_5 (
    .a(MDin), .b(32'h22), .eq(comparator_5_eq));  // open: gt, lt
  assign bit_extender_4_out = {{24{multiplexer_7_out[7]}}, multiplexer_7_out};  // Bit_Extender bit_extender_4
  Register #(.width(32), .trigger("rising"), .Select("low")) register_3 (
    .D(multiplexer_6_out), .en(INTR), .Q(EPC), .clk(CLK));  // open: clr
  D_Flip_Flop #(.trigger("high"), .Pre_Clr_Positions("LEGACY"), .NegatePresetClear("false"), .enable("true"), .NewFFLayout("false")) d_ff_1 (.Q(d_ff_1_q));  // open: clk, D, Qn, preset, en, reset
  // Probe on 13'hc
  and and_6 (and_6_out, ecall, comparator_5_eq);
  Comparator #(.width(13), .mode("twosComplement")) comparator_6 (
    .a(CNT_num), .b(13'hc), .eq(comparator_6_eq), .lt(comparator_6_lt));  // open: gt
  Clock #(.highDuration(1), .lowDuration(1)) clock_1 (.out(clock_1_out));
  Register #(.width(32), .trigger("rising"), .Select("low")) register_4 (
    .D(R1), .en(and_6_out), .Q(LedData), .clk(CLK), .clr(RST));
  Multiplexer #(.select(1), .width(32), .disabled("Z"), .enable("false")) multiplexer_8 (
    .in0(ram_1_data), .in1(bit_extender_4_out), .out(multiplexer_8_out), .sel(LB));
  Multiplexer #(.select(2), .width(32), .disabled("Z"), .enable("false")) multiplexer_9 (
    .in0(multiplexer_6_out), .in1(INTR_PC), .in2(EPC), .out(NEXT_PC), .sel(priority_encoder_3_out));  // open: in3
  Priority_Encoder #(.select(2), .disabled("Z")) priority_encoder_3 (
    .in0(1'b1), .in1(INTR), .in2(URET), .in3(1'b0), .out(priority_encoder_3_out));  // open: gs, en_out, en_in
  Counter #(.width(13), .max('h1fff), .ongoal("stay"), .trigger("rising"), .behavior("old")) counter_1 (
    .count(comparator_6_lt), .Q(CNT_num), .clk(clock_1_out));  // open: load, D, carry, clr, preset
  Register #(.width(1), .trigger("rising"), .Select("low")) register_5 (
    .D(1'b1), .Q(register_5_q), .clk(IRA), .clr(INTRA));  // open: en
  Register #(.width(1), .trigger("rising"), .Select("low")) register_6 (
    .D(1'b1), .Q(register_6_q), .clk(IRB), .clr(INTRB));  // open: en
  Register #(.width(1), .trigger("rising"), .Select("low")) register_7 (
    .D(1'b1), .Q(register_7_q), .clk(IRC), .clr(INTRC));  // open: en
  Multiplexer #(.select(1), .width(32), .disabled("Z"), .enable("false")) multiplexer_10 (
    .in0(alu_1_result), .in1(multiplexer_8_out), .out(multiplexer_10_out), .sel(M2Reg));
  nand nand_1 (nand_1_out, d_ff_1_q, comparator_6_eq);
  or or_7 (W1, INTRA, register_5_q);
  or or_8 (W2, INTRB, register_6_q);
  or or_9 (W3, INTRC, register_7_q);
  not not_4 (not_4_out, comparator_5_eq);
  or or_10 (or_10_out, JAL, JALR);
  assign CLK = nand_1_out ? clock_1_out : 1'bz;  // Controlled_Buffer controlled_buffer_1
  Pull_Resistor #(.pull(1)) pull_resistor_4 (.node(CLK));
  Pull_Resistor #(.pull(1)) pull_resistor_5 (.node(CLK));
  or or_11 (or_11_out, register_5_q, INTRA);
  or or_12 (or_12_out, register_6_q, INTRB);
  or or_13 (or_13_out, register_7_q, INTRC);
  and and_7 (and_7_out, ecall, not_4_out);
  Multiplexer #(.select(1), .width(32), .disabled("Z"), .enable("false")) multiplexer_11 (
    .in0(multiplexer_10_out), .in1(PC_4), .out(RDin), .sel(or_10_out));
  Register #(.width(1), .trigger("rising"), .Select("low")) register_8 (
    .D(or_11_out), .Q(INTRA), .clk(CLK), .clr(CLRA));  // open: en
  Register #(.width(1), .trigger("rising"), .Select("low")) register_9 (
    .D(or_12_out), .Q(INTRB), .clk(CLK), .clr(CLRB));  // open: en
  Register #(.width(1), .trigger("rising"), .Select("low")) register_10 (
    .D(or_13_out), .Q(INTRC), .clk(CLK), .clr(CLRC));  // open: en
  not not_5 (not_5_out, halt);
  Counter #(.width(16), .max('hffff), .ongoal("wrap"), .trigger("rising"), .behavior("new")) counter_2 (
    .count(not_5_out), .Q(\总周期数 ), .clk(CLK), .clr(RST));  // open: load, D, carry, preset, down
  Register #(.width(1), .trigger("falling"), .Select("low")) register_11 (
    .D(and_7_out), .en(not_5_out), .Q(halt), .clk(CLK), .clr(Go));

  // Other names for the same wires on the sheet: R2[31:0] = MDin

  // Notes on the sheet:
  //   中断源
  //   中断等待指示
  //   单级中断测试信号模拟器
  //   数码管输出应该用寄存器锁存，否则显示数据只能一闪而过
  //   总复位信号应将除ROM以外所有存储组件全部清零
  //   数码管输出
  //   指令探针
  //   指令存储器
  //   指令字
  //   contents of rom_1 (hex, n*v repeats v):
  //   7d000113 100413 1f41993 41f9d993 433 c00913 800b13 140413 f47413 800293 100313 499993 89e9b3 1300533
  //   2200893 73 406282b3 fe0294e3 140413 f00f93 1f47433 1c41413 800293 100313 49d993 89e9b3 1300533
  //   2200893 73 406282b3 fe0294e3 1c45413 406b0b33 b0463 f95ff06f 2b3 fff2c293 1029293 fff2e293 500533
  //   2200893 73 f5dff06f 1112023 410113 a12023 410113 812023 410113 1312023 410113 1412023 410113 1512023
  //   410113 1612023 410113 100b13 300a13 100a93 1600433 441413 14469b3 1300533 2200893 73 fe0416e3
  //   415a0a33 fe0a10e3 ffc10113 12b03 ffc10113 12a83 ffc10113 12a03 ffc10113 12983 ffc10113 12403
  //   ffc10113 12503 ffc10113 12883 200073 1112023 410113 a12023 410113 812023 410113 1312023 410113
  //   1412023 410113 1512023 410113 1612023 410113 200b13 300a13 100a93 1600433 441413 14469b3 1300533
  //   2200893 73 fe0416e3 415a0a33 fe0a10e3 ffc10113 12b03 ffc10113 12a83 ffc10113 12a03 ffc10113 12983
  //   ffc10113 12403 ffc10113 12503 ffc10113 12883 200073 1112023 410113 a12023 410113 812023 410113
  //   1312023 410113 1412023 410113 1512023 410113 1612023 410113 300b13 300a13 100a93 1600433 441413
  //   14469b3 1300533 2200893 73 fe0416e3 415a0a33 fe0a10e3 ffc10113 12b03 ffc10113 12a83 ffc10113 12a03
  //   ffc10113 12983 ffc10113 12403 ffc10113 12503 ffc10113 12883 200073
  //   JAL
  //   JALR
  //   URET
  //   R1
  //   a0
  //   R2
  //   I 指令
  //   S 指令
  //   B 指令
  //   J 指令
  //   中断响应
  //   Beq
  //   Bne
  //   AluOP
  //   AluSrcB
  //   RegWrite
  //   a7
  //   MemToReg
  //   MemWrite
  //   数据存储器
  //   为方便自动评测，需要输出PC，IR，寄存器堆写如数据RDin
  //   中断识别
  //   记录中断源，方便清除
  //   RAM写使能MemWrite、RAM写入数据MDin等信号
  //   控制位
  //   暂停节拍，不能为0
  //   戳工具置1进入计数暂停模式，ctrl+k时钟自动运行到对应节拍暂停
  //   ctrl+k关闭时钟连续运行，将控制位置零，进入单步调试模式调试
  //   可计数暂停的时钟源
endmodule

module \单周期_多级中断  (
  input  IR1,
  input  IR2,
  input  IR3,
  output RegWrite,
  output MemWrite,
  output [31:0] PC,
  output [31:0] IR,
  output [31:0] RDin,
  output [31:0] MDin,
  output [31:0] LedData
);

  wire ALU_EQU, ALU_LESS, and_1_out, and_2_out, and_3_out, and_6_out, and_7_out, and_8_out, and_9_out,
       and_10_out, BEQ, BLT, BNE, CLK, clock_1_out, CLRA, CLRB, CLRC, comparator_1_eq, comparator_2_eq,
       comparator_3_eq, comparator_4_eq, comparator_5_eq, comparator_6_eq, comparator_7_gt, comparator_8_eq,
       comparator_8_lt, CSRRCI, CSRRSI, d_ff_1_q, ecall, Go, halt, IE, INTR, INTRA, INTRB, INTRC, IR1_t,
       IR2_t, IR3_t, IRA, IRB, IRC, JAL, JALR, LB, M2Reg, nand_1_out, not_1_out, not_2_out, not_3_out,
       not_5_out, not_6_out, or_1_out, or_2_out, or_4_out, or_5_out, or_8_out, or_9_out, or_13_out,
       or_14_out, or_15_out, pull_resistor_1_node, pull_resistor_2_node, pull_resistor_3_node, register_1_q,
       register_2_q, register_11_q, register_12_q, register_13_q, RST, URET, W1, W2, W3,
       \单周期硬布线控制器_1_alu_src , \单周期硬布线控制器_1_s_type ;
  wire [1:0] alu_1_result, CUR_INT, multiplexer_9_out, multiplexer_13_out, multiplexer_16_out,
       priority_encoder_2_out, priority_encoder_3_out, register_6_q, register_9_q;
  wire [2:0] PC_SRC;
  wire [3:0] \单周期硬布线控制器_1_alu_op ;
  wire [4:0] multiplexer_1_out, multiplexer_3_out;
  wire [7:0] multiplexer_7_out;
  wire [9:0] alu_1_result_2;
  wire [11:0] multiplexer_2_out;
  wire [12:0] CNT_num;
  wire [15:0] \总周期数 ;
  wire [31:0] adder_2_out, adder_3_out, and_4_out, bit_extender_1_out, bit_extender_2_out,
       bit_extender_3_out, bit_extender_4_out, EPC, INTR_PC, IR_PC, multiplexer_4_out, multiplexer_8_out,
       multiplexer_10_out, multiplexer_12_out, multiplexer_14_out, multiplexer_17_out, NEXT_PC, PC_4, R1,
       ram_1_data, register_7_q, register_10_q, shifter_1_out, shifter_2_out;
  wire [31:12] alu_1_result_3;

  Button \u_继续运行  (.out(Go));
  Button \u_复位  (.out(RST));
  Button _1 (.out(IRA));
  Button _2 (.out(IRB));
  Button _3 (.out(IRC));
  LED #(.active("true")) led_1 (.in(W1));
  LED #(.active("true")) led_2 (.in(W2));
  LED #(.active("true")) led_3 (.in(W3));
  not not_1 (not_1_out, halt);
  Hex_Digit_Display hex_digit_display_1 (.value(LedData[31:28]));  // open: dp
  Comparator #(.width(16), .mode("twosComplement")) comparator_1 (
    .a(\总周期数 ), .b(16'h7), .eq(comparator_1_eq));  // open: gt, lt
  Comparator #(.width(16), .mode("twosComplement")) comparator_2 (
    .a(\总周期数 ), .b(16'h241), .eq(comparator_2_eq));  // open: gt, lt
  Register #(.width(32), .trigger("rising"), .Select("low")) u_PC (
    .D(NEXT_PC), .en(not_1_out), .Q(PC), .clk(CLK), .clr(RST));
  Hex_Digit_Display hex_digit_display_2 (.value(LedData[27:24]));  // open: dp
  Hex_Digit_Display hex_digit_display_3 (.value(LedData[23:20]));  // open: dp
  Comparator #(.width(16), .mode("twosComplement")) comparator_3 (
    .a(16'h258), .b(\总周期数 ), .eq(comparator_3_eq));  // open: gt, lt
  or or_1 (or_1_out, comparator_3_eq, comparator_4_eq);
  Comparator #(.width(16), .mode("twosComplement")) comparator_4 (
    .a(\总周期数 ), .b(16'h1), .eq(comparator_4_eq));  // open: gt, lt
  Comparator #(.width(16), .mode("twosComplement")) comparator_5 (
    .a(\总周期数 ), .b(16'h4), .eq(comparator_5_eq));  // open: gt, lt
  or or_2 (or_2_out, comparator_1_eq, comparator_2_eq);
  Hex_Digit_Display hex_digit_display_4 (.value(LedData[19:16]));  // open: dp
  Hex_Digit_Display hex_digit_display_5 (.value(LedData[15:12]));  // open: dp
  Pull_Resistor #(.pull(0)) pull_resistor_1 (.node(pull_resistor_1_node));
  assign pull_resistor_1_node = or_1_out ? ~CLK : 1'bz;  // Controlled_Inverter controlled_inverter_1
  Pull_Resistor #(.pull(0)) pull_resistor_2 (.node(pull_resistor_2_node));
  assign pull_resistor_2_node = comparator_5_eq ? ~CLK : 1'bz;  // Controlled_Inverter controlled_inverter_2
  Pull_Resistor #(.pull(0)) pull_resistor_3 (.node(pull_resistor_3_node));
  assign pull_resistor_3_node = or_2_out ? ~CLK : 1'bz;  // Controlled_Inverter controlled_inverter_3
  Hex_Digit_Display hex_digit_display_6 (.value(LedData[11:8]));  // open: dp
  Hex_Digit_Display hex_digit_display_7 (.value(LedData[7:4]));  // open: dp
  // Probe on \总周期数 
  // RiscV_Probe riscv_probe_1: pin names not known; wires that end beside it: IR
  ROM #(.addrWidth(10), .dataWidth(32), .Select("high")) rom_1 (.addr(PC[11:2]), .data(IR));
  Hex_Digit_Display hex_digit_display_8 (.value(LedData[3:0]));  // open: dp
  Register #(.width(1), .trigger("rising"), .Select("low")) register_1 (
    .D(INTR), .Q(register_1_q), .clk(CLK));  // open: en, clr
  \单周期硬布线控制器  \u_单周期硬布线控制器_1  (
    .Funct({IR[30], IR[25], IR[14:12]}), .OP(IR[6:2]), .ALU_OP(\单周期硬布线控制器_1_alu_op ), .MemToReg(M2Reg),
    .MemWrite(MemWrite), .ALU_SRC(\单周期硬布线控制器_1_alu_src ), .RegWrite(RegWrite), .ecall(ecall),
    .S_type(\单周期硬布线控制器_1_s_type ), .Jalr(JALR), .Beq(BEQ), .JAL(JAL), .Bne(BNE), .in_3(IR[21]), .uret(URET),
    .BLT(BLT), .LB(LB), .CSRRSI(CSRRSI), .CSRRCI(CSRRCI));
  Multiplexer #(.select(1), .width(5), .disabled("Z"), .enable("false")) multiplexer_1 (
    .in0(IR[19:15]), .in1(5'b01010), .out(multiplexer_1_out), .sel(ecall));
  Multiplexer #(.select(1), .width(12), .disabled("Z"), .enable("false")) multiplexer_2 (
    .in0(IR[31:20]), .in1({IR[31:25], IR[11:7]}), .out(multiplexer_2_out), .sel(\单周期硬布线控制器_1_s_type ));
  or or_3 (IR1_t, IR1, IRA);
  or or_4 (or_4_out, CSRRCI, register_1_q);
  or or_5 (or_5_out, URET, CSRRSI);
  not not_2 (not_2_out, or_5_out);
  Multiplexer #(.select(1), .width(5), .disabled("Z"), .enable("false")) multiplexer_3 (
    .in0(IR[24:20]), .in1(5'b10001), .out(multiplexer_3_out), .sel(ecall));
  assign bit_extender_1_out = {{20{IR[31]}}, {IR[31], IR[7], IR[30:25], IR[11:8]}};  // Bit_Extender bit_extender_1
  assign bit_extender_2_out = {{12{IR[31]}}, {IR[31], IR[19:12], IR[20], IR[30:21]}};  // Bit_Extender bit_extender_2
  not not_3 (not_3_out, ALU_EQU);
  and and_1 (and_1_out, ALU_LESS, BLT);
  or or_6 (IR2_t, IR2, IRB);
  not not_4 (IE, register_2_q);
  Register #(.width(1), .trigger("rising"), .Select("low")) register_2 (
    .D(1'b0), .Q(register_2_q), .clk(not_2_out), .preset(or_4_out));  // open: en, clr, cs
  Regifile regifile_1 (
    .Din(RDin), .Clk(CLK), .R1(R1), .R2(MDin), .WE(RegWrite), .W_num(IR[11:7]), .R1_num(multiplexer_1_out),
    .R2_num(multiplexer_3_out));
  assign bit_extender_3_out = {{20{multiplexer_2_out[11]}}, multiplexer_2_out};  // Bit_Extender bit_extender_3
  Shifter #(.width(32), .shift("ll")) shifter_1 (.in(bit_extender_1_out), .\dist (5'b00001), .out(shifter_1_out));
  Shifter #(.width(32), .shift("ll")) shifter_2 (.in(bit_extender_2_out), .\dist (5'b00001), .out(shifter_2_out));
  and and_2 (and_2_out, BNE, not_3_out);
  and and_3 (and_3_out, ALU_EQU, BEQ);
  Multiplexer #(.select(1), .width(32), .disabled("Z"), .enable("false")) multiplexer_4 (
    .in0(MDin), .in1(bit_extender_3_out), .out(multiplexer_4_out), .sel(\单周期硬布线控制器_1_alu_src ));
  or or_7 (IR3_t, IR3, IRC);
  ALU alu_1 (
    .X(R1), .Y(multiplexer_4_out), .AluOP(\单周期硬布线控制器_1_alu_op ), .Equal(ALU_EQU),
    .Result({alu_1_result_3, alu_1_result_2, alu_1_result}), .out_6(ALU_LESS));  // open: Result_2, out_4
  Adder #(.width(32)) adder_1 (.a(32'h4), .b(PC), .out(PC_4));  // open: cin, cout
  Adder #(.width(32)) adder_2 (.a(shifter_1_out), .b(PC), .out(adder_2_out));  // open: cin, cout
  Adder #(.width(32)) adder_3 (.a(shifter_2_out), .b(PC), .out(adder_3_out));  // open: cin, cout
  Priority_Encoder #(.select(3), .disabled("Z")) priority_encoder_1 (
    .in0(1'b1), .in1(and_2_out), .in2(and_3_out), .in3(JAL), .in4(JALR), .in5(and_1_out), .out(PC_SRC));  // open: in6, in7, gs, en_out, en_in
  assign and_4_out = {alu_1_result_3, alu_1_result_2, alu_1_result} & 32'hfffffffe;  // AND_Gate and_4, 32 bits wide
  Multiplexer #(.select(2), .width(32), .disabled("Z"), .enable("false")) multiplexer_5 (
    .in1(32'h30ac), .in2(32'h3158), .in3(32'h3204), .out(INTR_PC), .sel(priority_encoder_2_out));  // open: in0
  Priority_Encoder #(.select(2), .disabled("Z")) priority_encoder_2 (
    .in0(1'b1), .in1(INTRA), .in2(INTRB), .in3(INTRC), .out(priority_encoder_2_out));  // open: gs, en_out, en_in
  Multiplexer #(.select(3), .width(32), .disabled("Z"), .enable("false")) multiplexer_6 (
    .in0(PC_4), .in1(adder_2_out), .in2(adder_2_out), .in3(adder_3_out), .in4(and_4_out), .in5(adder_2_out),
    .out(IR_PC), .sel(PC_SRC));  // open: in6, in7
  Comparator #(.width(32), .mode("twosComplement")) comparator_6 (
    .a(MDin), .b(32'h22), .eq(comparator_6_eq));  // open: gt, lt
  RAM #(.addrWidth(10), .dataWidth(32), .bus("separate"), .Select("high")) ram_1 (
    .addr(alu_1_result_2), .din(MDin), .data(ram_1_data), .str(MemWrite), .clk(CLK));  // open: sel, ld, clr
  Comparator #(.width(2), .mode("unsigned")) comparator_7 (
    .a(priority_encoder_2_out), .b(CUR_INT), .gt(comparator_7_gt));  // open: eq, lt
  Multiplexer #(.select(2), .width(8), .disabled("Z"), .enable("false")) multiplexer_7 (
    .in0(ram_1_data[7:0]), .in1(ram_1_data[15:8]), .in2(ram_1_data[23:16]), .in3(ram_1_data[31:24]),
    .out(multiplexer_7_out), .sel(alu_1_result));
  and and_5 (INTR, comparator_7_gt, IE);
  Register #(.width(32), .trigger("rising"), .Select("low")) register_3 (
    .D(R1), .en(and_6_out), .Q(LedData), .clk(CLK), .clr(RST));
  and and_6 (and_6_out, ecall, comparator_6_eq);
  assign bit_extender_4_out = {{24{multiplexer_7_out[7]}}, multiplexer_7_out};  // Bit_Extender bit_extender_4
  D_Flip_Flop #(.trigger("high"), .Pre_Clr_Positions("LEGACY"), .NegatePresetClear("false"), .enable("true"), .NewFFLayout("false")) d_ff_1 (.Q(d_ff_1_q));  // open: clk, D, Qn, preset, en, reset
  // Probe on 13'hc
  Multiplexer #(.select(1), .width(32), .disabled("Z"), .enable("false")) multiplexer_8 (
    .in0(ram_1_data), .in1(bit_extender_4_out), .out(multiplexer_8_out), .sel(LB));
  Priority_Encoder #(.select(2), .disabled("Z")) priority_encoder_3 (
    .in0(1'b1), .in1(INTR), .in2(URET), .in3(1'b0), .out(priority_encoder_3_out));  // open: gs, en_out, en_in
  Comparator #(.width(13), .mode("twosComplement")) comparator_8 (
    .a(CNT_num), .b(13'hc), .eq(comparator_8_eq), .lt(comparator_8_lt));  // open: gt
  Clock #(.highDuration(1), .lowDuration(1)) clock_1 (.out(clock_1_out));
  or or_8 (or_8_out, INTR, URET);
  Multiplexer #(.select(1), .width(2), .disabled("Z"), .enable("false")) multiplexer_9 (
    .in0(priority_encoder_2_out), .in1(register_6_q), .out(multiplexer_9_out), .sel(URET));
  Multiplexer #(.select(1), .width(32), .disabled("Z"), .enable("false")) multiplexer_10 (
    .in0(IR_PC), .in1(register_7_q), .out(multiplexer_10_out), .sel(URET));
  not not_5 (not_5_out, comparator_6_eq);
  Multiplexer #(.select(2), .width(32), .disabled("Z"), .enable("false")) multiplexer_11 (
    .in0(IR_PC), .in1(INTR_PC), .in2(EPC), .out(NEXT_PC), .sel(priority_encoder_3_out));  // open: in3
  Counter #(.width(13), .max('h1fff), .ongoal("stay"), .trigger("rising"), .behavior("old")) counter_1 (
    .count(comparator_8_lt), .Q(CNT_num), .clk(clock_1_out));  // open: load, D, carry, clr, preset
  Register #(.width(2), .trigger("rising"), .Select("low")) register_4 (
    .D(multiplexer_9_out), .en(or_8_out), .Q(CUR_INT), .clk(CLK));  // open: clr
  Register #(.width(32), .trigger("rising"), .Select("low")) register_5 (
    .D(multiplexer_10_out), .en(or_8_out), .Q(EPC), .clk(CLK));  // open: clr
  Multiplexer #(.select(1), .width(32), .disabled("Z"), .enable("false")) multiplexer_12 (
    .in0({alu_1_result_3, alu_1_result_2, alu_1_result}), .in1(multiplexer_8_out), .out(multiplexer_12_out),
    .sel(M2Reg));
  nand nand_1 (nand_1_out, d_ff_1_q, comparator_8_eq);
  Multiplexer #(.select(1), .width(2), .disabled("Z"), .enable("false")) multiplexer_13 (
    .in0(CUR_INT), .in1(register_9_q), .out(multiplexer_13_out), .sel(URET));
  Multiplexer #(.select(1), .width(32), .disabled("Z"), .enable("false")) multiplexer_14 (
    .in0(EPC), .in1(register_10_q), .out(multiplexer_14_out), .sel(URET));
  and and_7 (and_7_out, ecall, not_5_out);
  or or_9 (or_9_out, JAL, JALR);
  Multiplexer #(.select(1), .width(32), .disabled("Z"), .enable("false")) multiplexer_15 (
    .in0(multiplexer_12_out), .in1(PC_4), .out(RDin), .sel(or_9_out));
  assign CLK = nand_1_out ? clock_1_out : 1'bz;  // Controlled_Buffer controlled_buffer_1
  Pull_Resistor #(.pull(1)) pull_resistor_4 (.node(CLK));
  Register #(.width(2), .trigger("rising"), .Select("low")) register_6 (
    .D(multiplexer_13_out), .en(or_8_out), .Q(register_6_q), .clk(CLK));  // open: clr
  Register #(.width(32), .trigger("rising"), .Select("low")) register_7 (
    .D(multiplexer_14_out), .en(or_8_out), .Q(register_7_q), .clk(CLK));  // open: clr
  Register #(.width(1), .trigger("falling"), .Select("low")) register_8 (
    .D(and_7_out), .en(not_6_out), .Q(halt), .clk(CLK), .clr(Go));
  not not_6 (not_6_out, halt);
  Multiplexer #(.select(1), .width(2), .disabled("Z"), .enable("false")) multiplexer_16 (
    .in0(register_6_q), .in1(2'b00), .out(multiplexer_16_out), .sel(URET));
  Multiplexer #(.select(1), .width(32), .disabled("Z"), .enable("false")) multiplexer_17 (
    .in0(register_7_q), .in1({32{1'b0}}), .out(multiplexer_17_out), .sel(URET));
  Counter #(.width(16), .max('hffff), .ongoal("wrap"), .trigger("rising"), .behavior("new")) counter_2 (
    .count(not_6_out), .Q(\总周期数 ), .clk(CLK), .clr(RST));  // open: load, D, carry, preset, down
  Register #(.width(2), .trigger("rising"), .Select("low")) register_9 (
    .D(multiplexer_16_out), .en(or_8_out), .Q(register_9_q), .clk(CLK));  // open: clr
  Register #(.width(32), .trigger("rising"), .Select("low")) register_10 (
    .D(multiplexer_17_out), .en(or_8_out), .Q(register_10_q), .clk(CLK));  // open: clr
  Demultiplexer #(.select(2), .width(1), .tristate("false"), .disabled("Z"), .enable("false")) demultiplexer_1 (
    .out1(CLRA), .out2(CLRB), .out3(CLRC), .in(URET), .sel(CUR_INT));  // open: out0
  Register #(.width(1), .trigger("rising"), .Select("low")) register_11 (
    .D(1'b1), .Q(register_11_q), .clk(IRA), .clr(INTRA));  // open: en
  or or_10 (W1, INTRA, register_11_q);
  Register #(.width(1), .trigger("rising"), .Select("low")) register_12 (
    .D(1'b1), .Q(register_12_q), .clk(IRB), .clr(INTRB));  // open: en
  or or_11 (W2, INTRB, register_12_q);
  Register #(.width(1), .trigger("rising"), .Select("low")) register_13 (
    .D(1'b1), .Q(register_13_q), .clk(IRC), .clr(INTRC));  // open: en
  or or_12 (W3, INTRC, register_13_q);
  and and_8 (and_8_out, or_13_out, ~CLRA);  // AND_Gate
  or or_13 (or_13_out, register_11_q, INTRA);
  and and_9 (and_9_out, or_14_out, ~CLRB);  // AND_Gate
  or or_14 (or_14_out, register_12_q, INTRB);
  and and_10 (and_10_out, or_15_out, ~CLRC);  // AND_Gate
  or or_15 (or_15_out, register_13_q, INTRC);
  Register #(.width(1), .trigger("rising"), .Select("low")) register_14 (
    .D(and_8_out), .Q(INTRA), .clk(CLK));  // open: en, clr
  Register #(.width(1), .trigger("rising"), .Select("low")) register_15 (
    .D(and_9_out), .Q(INTRB), .clk(CLK));  // open: en, clr
  Register #(.width(1), .trigger("rising"), .Select("low")) register_16 (
    .D(and_10_out), .Q(INTRC), .clk(CLK));  // open: en, clr

  // Other names for the same wires on the sheet: R2[31:0] = MDin

  // Notes on the sheet:
  //   中断源
  //   中断等待指示
  //   总复位信号应将除ROM以外所有存储组件全部清零
  //   多级中断测试信号模拟器
  //   数码管输出
  //   指令探针
  //   指令存储器
  //   数码管输出应该用寄存器锁存，否则显示数据只能一闪而过
  //   JALR
  //   指令字
  //   contents of rom_1 (hex, n*v repeats v):
  //   7d000113 100413 1f41993 41f9d993 433 c00913 800b13 140413 f47413 800293 100313 499993 89e9b3 1300533
  //   2200893 73 406282b3 fe0294e3 140413 f00f93 1f47433 1c41413 800293 100313 49d993 89e9b3 1300533
  //   2200893 73 406282b3 fe0294e3 1c45413 406b0b33 b0463 f95ff06f 2b3 fff2c293 1029293 fff2e293 500533
  //   2200893 73 f5dff06f 1112023 410113 a12023 410113 812023 410113 1312023 410113 1412023 410113 1512023
  //   410113 1612023 410113 40e073 100b13 300a13 100a93 1600433 441413 14469b3 1300533 2200893 73 fe0416e3
  //   415a0a33 fe0a10e3 40f073 ffc10113 12b03 ffc10113 12a83 ffc10113 12a03 ffc10113 12983 ffc10113 12403
  //   ffc10113 12503 ffc10113 12883 200073 1112023 410113 a12023 410113 812023 410113 1312023 410113
  //   1412023 410113 1512023 410113 1612023 410113 40e073 200b13 300a13 100a93 1600433 441413 14469b3
  //   1300533 2200893 73 fe0416e3 415a0a33 fe0a10e3 40f073 ffc10113 12b03 ffc10113 12a83 ffc10113 12a03
  //   ffc10113 12983 ffc10113 12403 ffc10113 12503 ffc10113 12883 200073 1112023 410113 a12023 410113
  //   812023 410113 1312023 410113 1412023 410113 1512023 410113 1612023 410113 40e073 300b13 300a13
  //   100a93 1600433 441413 14469b3 1300533 2200893 73 fe0416e3 415a0a33 fe0a10e3 40f073 ffc10113 12b03
  //   ffc10113 12a83 ffc10113 12a03 ffc10113 12983 ffc10113 12403 ffc10113 12503 ffc10113 12883 200073
  //   有险象,延迟一拍
  //   JAL
  //   URET
  //   R1
  //   a0
  //   R2
  //   a7
  //   I 指令
  //   S 指令
  //   B 指令
  //   J 指令
  //   中断响应
  //   Beq
  //   Bne
  //   MemToReg
  //   MemWrite
  //   AluOP
  //   AluSrcB
  //   RegWrite
  //   中断识别
  //   数据存储器
  //   为方便自动评测，需要输出PC，IR，寄存器堆写如数据RDin
  //   RAM写使能MemWrite、RAM写入数据MDin等信号
  //   控制位
  //   暂停节拍，不能为0
  //   戳工具置1进入计数暂停模式，ctrl+k时钟自动运行到对应节拍暂停
  //   ctrl+k关闭时钟连续运行，将控制位置零，进入单步调试模式调试
  //   中断排队
  //   需要锁存中断号
  //   可计数暂停的时钟源
  //   中断清除
endmodule

module \封装正确性测试  (
);

  wire IR1, IR2, IR3, MemW, RegW;
  wire [31:0] EX_PC, ID_PC, IF_PC, IR, LED, MDin, MDinr, MEM_PC, PC, RDin, RDinr, WB_PC;

  \单周期RISC_V  \u_单周期risc_v_1  (
    .IR1(IR1), .IR2(IR2), .IR3(IR3), .RegWrite(RegW), .MemWrite(MemW), .PC(PC), .IR(IR), .RDin(RDin),
    .MDin(MDin), .LedData(LED));
  \气泡流水线  \u_气泡流水线_1  (
    .RegWrite(RegW), .MemWrite(MemW), .IF_PC(IF_PC), .ID_PC(ID_PC), .EX_PC(EX_PC), .M_PC(MEM_PC),
    .WB_PC(WB_PC), .RDin(RDinr), .MDin(MDinr), .LedData(LED));
  \单周期_单级中断  \u_单周期_单级中断_1  (
    .IR1(IR1), .IR2(IR2), .IR3(IR3), .RegWrite(RegW), .MemWrite(MemW), .PC(PC), .IR(IR), .RDin(RDin),
    .MDin(MDin), .LedData(LED));
  \理想流水线  \u_理想流水线_1  (
    .RegWrite(RegW), .MemWrite(MemW), .IF_PC(IF_PC), .ID_PC(ID_PC), .EX_PC(EX_PC), .M_PC(MEM_PC),
    .WB_PC(WB_PC), .RDin(RDinr), .MDin(MDinr), .LedData(LED));
  \重定向流水线  \u_重定向流水线_1  (
    .RegWrite(RegW), .MemWrite(MemW), .IF_PC(IF_PC), .ID_PC(ID_PC), .EX_PC(EX_PC), .M_PC(MEM_PC),
    .WB_PC(WB_PC), .RDin(RDinr), .MDin(MDinr), .LedData(LED));
  \单周期_多级中断  \u_单周期_多级中断_1  (
    .IR1(IR1), .IR2(IR2), .IR3(IR3), .RegWrite(RegW), .MemWrite(MemW), .PC(PC), .IR(IR), .RDin(RDin),
    .MDin(MDin), .LedData(LED));

  // Notes on the sheet:
  //   单周期封装测试
  //   气泡流水封装测试
  //   单周期+单级中断封装测试
  //   请检查上面封装有无位宽不匹配，引脚标签是否和连接的标签相对应，否则无法在educoder平台上正确测试
  //   理想流水封装测试
  //   重定向流水封装测试
  //   单周期+多级中断封装测试
endmodule

module IF_ID (
  input  RESET,
  input  [31:0] IR,
  input  [31:0] PC,
  input  PREDICT_JUMP,
  input  bubble,
  input  EN,
  input  CLK,
  output [31:0] IRout,
  output [31:0] PCout,
  output PREDICT_JUMPout
);

  wire multiplexer_3_out, not_1_out;
  wire [31:0] multiplexer_1_out, multiplexer_2_out;

  Multiplexer #(.select(1), .width(32), .disabled("Z"), .enable("false")) multiplexer_1 (
    .in0(IR), .in1({32{1'b0}}), .out(multiplexer_1_out), .sel(bubble));
  Multiplexer #(.select(1), .width(32), .disabled("Z"), .enable("false")) multiplexer_2 (
    .in0(PC), .in1({32{1'b0}}), .out(multiplexer_2_out), .sel(bubble));
  Multiplexer #(.select(1), .width(1), .disabled("Z"), .enable("false")) multiplexer_3 (
    .in0(PREDICT_JUMP), .in1(1'b0), .out(multiplexer_3_out), .sel(bubble));
  not not_1 (not_1_out, EN);
  Register #(.width(32), .trigger("rising"), .Select("low")) register_1 (
    .D(multiplexer_1_out), .en(not_1_out), .Q(IRout), .clk(CLK), .clr(RESET));
  Register #(.width(32), .trigger("rising"), .Select("low")) register_2 (
    .D(multiplexer_2_out), .en(not_1_out), .Q(PCout), .clk(CLK), .clr(RESET));
  Register #(.width(1), .trigger("rising"), .Select("low")) register_3 (
    .D(multiplexer_3_out), .en(not_1_out), .Q(PREDICT_JUMPout), .clk(CLK), .clr(RESET));
endmodule

module ID_EX (
  input  RESET,
  input  JAL,
  input  BLT,
  input  JALR,
  input  LB,
  input  URET,
  input  BEQ,
  input  BNE,
  input  MemToReg,
  input  MemWrite,
  input  [3:0] AluOP,
  input  AluSrcB,
  input  RegWrite,
  input  ecall,
  input  PREDICT_JUMP,
  input  [1:0] R1_Forword,
  input  [1:0] R2_Forword,
  input  [31:0] R1,
  input  [31:0] R2,
  input  [31:0] Imm,
  input  [31:0] ImmB,
  input  [31:0] ImmJ,
  input  [4:0] WriteDest_num,
  input  [31:0] IR,
  input  [31:0] PC,
  input  bubble,
  input  EN,
  input  CLK,
  output JALout,
  output BLTout,
  output JALRout,
  output LBout,
  output URETout,
  output BEQout,
  output BNEout,
  output MemToRegout,
  output MemWriteout,
  output [3:0] AluOPout,
  output AluSrcBout,
  output RegWriteout,
  output ecallout,
  output PREDICT_JUMPout,
  output [1:0] R1_Forwordout,
  output [1:0] R2_Forwordout,
  output [31:0] R1out,
  output [31:0] R2out,
  output [31:0] Immout,
  output [31:0] ImmBout,
  output [31:0] ImmJout,
  output [4:0] WriteDest_out,
  output [31:0] IRout,
  output [31:0] PCout
);

  wire multiplexer_1_out, multiplexer_2_out, multiplexer_3_out, multiplexer_4_out, multiplexer_5_out,
       multiplexer_6_out, multiplexer_7_out, multiplexer_8_out, multiplexer_9_out, multiplexer_11_out,
       multiplexer_12_out, multiplexer_13_out, multiplexer_14_out, not_1_out;
  wire [1:0] multiplexer_15_out, multiplexer_16_out;
  wire [3:0] multiplexer_10_out;
  wire [4:0] multiplexer_22_out;
  wire [31:0] multiplexer_17_out, multiplexer_18_out, multiplexer_19_out, multiplexer_20_out,
       multiplexer_21_out, multiplexer_23_out, multiplexer_24_out;

  Multiplexer #(.select(1), .width(1), .disabled("Z"), .enable("false")) multiplexer_1 (
    .in0(JAL), .in1(1'b0), .out(multiplexer_1_out), .sel(bubble));
  Multiplexer #(.select(1), .width(1), .disabled("Z"), .enable("false")) multiplexer_2 (
    .in0(BLT), .in1(1'b0), .out(multiplexer_2_out), .sel(bubble));
  Multiplexer #(.select(1), .width(1), .disabled("Z"), .enable("false")) multiplexer_3 (
    .in0(JALR), .in1(1'b0), .out(multiplexer_3_out), .sel(bubble));
  Multiplexer #(.select(1), .width(1), .disabled("Z"), .enable("false")) multiplexer_4 (
    .in0(LB), .in1(1'b0), .out(multiplexer_4_out), .sel(bubble));
  Multiplexer #(.select(1), .width(1), .disabled("Z"), .enable("false")) multiplexer_5 (
    .in0(URET), .in1(1'b0), .out(multiplexer_5_out), .sel(bubble));
  Multiplexer #(.select(1), .width(1), .disabled("Z"), .enable("false")) multiplexer_6 (
    .in0(BEQ), .in1(1'b0), .out(multiplexer_6_out), .sel(bubble));
  Multiplexer #(.select(1), .width(1), .disabled("Z"), .enable("false")) multiplexer_7 (
    .in0(BNE), .in1(1'b0), .out(multiplexer_7_out), .sel(bubble));
  Multiplexer #(.select(1), .width(1), .disabled("Z"), .enable("false")) multiplexer_8 (
    .in0(MemToReg), .in1(1'b0), .out(multiplexer_8_out), .sel(bubble));
  Multiplexer #(.select(1), .width(1), .disabled("Z"), .enable("false")) multiplexer_9 (
    .in0(MemWrite), .in1(1'b0), .out(multiplexer_9_out), .sel(bubble));
  Multiplexer #(.select(1), .width(4), .disabled("Z"), .enable("false")) multiplexer_10 (
    .in0(AluOP), .in1(4'b0000), .out(multiplexer_10_out), .sel(bubble));
  Multiplexer #(.select(1), .width(1), .disabled("Z"), .enable("false")) multiplexer_11 (
    .in0(AluSrcB), .in1(1'b0), .out(multiplexer_11_out), .sel(bubble));
  Multiplexer #(.select(1), .width(1), .disabled("Z"), .enable("false")) multiplexer_12 (
    .in0(RegWrite), .in1(1'b0), .out(multiplexer_12_out), .sel(bubble));
  Multiplexer #(.select(1), .width(1), .disabled("Z"), .enable("false")) multiplexer_13 (
    .in0(ecall), .in1(1'b0), .out(multiplexer_13_out), .sel(bubble));
  Multiplexer #(.select(1), .width(1), .disabled("Z"), .enable("false")) multiplexer_14 (
    .in0(PREDICT_JUMP), .in1(1'b0), .out(multiplexer_14_out), .sel(bubble));
  Multiplexer #(.select(1), .width(2), .disabled("Z"), .enable("false")) multiplexer_15 (
    .in0(R1_Forword), .in1(2'b00), .out(multiplexer_15_out), .sel(bubble));
  Multiplexer #(.select(1), .width(2), .disabled("Z"), .enable("false")) multiplexer_16 (
    .in0(R2_Forword), .in1(2'b00), .out(multiplexer_16_out), .sel(bubble));
  Multiplexer #(.select(1), .width(32), .disabled("Z"), .enable("false")) multiplexer_17 (
    .in0(R1), .in1({32{1'b0}}), .out(multiplexer_17_out), .sel(bubble));
  Multiplexer #(.select(1), .width(32), .disabled("Z"), .enable("false")) multiplexer_18 (
    .in0(R2), .in1({32{1'b0}}), .out(multiplexer_18_out), .sel(bubble));
  Multiplexer #(.select(1), .width(32), .disabled("Z"), .enable("false")) multiplexer_19 (
    .in0(Imm), .in1({32{1'b0}}), .out(multiplexer_19_out), .sel(bubble));
  Multiplexer #(.select(1), .width(32), .disabled("Z"), .enable("false")) multiplexer_20 (
    .in0(ImmB), .in1({32{1'b0}}), .out(multiplexer_20_out), .sel(bubble));
  Multiplexer #(.select(1), .width(32), .disabled("Z"), .enable("false")) multiplexer_21 (
    .in0(ImmJ), .in1({32{1'b0}}), .out(multiplexer_21_out), .sel(bubble));
  Multiplexer #(.select(1), .width(5), .disabled("Z"), .enable("false")) multiplexer_22 (
    .in0(WriteDest_num), .in1({5{1'b0}}), .out(multiplexer_22_out), .sel(bubble));
  Multiplexer #(.select(1), .width(32), .disabled("Z"), .enable("false")) multiplexer_23 (
    .in0(IR), .in1({32{1'b0}}), .out(multiplexer_23_out), .sel(bubble));
  Multiplexer #(.select(1), .width(32), .disabled("Z"), .enable("false")) multiplexer_24 (
    .in0(PC), .in1({32{1'b0}}), .out(multiplexer_24_out), .sel(bubble));
  not not_1 (not_1_out, EN);
  Register #(.width(1), .trigger("rising"), .Select("low")) register_1 (
    .D(multiplexer_1_out), .en(not_1_out), .Q(JALout), .clk(CLK), .clr(RESET));
  Register #(.width(1), .trigger("rising"), .Select("low")) register_2 (
    .D(multiplexer_2_out), .en(not_1_out), .Q(BLTout), .clk(CLK), .clr(RESET));
  Register #(.width(1), .trigger("rising"), .Select("low")) register_3 (
    .D(multiplexer_3_out), .en(not_1_out), .Q(JALRout), .clk(CLK), .clr(RESET));
  Register #(.width(1), .trigger("rising"), .Select("low")) register_4 (
    .D(multiplexer_4_out), .en(not_1_out), .Q(LBout), .clk(CLK), .clr(RESET));
  Register #(.width(1), .trigger("rising"), .Select("low")) register_5 (
    .D(multiplexer_5_out), .en(not_1_out), .Q(URETout), .clk(CLK), .clr(RESET));
  Register #(.width(1), .trigger("rising"), .Select("low")) register_6 (
    .D(multiplexer_6_out), .en(not_1_out), .Q(BEQout), .clk(CLK), .clr(RESET));
  Register #(.width(1), .trigger("rising"), .Select("low")) register_7 (
    .D(multiplexer_7_out), .en(not_1_out), .Q(BNEout), .clk(CLK), .clr(RESET));
  Register #(.width(1), .trigger("rising"), .Select("low")) register_8 (
    .D(multiplexer_8_out), .en(not_1_out), .Q(MemToRegout), .clk(CLK), .clr(RESET));
  Register #(.width(1), .trigger("rising"), .Select("low")) register_9 (
    .D(multiplexer_9_out), .en(not_1_out), .Q(MemWriteout), .clk(CLK), .clr(RESET));
  Register #(.width(4), .trigger("rising"), .Select("low")) register_10 (
    .D(multiplexer_10_out), .en(not_1_out), .Q(AluOPout), .clk(CLK), .clr(RESET));
  Register #(.width(1), .trigger("rising"), .Select("low")) register_11 (
    .D(multiplexer_11_out), .en(not_1_out), .Q(AluSrcBout), .clk(CLK), .clr(RESET));
  Register #(.width(1), .trigger("rising"), .Select("low")) register_12 (
    .D(multiplexer_12_out), .en(not_1_out), .Q(RegWriteout), .clk(CLK), .clr(RESET));
  Register #(.width(1), .trigger("rising"), .Select("low")) register_13 (
    .D(multiplexer_13_out), .en(not_1_out), .Q(ecallout), .clk(CLK), .clr(RESET));
  Register #(.width(1), .trigger("rising"), .Select("low")) register_14 (
    .D(multiplexer_14_out), .en(not_1_out), .Q(PREDICT_JUMPout), .clk(CLK), .clr(RESET));
  Register #(.width(2), .trigger("rising"), .Select("low")) register_15 (
    .D(multiplexer_15_out), .en(not_1_out), .Q(R1_Forwordout), .clk(CLK), .clr(RESET));
  Register #(.width(2), .trigger("rising"), .Select("low")) register_16 (
    .D(multiplexer_16_out), .en(not_1_out), .Q(R2_Forwordout), .clk(CLK), .clr(RESET));
  Register #(.width(32), .trigger("rising"), .Select("low")) register_17 (
    .D(multiplexer_17_out), .en(not_1_out), .Q(R1out), .clk(CLK), .clr(RESET));
  Register #(.width(32), .trigger("rising"), .Select("low")) register_18 (
    .D(multiplexer_18_out), .en(not_1_out), .Q(R2out), .clk(CLK), .clr(RESET));
  Register #(.width(32), .trigger("rising"), .Select("low")) register_19 (
    .D(multiplexer_19_out), .en(not_1_out), .Q(Immout), .clk(CLK), .clr(RESET));
  Register #(.width(32), .trigger("rising"), .Select("low")) register_20 (
    .D(multiplexer_20_out), .en(not_1_out), .Q(ImmBout), .clk(CLK), .clr(RESET));
  Register #(.width(32), .trigger("rising"), .Select("low")) register_21 (
    .D(multiplexer_21_out), .en(not_1_out), .Q(ImmJout), .clk(CLK), .clr(RESET));
  Register #(.width(5), .trigger("rising"), .Select("low")) register_22 (
    .D(multiplexer_22_out), .en(not_1_out), .Q(WriteDest_out), .clk(CLK), .clr(RESET));
  Register #(.width(32), .trigger("rising"), .Select("low")) register_23 (
    .D(multiplexer_23_out), .en(not_1_out), .Q(IRout), .clk(CLK), .clr(RESET));
  Register #(.width(32), .trigger("rising"), .Select("low")) register_24 (
    .D(multiplexer_24_out), .en(not_1_out), .Q(PCout), .clk(CLK), .clr(RESET));
endmodule

module EX_MEM (
  input  RESET,
  input  JAL,
  input  BLT,
  input  JALR,
  input  LB,
  input  MemToReg,
  input  MemWrite,
  input  RegWrite,
  input  halt,
  input  [31:0] ALUResult,
  input  [31:0] R2,
  input  [4:0] RegWriteDest,
  input  [31:0] IR,
  input  [31:0] PC,
  input  bubble,
  input  EN,
  input  CLK,
  output JALout,
  output BLTout,
  output JALRout,
  output LBout,
  output MemToRegout,
  output MemWriteout,
  output RegWriteout,
  output haltout,
  output [31:0] ALUResultout,
  output [31:0] R2out,
  output [4:0] RegWriteDestout,
  output [31:0] IRout,
  output [31:0] PCout
);

  wire multiplexer_1_out, multiplexer_2_out, multiplexer_3_out, multiplexer_4_out, multiplexer_5_out,
       multiplexer_6_out, multiplexer_7_out, multiplexer_8_out, not_1_out;
  wire [4:0] multiplexer_11_out;
  wire [31:0] multiplexer_9_out, multiplexer_10_out, multiplexer_12_out, multiplexer_13_out;

  Multiplexer #(.select(1), .width(1), .disabled("Z"), .enable("false")) multiplexer_1 (
    .in0(JAL), .in1(1'b0), .out(multiplexer_1_out), .sel(bubble));
  Multiplexer #(.select(1), .width(1), .disabled("Z"), .enable("false")) multiplexer_2 (
    .in0(BLT), .in1(1'b0), .out(multiplexer_2_out), .sel(bubble));
  Multiplexer #(.select(1), .width(1), .disabled("Z"), .enable("false")) multiplexer_3 (
    .in0(JALR), .in1(1'b0), .out(multiplexer_3_out), .sel(bubble));
  Multiplexer #(.select(1), .width(1), .disabled("Z"), .enable("false")) multiplexer_4 (
    .in0(LB), .in1(1'b0), .out(multiplexer_4_out), .sel(bubble));
  Multiplexer #(.select(1), .width(1), .disabled("Z"), .enable("false")) multiplexer_5 (
    .in0(MemToReg), .in1(1'b0), .out(multiplexer_5_out), .sel(bubble));
  Multiplexer #(.select(1), .width(1), .disabled("Z"), .enable("false")) multiplexer_6 (
    .in0(MemWrite), .in1(1'b0), .out(multiplexer_6_out), .sel(bubble));
  Multiplexer #(.select(1), .width(1), .disabled("Z"), .enable("false")) multiplexer_7 (
    .in0(RegWrite), .in1(1'b0), .out(multiplexer_7_out), .sel(bubble));
  Multiplexer #(.select(1), .width(1), .disabled("Z"), .enable("false")) multiplexer_8 (
    .in0(halt), .in1(1'b0), .out(multiplexer_8_out), .sel(bubble));
  Multiplexer #(.select(1), .width(32), .disabled("Z"), .enable("false")) multiplexer_9 (
    .in0(ALUResult), .in1({32{1'b0}}), .out(multiplexer_9_out), .sel(bubble));
  Multiplexer #(.select(1), .width(32), .disabled("Z"), .enable("false")) multiplexer_10 (
    .in0(R2), .in1({32{1'b0}}), .out(multiplexer_10_out), .sel(bubble));
  Multiplexer #(.select(1), .width(5), .disabled("Z"), .enable("false")) multiplexer_11 (
    .in0(RegWriteDest), .in1({5{1'b0}}), .out(multiplexer_11_out), .sel(bubble));
  Multiplexer #(.select(1), .width(32), .disabled("Z"), .enable("false")) multiplexer_12 (
    .in0(IR), .in1({32{1'b0}}), .out(multiplexer_12_out), .sel(bubble));
  Multiplexer #(.select(1), .width(32), .disabled("Z"), .enable("false")) multiplexer_13 (
    .in0(PC), .in1({32{1'b0}}), .out(multiplexer_13_out), .sel(bubble));
  not not_1 (not_1_out, EN);
  Register #(.width(1), .trigger("rising"), .Select("low")) register_1 (
    .D(multiplexer_1_out), .en(not_1_out), .Q(JALout), .clk(CLK), .clr(RESET));
  Register #(.width(1), .trigger("rising"), .Select("low")) register_2 (
    .D(multiplexer_2_out), .en(not_1_out), .Q(BLTout), .clk(CLK), .clr(RESET));
  Register #(.width(1), .trigger("rising"), .Select("low")) register_3 (
    .D(multiplexer_3_out), .en(not_1_out), .Q(JALRout), .clk(CLK), .clr(RESET));
  Register #(.width(1), .trigger("rising"), .Select("low")) register_4 (
    .D(multiplexer_4_out), .en(not_1_out), .Q(LBout), .clk(CLK), .clr(RESET));
  Register #(.width(1), .trigger("rising"), .Select("low")) register_5 (
    .D(multiplexer_5_out), .en(not_1_out), .Q(MemToRegout), .clk(CLK), .clr(RESET));
  Register #(.width(1), .trigger("rising"), .Select("low")) register_6 (
    .D(multiplexer_6_out), .en(not_1_out), .Q(MemWriteout), .clk(CLK), .clr(RESET));
  Register #(.width(1), .trigger("rising"), .Select("low")) register_7 (
    .D(multiplexer_7_out), .en(not_1_out), .Q(RegWriteout), .clk(CLK), .clr(RESET));
  Register #(.width(1), .trigger("rising"), .Select("low")) register_8 (
    .D(multiplexer_8_out), .en(not_1_out), .Q(haltout), .clk(CLK), .clr(RESET));
  Register #(.width(32), .trigger("rising"), .Select("low")) register_9 (
    .D(multiplexer_9_out), .en(not_1_out), .Q(ALUResultout), .clk(CLK), .clr(RESET));
  Register #(.width(32), .trigger("rising"), .Select("low")) register_10 (
    .D(multiplexer_10_out), .en(not_1_out), .Q(R2out), .clk(CLK), .clr(RESET));
  Register #(.width(5), .trigger("rising"), .Select("low")) register_11 (
    .D(multiplexer_11_out), .en(not_1_out), .Q(RegWriteDestout), .clk(CLK), .clr(RESET));
  Register #(.width(32), .trigger("rising"), .Select("low")) register_12 (
    .D(multiplexer_12_out), .en(not_1_out), .Q(IRout), .clk(CLK), .clr(RESET));
  Register #(.width(32), .trigger("rising"), .Select("low")) register_13 (
    .D(multiplexer_13_out), .en(not_1_out), .Q(PCout), .clk(CLK), .clr(RESET));
endmodule

module MEM_WB (
  input  RESET,
  input  JAL,
  input  BLT,
  input  JALR,
  input  LB,
  input  MemToReg,
  input  RegWrite,
  input  halt,
  input  [1:0] ALUResultHigh,
  input  [31:0] ALUResult,
  input  [4:0] RegWriteDest,
  input  [31:0] MemData,
  input  [31:0] IR,
  input  [31:0] PC,
  input  bubble,
  input  EN,
  input  CLK,
  output JALout,
  output BLTout,
  output JALRout,
  output LBout,
  output MemToRegout,
  output RegWriteout,
  output haltout,
  output [1:0] ALUResultHighout,
  output [31:0] ALUResultout,
  output [4:0] RegWriteDestout,
  output [31:0] MemDataout,
  output [31:0] IRout,
  output [31:0] PCout
);

  wire multiplexer_1_out, multiplexer_2_out, multiplexer_3_out, multiplexer_4_out, multiplexer_5_out,
       multiplexer_6_out, multiplexer_7_out, not_1_out;
  wire [1:0] multiplexer_8_out;
  wire [4:0] multiplexer_10_out;
  wire [31:0] multiplexer_9_out, multiplexer_11_out, multiplexer_12_out, multiplexer_13_out;

  Multiplexer #(.select(1), .width(1), .disabled("Z"), .enable("false")) multiplexer_1 (
    .in0(JAL), .in1(1'b0), .out(multiplexer_1_out), .sel(bubble));
  Multiplexer #(.select(1), .width(1), .disabled("Z"), .enable("false")) multiplexer_2 (
    .in0(BLT), .in1(1'b0), .out(multiplexer_2_out), .sel(bubble));
  Multiplexer #(.select(1), .width(1), .disabled("Z"), .enable("false")) multiplexer_3 (
    .in0(JALR), .in1(1'b0), .out(multiplexer_3_out), .sel(bubble));
  Multiplexer #(.select(1), .width(1), .disabled("Z"), .enable("false")) multiplexer_4 (
    .in0(LB), .in1(1'b0), .out(multiplexer_4_out), .sel(bubble));
  Multiplexer #(.select(1), .width(1), .disabled("Z"), .enable("false")) multiplexer_5 (
    .in0(MemToReg), .in1(1'b0), .out(multiplexer_5_out), .sel(bubble));
  Multiplexer #(.select(1), .width(1), .disabled("Z"), .enable("false")) multiplexer_6 (
    .in0(RegWrite), .in1(1'b0), .out(multiplexer_6_out), .sel(bubble));
  Multiplexer #(.select(1), .width(1), .disabled("Z"), .enable("false")) multiplexer_7 (
    .in0(halt), .in1(1'b0), .out(multiplexer_7_out), .sel(bubble));
  Multiplexer #(.select(1), .width(2), .disabled("Z"), .enable("false")) multiplexer_8 (
    .in0(ALUResultHigh), .in1(2'b00), .out(multiplexer_8_out), .sel(bubble));
  Multiplexer #(.select(1), .width(32), .disabled("Z"), .enable("false")) multiplexer_9 (
    .in0(ALUResult), .in1({32{1'b0}}), .out(multiplexer_9_out), .sel(bubble));
  Multiplexer #(.select(1), .width(5), .disabled("Z"), .enable("false")) multiplexer_10 (
    .in0(RegWriteDest), .in1({5{1'b0}}), .out(multiplexer_10_out), .sel(bubble));
  Multiplexer #(.select(1), .width(32), .disabled("Z"), .enable("false")) multiplexer_11 (
    .in0(MemData), .in1({32{1'b0}}), .out(multiplexer_11_out), .sel(bubble));
  Multiplexer #(.select(1), .width(32), .disabled("Z"), .enable("false")) multiplexer_12 (
    .in0(IR), .in1({32{1'b0}}), .out(multiplexer_12_out), .sel(bubble));
  Multiplexer #(.select(1), .width(32), .disabled("Z"), .enable("false")) multiplexer_13 (
    .in0(PC), .in1({32{1'b0}}), .out(multiplexer_13_out), .sel(bubble));
  not not_1 (not_1_out, EN);
  Register #(.width(1), .trigger("rising"), .Select("low")) register_1 (
    .D(multiplexer_1_out), .en(not_1_out), .Q(JALout), .clk(CLK), .clr(RESET));
  Register #(.width(1), .trigger("rising"), .Select("low")) register_2 (
    .D(multiplexer_2_out), .en(not_1_out), .Q(BLTout), .clk(CLK), .clr(RESET));
  Register #(.width(1), .trigger("rising"), .Select("low")) register_3 (
    .D(multiplexer_3_out), .en(not_1_out), .Q(JALRout), .clk(CLK), .clr(RESET));
  Register #(.width(1), .trigger("rising"), .Select("low")) register_4 (
    .D(multiplexer_4_out), .en(not_1_out), .Q(LBout), .clk(CLK), .clr(RESET));
  Register #(.width(1), .trigger("rising"), .Select("low")) register_5 (
    .D(multiplexer_5_out), .en(not_1_out), .Q(MemToRegout), .clk(CLK), .clr(RESET));
  Register #(.width(1), .trigger("rising"), .Select("low")) register_6 (
    .D(multiplexer_6_out), .en(not_1_out), .Q(RegWriteout), .clk(CLK), .clr(RESET));
  Register #(.width(1), .trigger("rising"), .Select("low")) register_7 (
    .D(multiplexer_7_out), .en(not_1_out), .Q(haltout), .clk(CLK), .clr(RESET));
  Register #(.width(2), .trigger("rising"), .Select("low")) register_8 (
    .D(multiplexer_8_out), .en(not_1_out), .Q(ALUResultHighout), .clk(CLK), .clr(RESET));
  Register #(.width(32), .trigger("rising"), .Select("low")) register_9 (
    .D(multiplexer_9_out), .en(not_1_out), .Q(ALUResultout), .clk(CLK), .clr(RESET));
  Register #(.width(5), .trigger("rising"), .Select("low")) register_10 (
    .D(multiplexer_10_out), .en(not_1_out), .Q(RegWriteDestout), .clk(CLK), .clr(RESET));
  Register #(.width(32), .trigger("rising"), .Select("low")) register_11 (
    .D(multiplexer_11_out), .en(not_1_out), .Q(MemDataout), .clk(CLK), .clr(RESET));
  Register #(.width(32), .trigger("rising"), .Select("low")) register_12 (
    .D(multiplexer_12_out), .en(not_1_out), .Q(IRout), .clk(CLK), .clr(RESET));
  Register #(.width(32), .trigger("rising"), .Select("low")) register_13 (
    .D(multiplexer_13_out), .en(not_1_out), .Q(PCout), .clk(CLK), .clr(RESET));
endmodule

module \源寄存器使用情况  (
  input  OP2,
  input  OP3,
  input  OP4,
  input  OP5,
  input  OP6,
  input  F12,
  input  F13,
  input  F14,
  input  F25,
  input  F30,
  output R1_USED,
  output R2_USED
);

  wire and_1_out, and_2_out, and_3_out, and_4_out, and_5_out, and_6_out, and_7_out, and_8_out, and_9_out,
       and_10_out, and_11_out, and_12_out, and_13_out, and_14_out, and_15_out, and_16_out, and_17_out,
       and_18_out, and_19_out, and_20_out, and_21_out, and_22_out, and_23_out, and_24_out, and_25_out,
       and_26_out, and_27_out, and_28_out, and_29_out, and_30_out, and_31_out, and_32_out, and_33_out,
       and_34_out, and_35_out, and_36_out, and_37_out, not_1_out, not_2_out, not_3_out, not_4_out, not_5_out,
       not_6_out, not_7_out, not_8_out, not_9_out, not_10_out, not_11_out, not_12_out, not_13_out,
       not_14_out, not_15_out, not_16_out, not_17_out, not_18_out, not_19_out, not_20_out, not_21_out,
       not_22_out, not_23_out, not_24_out, not_25_out, not_26_out, not_27_out, not_28_out, not_29_out,
       not_30_out, not_31_out, not_32_out, not_33_out, not_34_out, not_35_out, not_36_out, not_37_out,
       not_38_out, not_39_out, not_40_out, not_41_out, not_42_out, not_43_out, not_44_out, not_45_out,
       not_46_out, not_47_out, not_48_out, not_49_out, not_50_out, not_51_out, not_52_out, not_53_out,
       not_54_out, not_55_out, not_56_out, not_57_out, not_58_out, not_59_out, not_60_out, not_61_out,
       not_62_out, not_63_out, not_64_out, not_65_out, not_66_out, not_67_out, not_68_out, not_69_out,
       not_70_out, not_71_out, not_72_out, not_73_out, not_74_out, not_75_out, not_76_out, not_77_out,
       not_78_out, not_79_out, not_80_out, not_81_out, not_82_out, not_83_out, not_84_out, not_85_out,
       not_86_out, not_87_out, not_88_out, not_89_out, not_90_out, not_91_out, not_92_out, not_93_out,
       not_94_out, not_95_out, not_96_out, not_97_out, not_98_out, not_99_out, not_100_out, not_101_out,
       not_102_out, not_103_out, not_104_out, not_105_out, not_106_out, not_107_out, not_108_out,
       not_109_out, not_110_out, not_111_out, not_112_out, not_113_out, not_114_out, not_115_out,
       not_116_out, not_117_out, not_118_out, not_119_out, not_120_out, not_121_out, not_122_out,
       not_123_out, not_124_out, not_125_out, not_126_out, not_127_out, not_128_out, not_129_out,
       not_130_out, not_131_out, not_132_out, not_133_out, not_134_out, not_135_out, not_136_out,
       not_137_out, not_138_out, not_139_out, not_140_out, not_141_out, not_142_out, not_143_out,
       not_144_out, not_145_out, not_146_out, not_147_out, not_148_out, not_149_out, not_150_out,
       not_151_out, not_152_out, not_153_out, not_154_out, not_155_out, not_156_out, not_157_out,
       not_158_out, not_159_out, not_160_out, not_161_out, not_162_out, not_163_out, not_164_out,
       not_165_out, not_166_out, not_167_out, not_168_out, not_169_out, not_170_out, not_171_out,
       not_172_out, not_173_out, not_174_out, not_175_out, not_176_out, not_177_out, not_178_out,
       not_179_out, not_180_out, not_181_out, not_182_out, not_183_out, not_184_out, not_185_out,
       not_186_out, not_187_out, not_188_out, not_189_out, not_190_out, not_191_out, not_192_out,
       not_193_out, not_194_out, not_195_out, not_196_out, not_197_out, not_198_out, not_199_out,
       not_200_out, not_201_out, not_202_out, not_203_out, not_204_out, not_205_out, not_206_out,
       not_207_out, not_208_out, not_209_out, not_210_out, not_211_out, not_212_out, not_213_out,
       not_214_out, not_215_out, not_216_out, not_217_out, not_218_out, not_219_out, not_220_out,
       not_221_out, not_222_out, not_223_out, not_224_out, not_225_out, not_226_out, not_227_out,
       not_228_out, not_229_out;

  not not_1 (not_1_out, F30);
  not not_2 (not_2_out, F25);
  not not_3 (not_3_out, F14);
  not not_4 (not_4_out, F13);
  not not_5 (not_5_out, F12);
  not not_6 (not_6_out, OP6);
  not not_7 (not_7_out, OP3);
  not not_8 (not_8_out, OP2);
  not not_9 (not_9_out, F25);
  not not_10 (not_10_out, F14);
  not not_11 (not_11_out, F13);
  not not_12 (not_12_out, F12);
  not not_13 (not_13_out, OP6);
  not not_14 (not_14_out, OP3);
  not not_15 (not_15_out, OP2);
  not not_16 (not_16_out, F30);
  not not_17 (not_17_out, F25);
  not not_18 (not_18_out, OP6);
  not not_19 (not_19_out, OP3);
  not not_20 (not_20_out, OP2);
  not not_21 (not_21_out, F30);
  not not_22 (not_22_out, F25);
  not not_23 (not_23_out, F12);
  not not_24 (not_24_out, OP6);
  not not_25 (not_25_out, OP3);
  not not_26 (not_26_out, OP2);
  not not_27 (not_27_out, F30);
  not not_28 (not_28_out, F25);
  not not_29 (not_29_out, F14);
  not not_30 (not_30_out, F12);
  not not_31 (not_31_out, OP6);
  not not_32 (not_32_out, OP3);
  not not_33 (not_33_out, OP2);
  not not_34 (not_34_out, F30);
  not not_35 (not_35_out, F25);
  not not_36 (not_36_out, F14);
  not not_37 (not_37_out, OP6);
  not not_38 (not_38_out, OP3);
  not not_39 (not_39_out, OP2);
  not not_40 (not_40_out, F14);
  not not_41 (not_41_out, F13);
  not not_42 (not_42_out, F12);
  not not_43 (not_43_out, OP6);
  not not_44 (not_44_out, OP5);
  not not_45 (not_45_out, OP3);
  not not_46 (not_46_out, OP2);
  not not_47 (not_47_out, OP6);
  not not_48 (not_48_out, OP5);
  not not_49 (not_49_out, OP3);
  not not_50 (not_50_out, OP2);
  not not_51 (not_51_out, F12);
  not not_52 (not_52_out, OP6);
  not not_53 (not_53_out, OP5);
  not not_54 (not_54_out, OP3);
  not not_55 (not_55_out, OP2);
  not not_56 (not_56_out, F13);
  not not_57 (not_57_out, F12);
  not not_58 (not_58_out, OP6);
  not not_59 (not_59_out, OP5);
  not not_60 (not_60_out, OP3);
  not not_61 (not_61_out, OP2);
  not not_62 (not_62_out, F14);
  not not_63 (not_63_out, F12);
  not not_64 (not_64_out, OP6);
  not not_65 (not_65_out, OP5);
  not not_66 (not_66_out, OP3);
  not not_67 (not_67_out, OP2);
  not not_68 (not_68_out, F30);
  not not_69 (not_69_out, F25);
  not not_70 (not_70_out, F14);
  not not_71 (not_71_out, F13);
  not not_72 (not_72_out, OP6);
  not not_73 (not_73_out, OP5);
  not not_74 (not_74_out, OP3);
  not not_75 (not_75_out, OP2);
  not not_76 (not_76_out, F30);
  not not_77 (not_77_out, F25);
  not not_78 (not_78_out, F13);
  not not_79 (not_79_out, OP6);
  not not_80 (not_80_out, OP5);
  not not_81 (not_81_out, OP3);
  not not_82 (not_82_out, OP2);
  not not_83 (not_83_out, F25);
  not not_84 (not_84_out, F13);
  not not_85 (not_85_out, OP6);
  not not_86 (not_86_out, OP5);
  not not_87 (not_87_out, OP3);
  not not_88 (not_88_out, OP2);
  not not_89 (not_89_out, F14);
  not not_90 (not_90_out, F12);
  not not_91 (not_91_out, OP6);
  not not_92 (not_92_out, OP5);
  not not_93 (not_93_out, OP4);
  not not_94 (not_94_out, OP3);
  not not_95 (not_95_out, OP2);
  not not_96 (not_96_out, F14);
  not not_97 (not_97_out, F12);
  not not_98 (not_98_out, OP6);
  not not_99 (not_99_out, OP4);
  not not_100 (not_100_out, OP3);
  not not_101 (not_101_out, OP2);
  not not_102 (not_102_out, F30);
  not not_103 (not_103_out, F25);
  not not_104 (not_104_out, F14);
  not not_105 (not_105_out, F13);
  not not_106 (not_106_out, F12);
  not not_107 (not_107_out, OP3);
  not not_108 (not_108_out, OP2);
  not not_109 (not_109_out, F14);
  not not_110 (not_110_out, F13);
  not not_111 (not_111_out, F12);
  not not_112 (not_112_out, OP4);
  not not_113 (not_113_out, OP3);
  not not_114 (not_114_out, OP2);
  not not_115 (not_115_out, F14);
  not not_116 (not_116_out, F13);
  not not_117 (not_117_out, OP4);
  not not_118 (not_118_out, OP3);
  not not_119 (not_119_out, OP2);
  not not_120 (not_120_out, F14);
  not not_121 (not_121_out, F13);
  not not_122 (not_122_out, F12);
  not not_123 (not_123_out, OP4);
  not not_124 (not_124_out, OP3);
  not not_125 (not_125_out, F25);
  not not_126 (not_126_out, F13);
  not not_127 (not_127_out, OP6);
  not not_128 (not_128_out, OP3);
  not not_129 (not_129_out, OP2);
  not not_130 (not_130_out, F30);
  not not_131 (not_131_out, F25);
  not not_132 (not_132_out, F13);
  not not_133 (not_133_out, F12);
  not not_134 (not_134_out, OP6);
  not not_135 (not_135_out, OP3);
  not not_136 (not_136_out, OP2);
  not not_137 (not_137_out, F14);
  not not_138 (not_138_out, F13);
  not not_139 (not_139_out, F12);
  not not_140 (not_140_out, OP6);
  not not_141 (not_141_out, OP5);
  not not_142 (not_142_out, OP4);
  not not_143 (not_143_out, OP3);
  not not_144 (not_144_out, OP2);
  not not_145 (not_145_out, F13);
  not not_146 (not_146_out, F12);
  not not_147 (not_147_out, OP4);
  not not_148 (not_148_out, OP3);
  not not_149 (not_149_out, OP2);
  not not_150 (not_150_out, F30);
  not not_151 (not_151_out, F25);
  not not_152 (not_152_out, F14);
  not not_153 (not_153_out, F13);
  not not_154 (not_154_out, F12);
  not not_155 (not_155_out, OP6);
  not not_156 (not_156_out, OP3);
  not not_157 (not_157_out, OP2);
  not not_158 (not_158_out, F25);
  not not_159 (not_159_out, F14);
  not not_160 (not_160_out, F13);
  not not_161 (not_161_out, F12);
  not not_162 (not_162_out, OP6);
  not not_163 (not_163_out, OP3);
  not not_164 (not_164_out, OP2);
  not not_165 (not_165_out, F30);
  not not_166 (not_166_out, F25);
  not not_167 (not_167_out, OP6);
  not not_168 (not_168_out, OP3);
  not not_169 (not_169_out, OP2);
  not not_170 (not_170_out, F30);
  not not_171 (not_171_out, F25);
  not not_172 (not_172_out, F12);
  not not_173 (not_173_out, OP6);
  not not_174 (not_174_out, OP3);
  not not_175 (not_175_out, OP2);
  not not_176 (not_176_out, F30);
  not not_177 (not_177_out, F25);
  not not_178 (not_178_out, F14);
  not not_179 (not_179_out, F12);
  not not_180 (not_180_out, OP6);
  not not_181 (not_181_out, OP3);
  not not_182 (not_182_out, OP2);
  not not_183 (not_183_out, F30);
  not not_184 (not_184_out, F25);
  not not_185 (not_185_out, F14);
  not not_186 (not_186_out, OP6);
  not not_187 (not_187_out, OP3);
  not not_188 (not_188_out, OP2);
  not not_189 (not_189_out, F14);
  not not_190 (not_190_out, F12);
  not not_191 (not_191_out, OP6);
  not not_192 (not_192_out, OP4);
  not not_193 (not_193_out, OP3);
  not not_194 (not_194_out, OP2);
  not not_195 (not_195_out, F30);
  not not_196 (not_196_out, F25);
  not not_197 (not_197_out, F14);
  not not_198 (not_198_out, F13);
  not not_199 (not_199_out, F12);
  not not_200 (not_200_out, OP3);
  not not_201 (not_201_out, OP2);
  not not_202 (not_202_out, F14);
  not not_203 (not_203_out, F13);
  not not_204 (not_204_out, F12);
  not not_205 (not_205_out, OP4);
  not not_206 (not_206_out, OP3);
  not not_207 (not_207_out, OP2);
  not not_208 (not_208_out, F14);
  not not_209 (not_209_out, F13);
  not not_210 (not_210_out, OP4);
  not not_211 (not_211_out, OP3);
  not not_212 (not_212_out, OP2);
  not not_213 (not_213_out, F25);
  not not_214 (not_214_out, F13);
  not not_215 (not_215_out, OP6);
  not not_216 (not_216_out, OP3);
  not not_217 (not_217_out, OP2);
  not not_218 (not_218_out, F30);
  not not_219 (not_219_out, F25);
  not not_220 (not_220_out, F13);
  not not_221 (not_221_out, F12);
  not not_222 (not_222_out, OP6);
  not not_223 (not_223_out, OP3);
  not not_224 (not_224_out, OP2);
  not not_225 (not_225_out, F13);
  not not_226 (not_226_out, F12);
  not not_227 (not_227_out, OP4);
  not not_228 (not_228_out, OP3);
  not not_229 (not_229_out, OP2);
  and and_1 (and_1_out, not_1_out, not_2_out, not_3_out, not_4_out, not_5_out, not_6_out, OP5, OP4, not_7_out, not_8_out);
  and and_2 (and_2_out, F30, not_9_out, not_10_out, not_11_out, not_12_out, not_13_out, OP5, OP4, not_14_out, not_15_out);
  and and_3 (and_3_out, not_16_out, not_17_out, F14, F13, F12, not_18_out, OP5, OP4, not_19_out, not_20_out);
  and and_4 (and_4_out, not_21_out, not_22_out, F14, F13, not_23_out, not_24_out, OP5, OP4, not_25_out, not_26_out);
  and and_5 (and_5_out, not_27_out, not_28_out, not_29_out, F13, not_30_out, not_31_out, OP5, OP4, not_32_out, not_33_out);
  and and_6 (and_6_out, not_34_out, not_35_out, not_36_out, F13, F12, not_37_out, OP5, OP4, not_38_out, not_39_out);
  and and_7 (and_7_out, not_40_out, not_41_out, not_42_out, not_43_out, not_44_out, OP4, not_45_out, not_46_out);
  and and_8 (and_8_out, F14, F13, F12, not_47_out, not_48_out, OP4, not_49_out, not_50_out);
  and and_9 (and_9_out, F14, F13, not_51_out, not_52_out, not_53_out, OP4, not_54_out, not_55_out);
  and and_10 (and_10_out, F14, not_56_out, not_57_out, not_58_out, not_59_out, OP4, not_60_out, not_61_out);
  and and_11 (and_11_out, not_62_out, F13, not_63_out, not_64_out, not_65_out, OP4, not_66_out, not_67_out);
  and and_12 (and_12_out, not_68_out, not_69_out, not_70_out, not_71_out, F12, not_72_out, not_73_out, OP4, not_74_out, not_75_out);
  and and_13 (and_13_out, not_76_out, not_77_out, F14, not_78_out, F12, not_79_out, not_80_out, OP4, not_81_out, not_82_out);
  and and_14 (and_14_out, F30, not_83_out, F14, not_84_out, F12, not_85_out, not_86_out, OP4, not_87_out, not_88_out);
  and and_15 (and_15_out, not_89_out, F13, not_90_out, not_91_out, not_92_out, not_93_out, not_94_out, not_95_out);
  and and_16 (and_16_out, not_96_out, F13, not_97_out, not_98_out, OP5, not_99_out, not_100_out, not_101_out);
  and and_17 (and_17_out, not_102_out, not_103_out, not_104_out, not_105_out, not_106_out, OP6, OP5, OP4, not_107_out, not_108_out);
  and and_18 (and_18_out, not_109_out, not_110_out, not_111_out, OP6, OP5, not_112_out, not_113_out, not_114_out);
  and and_19 (and_19_out, not_115_out, not_116_out, F12, OP6, OP5, not_117_out, not_118_out, not_119_out);
  and and_20 (and_20_out, not_120_out, not_121_out, not_122_out, OP6, OP5, not_123_out, not_124_out, OP2);
  and and_21 (and_21_out, F30, not_125_out, F14, not_126_out, F12, not_127_out, OP5, OP4, not_128_out, not_129_out);
  and and_22 (and_22_out, not_130_out, not_131_out, F14, not_132_out, not_133_out, not_134_out, OP5, OP4, not_135_out, not_136_out);
  and and_23 (and_23_out, not_137_out, not_138_out, not_139_out, not_140_out, not_141_out, not_142_out, not_143_out, not_144_out);
  and and_24 (and_24_out, F14, not_145_out, not_146_out, OP6, OP5, not_147_out, not_148_out, not_149_out);
  and and_25 (and_25_out, not_150_out, not_151_out, not_152_out, not_153_out, not_154_out, not_155_out, OP5, OP4, not_156_out, not_157_out);
  and and_26 (and_26_out, F30, not_158_out, not_159_out, not_160_out, not_161_out, not_162_out, OP5, OP4, not_163_out, not_164_out);
  and and_27 (and_27_out, not_165_out, not_166_out, F14, F13, F12, not_167_out, OP5, OP4, not_168_out, not_169_out);
  and and_28 (and_28_out, not_170_out, not_171_out, F14, F13, not_172_out, not_173_out, OP5, OP4, not_174_out, not_175_out);
  and and_29 (and_29_out, not_176_out, not_177_out, not_178_out, F13, not_179_out, not_180_out, OP5, OP4, not_181_out, not_182_out);
  and and_30 (and_30_out, not_183_out, not_184_out, not_185_out, F13, F12, not_186_out, OP5, OP4, not_187_out, not_188_out);
  and and_31 (and_31_out, not_189_out, F13, not_190_out, not_191_out, OP5, not_192_out, not_193_out, not_194_out);
  and and_32 (and_32_out, not_195_out, not_196_out, not_197_out, not_198_out, not_199_out, OP6, OP5, OP4, not_200_out, not_201_out);
  and and_33 (and_33_out, not_202_out, not_203_out, not_204_out, OP6, OP5, not_205_out, not_206_out, not_207_out);
  and and_34 (and_34_out, not_208_out, not_209_out, F12, OP6, OP5, not_210_out, not_211_out, not_212_out);
  and and_35 (and_35_out, F30, not_213_out, F14, not_214_out, F12, not_215_out, OP5, OP4, not_216_out, not_217_out);
  and and_36 (and_36_out, not_218_out, not_219_out, F14, not_220_out, not_221_out, not_222_out, OP5, OP4, not_223_out, not_224_out);
  and and_37 (and_37_out, F14, not_225_out, not_226_out, OP6, OP5, not_227_out, not_228_out, not_229_out);
  or or_1 (R2_USED, and_25_out, and_26_out, and_27_out, and_28_out, and_29_out, and_30_out, and_31_out, and_32_out, and_33_out, and_34_out, and_35_out, and_36_out, and_37_out);
  or or_2 (R1_USED, and_1_out, and_2_out, and_3_out, and_4_out, and_5_out, and_6_out, and_7_out, and_8_out, and_9_out, and_10_out, and_11_out, and_12_out, and_13_out, and_14_out, and_15_out, and_16_out, and_17_out, and_18_out, and_19_out, and_20_out, and_21_out, and_22_out, and_23_out, and_24_out);
endmodule

module \流水冲突检测器4气泡  (
  input  EX_RegWrite,
  input  MEM_RegWrite,
  input  [4:0] EX_RegWriteDest_num,
  input  [4:0] MEM_RegWriteDest_num,
  input  [31:0] IR,
  input  ecall,
  output stall
);

  wire and_1_out, and_2_out, and_3_out, and_4_out, and_5_out, and_6_out, comparator_1_eq, comparator_2_eq,
       comparator_3_eq, comparator_4_eq, comparator_5_eq, comparator_6_eq, not_1_out, not_2_out, R1_USED,
       R2_USED;
  wire [4:0] multiplexer_1_out, multiplexer_2_out;

  \源寄存器使用情况  \u_源寄存器使用情况_1  (
    .OP2(IR[2]), .OP3(IR[3]), .OP4(IR[4]), .OP5(IR[5]), .OP6(IR[6]), .F12(IR[12]), .F13(IR[13]),
    .F14(IR[14]), .F25(IR[25]), .F30(IR[30]), .R1_USED(R1_USED), .R2_USED(R2_USED));
  Multiplexer #(.select(1), .width(5), .disabled("Z"), .enable("false")) multiplexer_1 (
    .in0(IR[19:15]), .in1(5'b01010), .out(multiplexer_1_out), .sel(ecall));
  Multiplexer #(.select(1), .width(5), .disabled("Z"), .enable("false")) multiplexer_2 (
    .in0(IR[24:20]), .in1(5'b10001), .out(multiplexer_2_out), .sel(ecall));
  Comparator #(.width(5), .mode("twosComplement")) comparator_1 (
    .a(multiplexer_1_out), .b(EX_RegWriteDest_num), .eq(comparator_1_eq));  // open: gt, lt
  Comparator #(.width(5), .mode("twosComplement")) comparator_2 (
    .a(multiplexer_1_out), .b(MEM_RegWriteDest_num), .eq(comparator_2_eq));  // open: gt, lt
  not not_1 (not_1_out, comparator_3_eq);
  Comparator #(.width(5), .mode("twosComplement")) comparator_3 (
    .a(multiplexer_1_out), .b({5{1'b0}}), .eq(comparator_3_eq));  // open: gt, lt
  Comparator #(.width(5), .mode("twosComplement")) comparator_4 (
    .a(multiplexer_2_out), .b(EX_RegWriteDest_num), .eq(comparator_4_eq));  // open: gt, lt
  Comparator #(.width(5), .mode("twosComplement")) comparator_5 (
    .a(multiplexer_2_out), .b(MEM_RegWriteDest_num), .eq(comparator_5_eq));  // open: gt, lt
  Comparator #(.width(5), .mode("twosComplement")) comparator_6 (
    .a(multiplexer_2_out), .b({5{1'b0}}), .eq(comparator_6_eq));  // open: gt, lt
  not not_2 (not_2_out, comparator_6_eq);
  and and_1 (and_1_out, not_1_out, R1_USED);
  and and_2 (and_2_out, not_2_out, R2_USED);
  and and_3 (and_3_out, comparator_1_eq, EX_RegWrite, and_1_out);
  and and_4 (and_4_out, comparator_2_eq, MEM_RegWrite, and_1_out);
  and and_5 (and_5_out, comparator_4_eq, EX_RegWrite, and_2_out);
  and and_6 (and_6_out, comparator_5_eq, MEM_RegWrite, and_2_out);
  or or_1 (stall, and_3_out, and_4_out, and_5_out, and_6_out);
endmodule

module \流水冲突检测器4重定向  (
  input  EX_MEMToReg,
  input  [4:0] MEM_RegWriteDest_num,
  input  [31:0] IR,
  input  ecall,
  input  MEM_RegWrite,
  input  [4:0] EX_RegWriteDest_num,
  input  EX_RegWrite,
  output load_use,
  output [1:0] R1_Forword,
  output [1:0] R2_Forword
);

  wire and_1_out, and_2_out, and_3_out, and_4_out, comparator_1_eq, comparator_2_eq, comparator_3_eq,
       comparator_4_eq, comparator_5_eq, comparator_6_eq, not_1_out, not_2_out, R1_USED, R2_USED;
  wire [4:0] multiplexer_1_out, multiplexer_2_out;

  \源寄存器使用情况  \u_源寄存器使用情况_1  (
    .OP2(IR[2]), .OP3(IR[3]), .OP4(IR[4]), .OP5(IR[5]), .OP6(IR[6]), .F12(IR[12]), .F13(IR[13]),
    .F14(IR[14]), .F25(IR[25]), .F30(IR[30]), .R1_USED(R1_USED), .R2_USED(R2_USED));
  Multiplexer #(.select(1), .width(5), .disabled("Z"), .enable("false")) multiplexer_1 (
    .in0(IR[19:15]), .in1(5'b01010), .out(multiplexer_1_out), .sel(ecall));
  Multiplexer #(.select(1), .width(5), .disabled("Z"), .enable("false")) multiplexer_2 (
    .in0(IR[24:20]), .in1(5'b10001), .out(multiplexer_2_out), .sel(ecall));
  Comparator #(.width(5), .mode("twosComplement")) comparator_1 (
    .a(multiplexer_1_out), .b(EX_RegWriteDest_num), .eq(comparator_1_eq));  // open: gt, lt
  Comparator #(.width(5), .mode("twosComplement")) comparator_2 (
    .a(EX_RegWriteDest_num), .b(multiplexer_2_out), .eq(comparator_2_eq));  // open: gt, lt
  Comparator #(.width(5), .mode("twosComplement")) comparator_3 (
    .a(multiplexer_1_out), .b(MEM_RegWriteDest_num), .eq(comparator_3_eq));  // open: gt, lt
  not not_1 (not_1_out, comparator_4_eq);
  Comparator #(.width(5), .mode("twosComplement")) comparator_4 (
    .a(multiplexer_1_out), .b({5{1'b0}}), .eq(comparator_4_eq));  // open: gt, lt
  Comparator #(.width(5), .mode("twosComplement")) comparator_5 (
    .a(multiplexer_2_out), .b(MEM_RegWriteDest_num), .eq(comparator_5_eq));  // open: gt, lt
  Comparator #(.width(5), .mode("twosComplement")) comparator_6 (
    .a(multiplexer_2_out), .b({5{1'b0}}), .eq(comparator_6_eq));  // open: gt, lt
  not not_2 (not_2_out, comparator_6_eq);
  and and_1 (and_1_out, not_2_out, R2_USED);
  and and_2 (and_2_out, not_1_out, R1_USED);
  and and_3 (and_3_out, comparator_1_eq, EX_MEMToReg, and_2_out);
  and and_4 (and_4_out, comparator_2_eq, EX_MEMToReg, and_1_out);
  and and_5 (R1_Forword[0], and_2_out, comparator_3_eq, MEM_RegWrite);
  and and_6 (R1_Forword[1], and_2_out, comparator_1_eq, EX_RegWrite);
  and and_7 (R2_Forword[0], comparator_5_eq, and_1_out, MEM_RegWrite);
  and and_8 (R2_Forword[1], and_1_out, comparator_2_eq, EX_RegWrite);
  or or_1 (load_use, and_3_out, and_4_out);
endmodule

module \流水线_单级中断  (
  output RegWrite,
  output MemWrite,
  output [31:0] IF_PC,
  output [31:0] ID_PC,
  output [31:0] EX_PC,
  output [31:0] M_PC,
  output [31:0] WB_PC,
  output [31:0] RDin,
  output [31:0] MDin,
  output [31:0] LedData
);

  wire ALU_EQU, ALU_LESS, and_1_out, and_3_out, and_4_out, and_5_out, and_6_out, and_8_out, BEQ, BLT, BNE,
       Branch_Success, CLK, clock_1_out, CLRA, CLRB, CLRC, comparator_1_eq, comparator_2_eq, comparator_3_eq,
       comparator_4_eq, comparator_5_eq, comparator_5_lt, comparator_6_eq, comparator_6_gt, comparator_7_eq,
       controlled_inverter_3_out, d_ff_1_q, ecall, ex_mem_1_bltout, ex_mem_1_haltout, ex_mem_1_jalout,
       ex_mem_1_jalrout, ex_mem_1_lbout, ex_mem_1_memtoregout, EX_MemToReg, EX_RegWrite, Go, halt, haltsign,
       id_ex_1_alusrcbout, id_ex_1_lbout, id_ex_1_memwriteout, IE, InBranch, INTR, INTRA, INTRB, INTRC,
       IR_ecall, IRA, IRB, IRC, JAL, JALR, load_use, MEM_RegWrite, mem_wb_1_jalout, mem_wb_1_jalrout,
       mem_wb_1_lbout, mem_wb_1_memtoregout, nand_1_out, nor_1_out, nor_2_out, nor_3_out, not_1_out,
       not_2_out, not_3_out, not_4_out, not_5_out, not_6_out, not_7_out, not_8_out, not_9_out, or_1_out,
       or_2_out, or_3_out, or_4_out, or_5_out, or_6_out, or_8_out, or_13_out, or_14_out, or_15_out,
       or_16_out, or_17_out, register_3_q, register_4_q, register_5_q, riscv_probe_2_p2, riscv_probe_2_p3,
       RST, URET, W1, W2, W3, \单周期硬布线控制器_1_alu_src , \单周期硬布线控制器_1_beq , \单周期硬布线控制器_1_blt , \单周期硬布线控制器_1_bne ,
       \单周期硬布线控制器_1_jal , \单周期硬布线控制器_1_jalr , \单周期硬布线控制器_1_lb , \单周期硬布线控制器_1_memtoreg ,
       \单周期硬布线控制器_1_memwrite , \单周期硬布线控制器_1_regwrite , \单周期硬布线控制器_1_s_type , \单周期硬布线控制器_1_uret ;
  wire [1:0] EX_R1Forword, EX_R2Forword, MEM_ALUHIGH, mem_wb_1_aluresulthighout, priority_encoder_1_out,
       priority_encoder_3_out, R1_Forword, R2_Forword, register_2_q;
  wire [2:0] PC_SRC;
  wire [3:0] id_ex_1_aluopout, \单周期硬布线控制器_1_alu_op ;
  wire [4:0] EX_RegWriteDest_num, MEM_RegWriteDest_num, multiplexer_3_out, multiplexer_4_out, RegWriteDest;
  wire [7:0] multiplexer_9_out, multiplexer_14_out;
  wire [11:0] multiplexer_5_out;
  wire [12:0] CNT_num;
  wire [15:0] \LoadUse次数 , \总周期数 , \无条件分支数 , \条件分支成功数 ;
  wire [31:0] adder_1_out, adder_2_out, adder_3_out, adder_4_out, adder_5_out, alu_1_result, and_7_out,
       bit_extender_1_out, bit_extender_2_out, bit_extender_3_out, bit_extender_4_out, bit_extender_5_out,
       EPC, EX_IR, EX_R1, EX_R2, id_ex_1_immbout, id_ex_1_immjout, id_ex_1_immout, ID_IR, IF_IR, INTR_PC,
       MEM_DATAOUT, MEM_IR, MEM_ReadData, mem_wb_1_aluresultout, mem_wb_1_memdataout, multiplexer_7_out,
       multiplexer_8_out, multiplexer_10_out, multiplexer_11_out, multiplexer_15_out, multiplexer_16_out,
       NEXT_PC, R1, R2, regifile4bubble_1_r1, regifile4bubble_1_r2, shifter_1_out, shifter_2_out, WB_IR;
  wire [31:2] ex_mem_1_aluresultout;

  Button \u_总复位  (.out(RST));
  Button _1 (.out(IRA));
  Button _2 (.out(IRB));
  Button _3 (.out(IRC));
  // Probe on \总周期数 
  // Probe on \总周期数 
  Button \u_继续运行  (.out(Go));
  LED #(.active("true")) led_1 (.in(W1));
  LED #(.active("true")) led_2 (.in(W2));
  LED #(.active("true")) led_3 (.in(W3));
  or or_1 (or_1_out, Go, not_1_out);
  not not_1 (not_1_out, halt);
  Hex_Digit_Display hex_digit_display_1 (.value(LedData[31:28]));  // open: dp
  // Probe on IF_PC[19:0]
  // RiscV_Probe riscv_probe_1: pin names not known; wires that end beside it: IF_IR
  Comparator #(.width(16), .mode("twosComplement")) comparator_1 (
    .a(16'h23b), .b(\总周期数 ), .eq(comparator_1_eq));  // open: gt, lt
  Comparator #(.width(16), .mode("twosComplement")) comparator_2 (
    .a(\总周期数 ), .b(16'h1), .eq(comparator_2_eq));  // open: gt, lt
  Comparator #(.width(16), .mode("twosComplement")) comparator_3 (
    .a(\总周期数 ), .b(16'h4), .eq(comparator_3_eq));  // open: gt, lt
  Comparator #(.width(16), .mode("twosComplement")) comparator_4 (
    .a(\总周期数 ), .b(16'h7), .eq(comparator_4_eq));  // open: gt, lt
  Counter #(.width(16), .max('hffff), .ongoal("wrap"), .trigger("rising"), .behavior("new")) counter_1 (
    .count(or_1_out), .Q(\总周期数 ), .clk(CLK), .clr(RST));  // open: load, D, carry, preset, down
  and and_1 (and_1_out, or_1_out, not_2_out);
  not not_2 (not_2_out, load_use);
  Hex_Digit_Display hex_digit_display_2 (.value(LedData[27:24]));  // open: dp
  Hex_Digit_Display hex_digit_display_3 (.value(LedData[23:20]));  // open: dp
  // Probe on ID_PC[19:0]
  // RiscV_Probe riscv_probe_2: pin names not known; wires that end beside it: ID_IR, riscv_probe_2_p2, riscv_probe_2_p3, IRA, IRB
  or or_2 (or_2_out, comparator_1_eq, comparator_2_eq);
  assign riscv_probe_2_p2 = or_2_out ? ~CLK : 1'bz;  // Controlled_Inverter controlled_inverter_1
  assign riscv_probe_2_p3 = comparator_3_eq ? ~CLK : 1'bz;  // Controlled_Inverter controlled_inverter_2
  assign controlled_inverter_3_out = comparator_4_eq ? ~CLK : 1'bz;  // Controlled_Inverter controlled_inverter_3
  Register #(.width(32), .trigger("rising"), .Select("low")) PC (
    .D(NEXT_PC), .en(and_1_out), .Q(IF_PC), .clk(CLK), .clr(RST));
  Hex_Digit_Display hex_digit_display_4 (.value(LedData[19:16]));  // open: dp
  Hex_Digit_Display hex_digit_display_5 (.value(LedData[15:12]));  // open: dp
  Pull_Resistor #(.pull(0)) pull_resistor_1 (.node(riscv_probe_2_p2));
  Pull_Resistor #(.pull(0)) pull_resistor_2 (.node(riscv_probe_2_p3));
  Pull_Resistor #(.pull(0)) pull_resistor_3 (.node(controlled_inverter_3_out));
  not not_3 (not_3_out, halt);
  Hex_Digit_Display hex_digit_display_6 (.value(LedData[11:8]));  // open: dp
  Hex_Digit_Display hex_digit_display_7 (.value(LedData[7:4]));  // open: dp
  // Probe on EX_PC[19:0]
  // RiscV_Probe riscv_probe_3: pin names not known; wires that end beside it: EX_IR
  nor nor_1 (nor_1_out, Go, not_3_out);
  Hex_Digit_Display hex_digit_display_8 (.value(LedData[3:0]));  // open: dp
  ROM #(.addrWidth(10), .dataWidth(32), .Select("low")) rom_1 (.addr(IF_PC[11:2]), .data(IF_IR));
  // Probe on \总周期数 
  // Probe on M_PC[19:0]
  // RiscV_Probe riscv_probe_4: pin names not known; wires that end beside it: MEM_IR
  IF_ID if_id_1 (
    .IR(IF_IR), .PC(IF_PC), .IRout(ID_IR), .PCout(ID_PC), .bubble(InBranch), .EN(or_4_out), .CLK(CLK),
    .RESET(RST));  // open: PREDICT_JUMP, PREDICT_JUMPout
  // Probe on \总周期数 
  // Probe on \无条件分支数 
  // Probe on \条件分支成功数 
  // Probe on \LoadUse次数 
  // Probe on \LoadUse次数 
  or or_3 (or_3_out, INTRA, INTRB, INTRC);
  not not_4 (not_4_out, or_3_out);
  Counter #(.width(16), .max('hffff), .ongoal("wrap"), .trigger("rising"), .behavior("new")) counter_2 (
    .count(load_use), .Q(\LoadUse次数 ), .clk(CLK), .clr(RST));  // open: load, D, carry, preset, down
  or or_4 (or_4_out, nor_1_out, load_use);
  // Probe on IF_PC[11:0]
  // Probe on WB_PC[19:0]
  // RiscV_Probe riscv_probe_5: pin names not known; wires that end beside it: WB_IR
  and and_2 (INTR, IE, or_3_out);
  or or_5 (or_5_out, not_4_out, URET);
  \流水冲突检测器4重定向  \u_流水冲突检测器4重定向_1  (
    .EX_RegWrite(EX_RegWrite), .MEM_RegWrite(MEM_RegWrite), .EX_RegWriteDest_num(EX_RegWriteDest_num),
    .MEM_RegWriteDest_num(MEM_RegWriteDest_num), .IR(ID_IR), .ecall(IR_ecall), .load_use(load_use),
    .EX_MEMToReg(EX_MemToReg), .R1_Forword(R1_Forword), .R2_Forword(R2_Forword));
  Multiplexer #(.select(2), .width(32), .disabled("Z"), .enable("false")) multiplexer_1 (
    .in0(EX_R1), .in1(RDin), .in2(MEM_DATAOUT), .in3(MEM_DATAOUT), .out(R1), .sel(EX_R1Forword));
  Multiplexer #(.select(2), .width(32), .disabled("Z"), .enable("false")) multiplexer_2 (
    .in0(EX_R2), .in1(RDin), .in2(MEM_DATAOUT), .in3(MEM_DATAOUT), .out(R2), .sel(EX_R2Forword));
  // Probe on ID_PC[11:0]
  // Probe on EX_PC[11:0]
  Register #(.width(1), .trigger("rising"), .Select("low")) register_1 (
    .D(or_5_out), .Q(IE), .clk(CLK));  // open: en, clr
  \单周期硬布线控制器  \u_单周期硬布线控制器_1  (
    .Funct({ID_IR[30], ID_IR[25], ID_IR[14:12]}), .OP(ID_IR[6:2]), .ALU_OP(\单周期硬布线控制器_1_alu_op ),
    .MemToReg(\单周期硬布线控制器_1_memtoreg ), .MemWrite(\单周期硬布线控制器_1_memwrite ), .ALU_SRC(\单周期硬布线控制器_1_alu_src ),
    .RegWrite(\单周期硬布线控制器_1_regwrite ), .ecall(IR_ecall), .S_type(\单周期硬布线控制器_1_s_type ),
    .Jalr(\单周期硬布线控制器_1_jalr ), .Beq(\单周期硬布线控制器_1_beq ), .JAL(\单周期硬布线控制器_1_jal ), .Bne(\单周期硬布线控制器_1_bne ),
    .in_3(ID_IR[21]), .uret(\单周期硬布线控制器_1_uret ), .BLT(\单周期硬布线控制器_1_blt ), .LB(\单周期硬布线控制器_1_lb ));  // open: CSRRSI, CSRRCI
  Multiplexer #(.select(1), .width(5), .disabled("Z"), .enable("false")) multiplexer_3 (
    .in0(ID_IR[19:15]), .in1(5'b01010), .out(multiplexer_3_out), .sel(IR_ecall));
  Multiplexer #(.select(1), .width(5), .disabled("Z"), .enable("false")) multiplexer_4 (
    .in0(ID_IR[24:20]), .in1(5'b10001), .out(multiplexer_4_out), .sel(IR_ecall));
  Multiplexer #(.select(1), .width(12), .disabled("Z"), .enable("false")) multiplexer_5 (
    .in0(ID_IR[31:20]), .in1({ID_IR[31:25], ID_IR[11:7]}), .out(multiplexer_5_out), .sel(\单周期硬布线控制器_1_s_type ));
  // Probe on M_PC[11:0]
  D_Flip_Flop #(.trigger("high"), .Pre_Clr_Positions("LEGACY"), .NegatePresetClear("false"), .enable("true"), .NewFFLayout("false")) d_ff_1 (.Q(d_ff_1_q));  // open: clk, D, Qn, preset, en, reset
  // Probe on 13'h373
  assign bit_extender_1_out = {{20{multiplexer_5_out[11]}}, multiplexer_5_out};  // Bit_Extender bit_extender_1
  assign bit_extender_2_out = {{20{ID_IR[31]}}, {ID_IR[31], ID_IR[7], ID_IR[30:25], ID_IR[11:8]}};  // Bit_Extender bit_extender_2
  assign bit_extender_3_out = {{12{ID_IR[31]}}, {ID_IR[31], ID_IR[19:12], ID_IR[20], ID_IR[30:21]}};  // Bit_Extender bit_extender_3
  // Probe on WB_PC[11:0]
  Comparator #(.width(13), .mode("twosComplement")) comparator_5 (
    .a(CNT_num), .b(13'h373), .eq(comparator_5_eq), .lt(comparator_5_lt));  // open: gt
  Clock #(.highDuration(1), .lowDuration(1)) clock_1 (.out(clock_1_out));
  nand nand_1 (nand_1_out, d_ff_1_q, comparator_5_eq);
  Counter #(.width(13), .max('h1fff), .ongoal("stay"), .trigger("rising"), .behavior("old")) counter_3 (
    .count(comparator_5_lt), .Q(CNT_num), .clk(clock_1_out));  // open: load, D, carry, clr, preset
  Priority_Encoder #(.select(2), .disabled("Z")) priority_encoder_1 (
    .in0(INTRA), .in1(INTRB), .in2(INTRC), .out(priority_encoder_1_out));  // open: in3, gs, en_out, en_in
  Comparator #(.width(32), .mode("twosComplement")) comparator_6 (
    .a({32{1'b0}}), .b(ID_IR), .gt(comparator_6_gt), .eq(comparator_6_eq));  // open: lt
  Regifile4Bubble regifile4bubble_1 (
    .Din(RDin), .Clk(CLK), .R1(regifile4bubble_1_r1), .R2(regifile4bubble_1_r2), .WE(RegWrite),
    .W_num(RegWriteDest), .R1_num(multiplexer_3_out), .R2_num(multiplexer_4_out));
  not not_5 (not_5_out, halt);
  assign CLK = nand_1_out ? clock_1_out : 1'bz;  // Controlled_Buffer controlled_buffer_1
  Multiplexer #(.select(2), .width(32), .disabled("Z"), .enable("false")) multiplexer_6 (
    .in0(32'h30ac), .in1(32'h3150), .in2(32'h31f4), .out(INTR_PC), .sel(priority_encoder_1_out));  // open: in3
  and and_3 (and_3_out, \单周期硬布线控制器_1_regwrite , not_6_out);
  not not_6 (not_6_out, comparator_6_eq);
  nor nor_2 (nor_2_out, Go, not_5_out);
  Pull_Resistor #(.pull(1)) pull_resistor_4 (.node(CLK));
  ID_EX id_ex_1 (
    .JAL(\单周期硬布线控制器_1_jal ), .BLT(\单周期硬布线控制器_1_blt ), .JALR(\单周期硬布线控制器_1_jalr ), .LB(\单周期硬布线控制器_1_lb ),
    .URET(\单周期硬布线控制器_1_uret ), .BEQ(\单周期硬布线控制器_1_beq ), .BNE(\单周期硬布线控制器_1_bne ),
    .MemToReg(\单周期硬布线控制器_1_memtoreg ), .MemWrite(\单周期硬布线控制器_1_memwrite ), .AluOP(\单周期硬布线控制器_1_alu_op ),
    .AluSrcB(\单周期硬布线控制器_1_alu_src ), .RegWrite(and_3_out), .R1(regifile4bubble_1_r1),
    .R2(regifile4bubble_1_r2), .Imm(bit_extender_1_out), .IR(ID_IR), .PC(ID_PC), .bubble(or_6_out),
    .EN(nor_2_out), .CLK(CLK), .JALout(JAL), .BLTout(BLT), .JALRout(JALR), .LBout(id_ex_1_lbout),
    .URETout(URET), .BEQout(BEQ), .BNEout(BNE), .MemToRegout(EX_MemToReg), .MemWriteout(id_ex_1_memwriteout),
    .AluOPout(id_ex_1_aluopout), .AluSrcBout(id_ex_1_alusrcbout), .RegWriteout(EX_RegWrite), .R1out(EX_R1),
    .R2out(EX_R2), .Immout(id_ex_1_immout), .IRout(EX_IR), .PCout(EX_PC), .RESET(RST), .ecallout(ecall),
    .ecall(IR_ecall), .ImmB(bit_extender_2_out), .ImmJ(bit_extender_3_out), .ImmBout(id_ex_1_immbout),
    .ImmJout(id_ex_1_immjout), .WriteDest_num(ID_IR[11:7]), .WriteDest_out(EX_RegWriteDest_num),
    .R1_Forword(R1_Forword), .R2_Forword(R2_Forword), .R1_Forwordout(EX_R1Forword),
    .R2_Forwordout(EX_R2Forword));  // open: PREDICT_JUMP, PREDICT_JUMPout
  or or_6 (or_6_out, InBranch, load_use);
  not not_7 (not_7_out, ALU_EQU);
  Register #(.width(2), .trigger("rising"), .Select("low")) register_2 (
    .D(priority_encoder_1_out), .en(INTR), .Q(register_2_q), .clk(CLK));  // open: clr
  and and_4 (and_4_out, BNE, not_7_out);
  and and_5 (and_5_out, ALU_EQU, BEQ);
  and and_6 (and_6_out, BLT, ALU_LESS);
  Demultiplexer #(.select(2), .width(1), .tristate("false"), .disabled("Z"), .enable("false")) demultiplexer_1 (
    .out0(CLRA), .out1(CLRB), .out2(CLRC), .in(URET), .sel(register_2_q));  // open: out3
  Multiplexer #(.select(1), .width(32), .disabled("Z"), .enable("false")) multiplexer_7 (
    .in0(R2), .in1(id_ex_1_immout), .out(multiplexer_7_out), .sel(id_ex_1_alusrcbout));
  Shifter #(.width(32), .shift("ll")) shifter_1 (.in(id_ex_1_immbout), .\dist (5'b00001), .out(shifter_1_out));
  Shifter #(.width(32), .shift("ll")) shifter_2 (.in(id_ex_1_immjout), .\dist (5'b00001), .out(shifter_2_out));
  Adder #(.width(32)) adder_1 (.a(shifter_1_out), .b(EX_PC), .out(adder_1_out));  // open: cin, cout
  Adder #(.width(32)) adder_2 (.a(shifter_2_out), .b(EX_PC), .out(adder_2_out));  // open: cin, cout
  Adder #(.width(32)) adder_3 (.a(IF_PC), .b(32'h4), .out(adder_3_out));  // open: cin, cout
  Priority_Encoder #(.select(3), .disabled("Z")) priority_encoder_2 (
    .in0(1'b1), .in1(and_4_out), .in2(and_5_out), .in3(JAL), .in4(JALR), .in5(and_6_out), .out(PC_SRC));  // open: in6, in7, gs, en_out, en_in
  or or_7 (InBranch, INTR, JAL, JALR, Branch_Success, URET);
  or or_8 (or_8_out, JALR, JAL);
  ALU alu_1 (
    .X(R1), .Y(multiplexer_7_out), .AluOP(id_ex_1_aluopout), .Equal(ALU_EQU), .Result(alu_1_result),
    .out_6(ALU_LESS));  // open: Result_2, out_4
  or or_9 (Branch_Success, and_5_out, and_4_out, and_6_out);
  Counter #(.width(16), .max('hffff), .ongoal("wrap"), .trigger("rising"), .behavior("new")) counter_4 (
    .count(or_8_out), .Q(\无条件分支数 ), .clk(CLK), .clr(RST));  // open: load, D, carry, preset, down
  assign and_7_out = alu_1_result & 32'hfffffffe;  // AND_Gate and_7, 32 bits wide
  Register #(.width(1), .trigger("rising"), .Select("low")) register_3 (
    .D(1'b1), .Q(register_3_q), .clk(IRA), .clr(INTRA));  // open: en
  or or_10 (W1, INTRA, register_3_q);
  Register #(.width(1), .trigger("rising"), .Select("low")) register_4 (
    .D(1'b1), .Q(register_4_q), .clk(IRB), .clr(INTRB));  // open: en
  or or_11 (W2, INTRB, register_4_q);
  Register #(.width(1), .trigger("rising"), .Select("low")) register_5 (
    .D(1'b1), .Q(register_5_q), .clk(IRC), .clr(INTRC));  // open: en
  or or_12 (W3, INTRC, register_5_q);
  EX_MEM ex_mem_1 (
    .JAL(JAL), .JALR(JALR), .LB(id_ex_1_lbout), .MemToReg(EX_MemToReg), .MemWrite(id_ex_1_memwriteout),
    .RegWrite(EX_RegWrite), .ALUResult(alu_1_result), .R2(R2), .RegWriteDest(EX_RegWriteDest_num),
    .IR(EX_IR), .PC(EX_PC), .JALout(ex_mem_1_jalout), .JALRout(ex_mem_1_jalrout), .LBout(ex_mem_1_lbout),
    .MemToRegout(ex_mem_1_memtoregout), .MemWriteout(MemWrite), .RegWriteout(MEM_RegWrite),
    .ALUResultout({ex_mem_1_aluresultout, MEM_ALUHIGH}), .R2out(MDin),
    .RegWriteDestout(MEM_RegWriteDest_num), .IRout(MEM_IR), .PCout(M_PC), .RESET(RST), .bubble(1'b0),
    .EN(nor_3_out), .CLK(CLK), .BLT(BLT), .BLTout(ex_mem_1_bltout), .halt(haltsign),
    .haltout(ex_mem_1_haltout));
  Multiplexer #(.select(3), .width(32), .disabled("Z"), .enable("false")) multiplexer_8 (
    .in0(adder_3_out), .in1(adder_1_out), .in2(adder_1_out), .in3(adder_2_out), .in4(and_7_out),
    .in5(adder_1_out), .out(multiplexer_8_out), .sel(PC_SRC));  // open: in6, in7
  Multiplexer #(.select(2), .width(8), .disabled("Z"), .enable("false")) multiplexer_9 (
    .in0(MEM_ReadData[7:0]), .in1(MEM_ReadData[15:8]), .in2(MEM_ReadData[23:16]), .in3(MEM_ReadData[31:24]),
    .out(multiplexer_9_out), .sel(MEM_ALUHIGH));
  or or_13 (or_13_out, register_3_q, INTRA);
  or or_14 (or_14_out, register_4_q, INTRB);
  or or_15 (or_15_out, register_5_q, INTRC);
  assign bit_extender_4_out = {{24{multiplexer_9_out[7]}}, multiplexer_9_out};  // Bit_Extender bit_extender_4
  Register #(.width(1), .trigger("rising"), .Select("low")) register_6 (
    .D(or_13_out), .Q(INTRA), .clk(CLK), .clr(CLRA));  // open: en
  Register #(.width(1), .trigger("rising"), .Select("low")) register_7 (
    .D(or_14_out), .Q(INTRB), .clk(CLK), .clr(CLRB));  // open: en
  Register #(.width(1), .trigger("rising"), .Select("low")) register_8 (
    .D(or_15_out), .Q(INTRC), .clk(CLK), .clr(CLRC));  // open: en
  Counter #(.width(16), .max('hffff), .ongoal("wrap"), .trigger("rising"), .behavior("new")) counter_5 (
    .count(Branch_Success), .Q(\条件分支成功数 ), .clk(CLK), .clr(RST));  // open: load, D, carry, preset, down
  Multiplexer #(.select(1), .width(32), .disabled("Z"), .enable("false")) multiplexer_10 (
    .in0(MEM_ReadData), .in1(bit_extender_4_out), .out(multiplexer_10_out), .sel(ex_mem_1_lbout));
  or or_16 (or_16_out, ex_mem_1_jalrout, ex_mem_1_jalout);
  Multiplexer #(.select(1), .width(32), .disabled("Z"), .enable("false")) multiplexer_11 (
    .in0({ex_mem_1_aluresultout, MEM_ALUHIGH}), .in1(multiplexer_10_out), .out(multiplexer_11_out),
    .sel(ex_mem_1_memtoregout));
  Multiplexer #(.select(1), .width(32), .disabled("Z"), .enable("false")) multiplexer_12 (
    .in0(multiplexer_11_out), .in1(adder_4_out), .out(MEM_DATAOUT), .sel(or_16_out));
  Adder #(.width(32)) adder_4 (.a(32'h4), .b(M_PC), .out(adder_4_out));  // open: cin, cout
  RAM #(.addrWidth(10), .dataWidth(32), .bus("separate"), .Select("high")) ram_1 (
    .addr(ex_mem_1_aluresultout[11:2]), .din(MDin), .data(MEM_ReadData), .str(MemWrite), .clk(CLK));  // open: sel, ld, clr
  not not_8 (not_8_out, halt);
  Register #(.width(32), .trigger("rising"), .Select("low")) register_9 (
    .D(multiplexer_8_out), .en(INTR), .Q(EPC), .clk(CLK));  // open: clr
  nor nor_3 (nor_3_out, Go, not_8_out);
  MEM_WB mem_wb_1 (
    .JAL(ex_mem_1_jalout), .JALR(ex_mem_1_jalrout), .LB(ex_mem_1_lbout), .MemToReg(ex_mem_1_memtoregout),
    .RegWrite(MEM_RegWrite), .ALUResult({ex_mem_1_aluresultout, MEM_ALUHIGH}),
    .RegWriteDest(MEM_RegWriteDest_num), .IR(MEM_IR), .PC(M_PC), .JALout(mem_wb_1_jalout),
    .JALRout(mem_wb_1_jalrout), .LBout(mem_wb_1_lbout), .MemToRegout(mem_wb_1_memtoregout),
    .RegWriteout(RegWrite), .ALUResultout(mem_wb_1_aluresultout), .RegWriteDestout(RegWriteDest),
    .MemDataout(mem_wb_1_memdataout), .IRout(WB_IR), .PCout(WB_PC), .RESET(RST), .bubble(1'b0),
    .EN(nor_3_out), .CLK(CLK), .BLT(ex_mem_1_bltout), .ALUResultHigh(MEM_ALUHIGH),
    .ALUResultHighout(mem_wb_1_aluresulthighout), .MemData(MEM_ReadData), .halt(ex_mem_1_haltout),
    .haltout(halt));  // open: BLTout
  Multiplexer #(.select(2), .width(32), .disabled("Z"), .enable("false")) multiplexer_13 (
    .in0(multiplexer_8_out), .in1(INTR_PC), .in2(EPC), .out(NEXT_PC), .sel(priority_encoder_3_out));  // open: in3
  Priority_Encoder #(.select(2), .disabled("Z")) priority_encoder_3 (
    .in0(1'b1), .in1(INTR), .in2(URET), .in3(1'b0), .out(priority_encoder_3_out));  // open: gs, en_out, en_in
  Comparator #(.width(32), .mode("twosComplement")) comparator_7 (
    .a(R2), .b(32'h22), .eq(comparator_7_eq));  // open: gt, lt
  Multiplexer #(.select(2), .width(8), .disabled("Z"), .enable("false")) multiplexer_14 (
    .in0(mem_wb_1_memdataout[7:0]), .in1(mem_wb_1_memdataout[15:8]), .in2(mem_wb_1_memdataout[23:16]),
    .in3(mem_wb_1_memdataout[31:24]), .out(multiplexer_14_out), .sel(mem_wb_1_aluresulthighout));
  and and_8 (and_8_out, ecall, comparator_7_eq);
  assign bit_extender_5_out = {{24{multiplexer_14_out[7]}}, multiplexer_14_out};  // Bit_Extender bit_extender_5
  Register #(.width(32), .trigger("rising"), .Select("low")) register_10 (
    .D(R1), .en(and_8_out), .Q(LedData), .clk(CLK), .clr(RST));
  Multiplexer #(.select(1), .width(32), .disabled("Z"), .enable("false")) multiplexer_15 (
    .in0(mem_wb_1_memdataout), .in1(bit_extender_5_out), .out(multiplexer_15_out), .sel(mem_wb_1_lbout));
  not not_9 (not_9_out, comparator_7_eq);
  Multiplexer #(.select(1), .width(32), .disabled("Z"), .enable("false")) multiplexer_16 (
    .in0(mem_wb_1_aluresultout), .in1(multiplexer_15_out), .out(multiplexer_16_out),
    .sel(mem_wb_1_memtoregout));
  and and_9 (haltsign, ecall, not_9_out);
  or or_17 (or_17_out, mem_wb_1_jalout, mem_wb_1_jalrout);
  Adder #(.width(32)) adder_5 (.a(WB_PC), .b(32'h4), .out(adder_5_out));  // open: cin, cout
  Multiplexer #(.select(1), .width(32), .disabled("Z"), .enable("false")) multiplexer_17 (
    .in0(multiplexer_16_out), .in1(adder_5_out), .out(RDin), .sel(or_17_out));

  // Other names for the same wires on the sheet: MEM_PC[31:0] = M_PC; 插入气泡数[15:0] = \LoadUse次数 

  // Notes on the sheet:
  //   中断源
  //   时空图监测，可删除
  //   中断等待指示
  //   单级中断测试信号模拟器
  //   总复位信号应将除ROM以外所有存储组件全部清零
  //   数码管输出
  //   contents of rom_1 (hex, n*v repeats v):
  //   7d000113 100413 1f41993 41f9d993 433 c00913 800b13 140413 f47413 800293 100313 499993 89e9b3 1300533
  //   2200893 73 406282b3 fe0294e3 140413 f00f93 1f47433 1c41413 800293 100313 49d993 89e9b3 1300533
  //   2200893 73 406282b3 fe0294e3 1c45413 406b0b33 b0463 f95ff06f 2b3 fff2c293 1029293 fff2e293 500533
  //   2200893 73 f5dff06f 1112023 410113 a12023 410113 812023 410113 1312023 410113 1412023 410113 1512023
  //   410113 1612023 410113 100b13 300a13 100a93 1600433 441413 14469b3 1300533 2200893 73 fe0416e3
  //   415a0a33 fe0a10e3 ffc10113 12b03 ffc10113 12a83 ffc10113 12a03 ffc10113 12983 ffc10113 12403
  //   ffc10113 12503 ffc10113 12883 200073 1112023 410113 a12023 410113 812023 410113 1312023 410113
  //   1412023 410113 1512023 410113 1612023 410113 200b13 300a13 100a93 1600433 441413 14469b3 1300533
  //   2200893 73 fe0416e3 415a0a33 fe0a10e3 ffc10113 12b03 ffc10113 12a83 ffc10113 12a03 ffc10113 12983
  //   ffc10113 12403 ffc10113 12503 ffc10113 12883 200073 1112023 410113 a12023 410113 812023 410113
  //   1312023 410113 1412023 410113 1512023 410113 1612023 410113 300b13 300a13 100a93 1600433 441413
  //   14469b3 1300533 2200893 73 fe0416e3 415a0a33 fe0a10e3 ffc10113 12b03 ffc10113 12a83 ffc10113 12a03
  //   ffc10113 12983 ffc10113 12403 ffc10113 12503 ffc10113 12883 200073
  //   MEM段写寄存器，将写回数据先返回
  //   EX段写寄存器，将MEM段数据提前返回
  //   中断响应
  //   R1
  //   R2
  //   WriteReg#
  //   I
  //   S
  //   B
  //   J
  //   流水调试日志用
  //   暂停节拍，不能为0
  //   戳工具置1进入计数暂停模式，ctrl+k时钟自动运行到对应节拍暂停
  //   ctrl+k关闭时钟连续运行，将控制位置零，进入单步调试模式调试
  //   用这个时钟源需要去掉电路中的其他时钟源
  //   可计数暂停的时钟源
  //   中断识别
  //   记录中断源，方便清除
  //   为方便自动评测，需要输出流水线各段保存的PC值，注意是PC不是PC+4，另外ID段寄存器写入信息，Mem段内存写入信息也要输出
endmodule
module \流水线_多级中断  (
  output RegWrite,
  output MemWrite,
  output [31:0] IF_PC,
  output [31:0] ID_PC,
  output [31:0] EX_PC,
  output [31:0] M_PC,
  output [31:0] WB_PC,
  output [31:0] RDin,
  output [31:0] MDin,
  output [31:0] LedData
);

  wire ALU_EQU, ALU_LESS, and_1_out, and_2_out, and_4_out, and_5_out, and_6_out, and_8_out, and_9_out,
       and_10_out, and_11_out, BEQ, BLT, BNE, Branch_Success, CLK, clock_1_out, CLRA, CLRB, CLRC,
       comparator_1_eq, comparator_2_eq, comparator_3_eq, comparator_4_eq, comparator_5_eq, comparator_6_eq,
       comparator_6_lt, comparator_7_eq, comparator_7_gt, comparator_8_gt, comparator_9_eq, CSRRCI, CSRRSI,
       d_ff_1_q, ecall, ex_mem_1_bltout, ex_mem_1_haltout, ex_mem_1_jalout, ex_mem_1_jalrout, ex_mem_1_lbout,
       ex_mem_1_memtoregout, EX_MemToReg, EX_RegWrite, Go, halt, haltsign, ID_CSRRCI, ID_CSRRSI,
       id_ex_1_alusrcbout, id_ex_1_lbout, id_ex_1_memwriteout, IE, InBranch, INTR, INTRA, INTRB, INTRC,
       IR_ecall, IRA, IRB, IRC, JAL, JALR, load_use, MEM_RegWrite, mem_wb_1_jalout, mem_wb_1_jalrout,
       mem_wb_1_lbout, mem_wb_1_memtoregout, multiplexer_6_out, multiplexer_7_out, nand_1_out, nor_1_out,
       nor_2_out, nor_3_out, not_1_out, not_2_out, not_3_out, not_5_out, not_6_out, not_7_out, not_8_out,
       not_9_out, not_10_out, not_11_out, or_1_out, or_2_out, or_3_out, or_4_out, or_5_out, or_6_out,
       or_7_out, or_8_out, or_10_out, or_12_out, or_16_out, or_17_out, or_18_out, or_19_out, register_1_q,
       register_2_q, register_11_q, register_12_q, register_13_q, RST, URET, W1, W2, W3,
       \单周期硬布线控制器_1_alu_src , \单周期硬布线控制器_1_beq , \单周期硬布线控制器_1_blt , \单周期硬布线控制器_1_bne , \单周期硬布线控制器_1_jal ,
       \单周期硬布线控制器_1_jalr , \单周期硬布线控制器_1_lb , \单周期硬布线控制器_1_memtoreg , \单周期硬布线控制器_1_memwrite ,
       \单周期硬布线控制器_1_regwrite , \单周期硬布线控制器_1_s_type , \单周期硬布线控制器_1_uret ;
  wire [1:0] CUR_INT, EX_R1Forword, EX_R2Forword, MEM_ALUHIGH, mem_wb_1_aluresulthighout, multiplexer_9_out,
       multiplexer_12_out, multiplexer_14_out, priority_encoder_1_out, priority_encoder_3_out, R1_Forword,
       R2_Forword, register_7_q, register_9_q;
  wire [2:0] PC_SRC;
  wire [3:0] id_ex_1_aluopout, \单周期硬布线控制器_1_alu_op ;
  wire [4:0] EX_RegWriteDest_num, MEM_RegWriteDest_num, multiplexer_3_out, multiplexer_4_out, RegWriteDest;
  wire [7:0] multiplexer_17_out, multiplexer_22_out;
  wire [11:0] multiplexer_5_out;
  wire [12:0] CNT_num;
  wire [15:0] \LoadUse次数 , \总周期数 , \无条件分支数 , \条件分支成功数 ;
  wire [31:0] adder_1_out, adder_2_out, adder_3_out, adder_4_out, adder_5_out, alu_1_result, and_7_out,
       bit_extender_1_out, bit_extender_2_out, bit_extender_3_out, bit_extender_4_out, bit_extender_5_out,
       EPC, EX_IR, EX_R1, EX_R2, id_ex_1_immbout, id_ex_1_immjout, id_ex_1_immout, ID_IR, IF_IR, INTR_PC,
       IR_PC, MEM_DATAOUT, MEM_IR, MEM_ReadData, mem_wb_1_aluresultout, mem_wb_1_memdataout,
       multiplexer_10_out, multiplexer_11_out, multiplexer_13_out, multiplexer_15_out, multiplexer_18_out,
       multiplexer_19_out, multiplexer_23_out, multiplexer_24_out, NEXT_PC, R1, R2, regifile4bubble_1_r1,
       regifile4bubble_1_r2, register_8_q, register_10_q, shifter_1_out, shifter_2_out, WB_IR;
  wire [31:2] ex_mem_1_aluresultout;

  Button \u_总复位  (.out(RST));
  Button _1 ();  // open: out
  Button _2 ();  // open: out
  Button _3 ();  // open: out
  // Probe on \总周期数 
  // Probe on \总周期数 
  Button \u_继续运行  (.out(Go));
  LED #(.active("true")) led_1 (.in(W1));
  LED #(.active("true")) led_2 (.in(W2));
  LED #(.active("true")) led_3 (.in(W3));
  or or_1 (or_1_out, Go, not_1_out);
  not not_1 (not_1_out, halt);
  Hex_Digit_Display hex_digit_display_1 (.value(LedData[31:28]));  // open: dp
  // Probe on IF_PC[19:0]
  // RiscV_Probe riscv_probe_1: pin names not known; wires that end beside it: IRA, IRB, IRC, IF_IR
  Comparator #(.width(16), .mode("twosComplement")) comparator_1 (
    .a(16'h258), .b(\总周期数 ), .eq(comparator_1_eq));  // open: gt, lt
  Comparator #(.width(16), .mode("twosComplement")) comparator_2 (
    .a(\总周期数 ), .b(16'h1), .eq(comparator_2_eq));  // open: gt, lt
  Comparator #(.width(16), .mode("twosComplement")) comparator_3 (
    .a(\总周期数 ), .b(16'h4), .eq(comparator_3_eq));  // open: gt, lt
  Comparator #(.width(16), .mode("twosComplement")) comparator_4 (
    .a(\总周期数 ), .b(16'h7), .eq(comparator_4_eq));  // open: gt, lt
  or or_2 (or_2_out, comparator_4_eq, comparator_5_eq);
  Comparator #(.width(16), .mode("twosComplement")) comparator_5 (
    .a(\总周期数 ), .b(16'h241), .eq(comparator_5_eq));  // open: gt, lt
  Counter #(.width(16), .max('hffff), .ongoal("wrap"), .trigger("rising"), .behavior("new")) counter_1 (
    .count(or_1_out), .Q(\总周期数 ), .clk(CLK), .clr(RST));  // open: load, D, carry, preset, down
  and and_1 (and_1_out, or_1_out, not_2_out);
  not not_2 (not_2_out, load_use);
  Hex_Digit_Display hex_digit_display_2 (.value(LedData[23:20]));  // open: dp
  Hex_Digit_Display hex_digit_display_3 (.value(LedData[27:24]));  // open: dp
  // Probe on ID_PC[19:0]
  // RiscV_Probe riscv_probe_2: pin names not known; wires that end beside it: ID_IR
  or or_3 (or_3_out, comparator_1_eq, comparator_2_eq);
  Pull_Resistor #(.pull(0)) pull_resistor_1 (.node(IRA));
  assign IRA = or_3_out ? ~CLK : 1'bz;  // Controlled_Inverter controlled_inverter_1
  Pull_Resistor #(.pull(0)) pull_resistor_2 (.node(IRB));
  assign IRB = comparator_3_eq ? ~CLK : 1'bz;  // Controlled_Inverter controlled_inverter_2
  Pull_Resistor #(.pull(0)) pull_resistor_3 (.node(IRC));
  assign IRC = or_2_out ? ~CLK : 1'bz;  // Controlled_Inverter controlled_inverter_3
  Register #(.width(32), .trigger("rising"), .Select("low")) PC (
    .D(NEXT_PC), .en(and_1_out), .Q(IF_PC), .clk(CLK), .clr(RST));
  Hex_Digit_Display hex_digit_display_4 (.value(LedData[15:12]));  // open: dp
  Hex_Digit_Display hex_digit_display_5 (.value(LedData[19:16]));  // open: dp
  not not_3 (not_3_out, halt);
  Hex_Digit_Display hex_digit_display_6 (.value(LedData[7:4]));  // open: dp
  Hex_Digit_Display hex_digit_display_7 (.value(LedData[11:8]));  // open: dp
  // Probe on EX_PC[19:0]
  // RiscV_Probe riscv_probe_3: pin names not known; wires that end beside it: EX_IR
  nor nor_1 (nor_1_out, Go, not_3_out);
  Hex_Digit_Display hex_digit_display_8 (.value(LedData[3:0]));  // open: dp
  Register #(.width(1), .trigger("rising"), .Select("low")) register_1 (
    .D(INTR), .Q(register_1_q), .clk(CLK));  // open: en, clr
  ROM #(.addrWidth(10), .dataWidth(32), .Select("low")) rom_1 (.addr(IF_PC[11:2]), .data(IF_IR));
  // Probe on \总周期数 
  // Probe on M_PC[19:0]
  // RiscV_Probe riscv_probe_4: pin names not known; wires that end beside it: MEM_IR
  or or_4 (or_4_out, URET, CSRRSI);
  IF_ID if_id_1 (
    .IR(IF_IR), .PC(IF_PC), .IRout(ID_IR), .PCout(ID_PC), .bubble(InBranch), .EN(or_6_out), .CLK(CLK),
    .RESET(RST));  // open: PREDICT_JUMP, PREDICT_JUMPout
  // Probe on \总周期数 
  // Probe on \无条件分支数 
  // Probe on \条件分支成功数 
  // Probe on \LoadUse次数 
  // Probe on \LoadUse次数 
  or or_5 (or_5_out, CSRRCI, register_1_q);
  not not_4 (IE, register_2_q);
  Register #(.width(1), .trigger("rising"), .Select("low")) register_2 (
    .D(1'b0), .Q(register_2_q), .clk(not_5_out), .preset(or_5_out));  // open: en, clr, cs
  not not_5 (not_5_out, or_4_out);
  Counter #(.width(16), .max('hffff), .ongoal("wrap"), .trigger("rising"), .behavior("new")) counter_2 (
    .count(load_use), .Q(\LoadUse次数 ), .clk(CLK), .clr(RST));  // open: load, D, carry, preset, down
  or or_6 (or_6_out, nor_1_out, load_use);
  // Probe on IF_PC[11:0]
  // Probe on WB_PC[19:0]
  // RiscV_Probe riscv_probe_5: pin names not known; wires that end beside it: WB_IR
  \流水冲突检测器4重定向  \u_流水冲突检测器4重定向_1  (
    .EX_RegWrite(EX_RegWrite), .MEM_RegWrite(MEM_RegWrite), .EX_RegWriteDest_num(EX_RegWriteDest_num),
    .MEM_RegWriteDest_num(MEM_RegWriteDest_num), .IR(ID_IR), .ecall(IR_ecall), .load_use(load_use),
    .EX_MEMToReg(EX_MemToReg), .R1_Forword(R1_Forword), .R2_Forword(R2_Forword));
  Multiplexer #(.select(2), .width(32), .disabled("Z"), .enable("false")) multiplexer_1 (
    .in0(EX_R1), .in1(RDin), .in2(MEM_DATAOUT), .in3(MEM_DATAOUT), .out(R1), .sel(EX_R1Forword));
  Multiplexer #(.select(2), .width(32), .disabled("Z"), .enable("false")) multiplexer_2 (
    .in0(EX_R2), .in1(RDin), .in2(MEM_DATAOUT), .in3(MEM_DATAOUT), .out(R2), .sel(EX_R2Forword));
  // Probe on EX_PC[11:0]
  // Probe on ID_PC[11:0]
  \单周期硬布线控制器  \u_单周期硬布线控制器_1  (
    .Funct({ID_IR[30], ID_IR[25], ID_IR[14:12]}), .OP(ID_IR[6:2]), .ALU_OP(\单周期硬布线控制器_1_alu_op ),
    .MemToReg(\单周期硬布线控制器_1_memtoreg ), .MemWrite(\单周期硬布线控制器_1_memwrite ), .ALU_SRC(\单周期硬布线控制器_1_alu_src ),
    .RegWrite(\单周期硬布线控制器_1_regwrite ), .ecall(IR_ecall), .S_type(\单周期硬布线控制器_1_s_type ),
    .Jalr(\单周期硬布线控制器_1_jalr ), .Beq(\单周期硬布线控制器_1_beq ), .JAL(\单周期硬布线控制器_1_jal ), .Bne(\单周期硬布线控制器_1_bne ),
    .in_3(ID_IR[21]), .uret(\单周期硬布线控制器_1_uret ), .BLT(\单周期硬布线控制器_1_blt ), .LB(\单周期硬布线控制器_1_lb ),
    .CSRRSI(ID_CSRRSI), .CSRRCI(ID_CSRRCI));
  Multiplexer #(.select(1), .width(5), .disabled("Z"), .enable("false")) multiplexer_3 (
    .in0(ID_IR[19:15]), .in1(5'b01010), .out(multiplexer_3_out), .sel(IR_ecall));
  Multiplexer #(.select(1), .width(5), .disabled("Z"), .enable("false")) multiplexer_4 (
    .in0(ID_IR[24:20]), .in1(5'b10001), .out(multiplexer_4_out), .sel(IR_ecall));
  Multiplexer #(.select(1), .width(12), .disabled("Z"), .enable("false")) multiplexer_5 (
    .in0(ID_IR[31:20]), .in1({ID_IR[31:25], ID_IR[11:7]}), .out(multiplexer_5_out), .sel(\单周期硬布线控制器_1_s_type ));
  Multiplexer #(.select(1), .width(1), .disabled("Z"), .enable("false")) multiplexer_6 (
    .in0(ID_CSRRSI), .in1(1'b0), .out(multiplexer_6_out), .sel(or_7_out));
  Multiplexer #(.select(1), .width(1), .disabled("Z"), .enable("false")) multiplexer_7 (
    .in0(ID_CSRRCI), .in1(1'b0), .out(multiplexer_7_out), .sel(or_7_out));
  // Probe on M_PC[11:0]
  D_Flip_Flop #(.trigger("high"), .Pre_Clr_Positions("LEGACY"), .NegatePresetClear("false"), .enable("true"), .NewFFLayout("false")) d_ff_1 (.Q(d_ff_1_q));  // open: clk, D, Qn, preset, en, reset
  // Probe on 13'h373
  Multiplexer #(.select(2), .width(32), .disabled("Z"), .enable("false")) multiplexer_8 (
    .in1(32'h30ac), .in2(32'h3158), .in3(32'h3204), .out(INTR_PC), .sel(priority_encoder_1_out));  // open: in0
  Priority_Encoder #(.select(2), .disabled("Z")) priority_encoder_1 (
    .in0(1'b1), .in1(INTRA), .in2(INTRB), .in3(INTRC), .out(priority_encoder_1_out));  // open: gs, en_out, en_in
  assign bit_extender_1_out = {{20{multiplexer_5_out[11]}}, multiplexer_5_out};  // Bit_Extender bit_extender_1
  assign bit_extender_2_out = {{20{ID_IR[31]}}, {ID_IR[31], ID_IR[7], ID_IR[30:25], ID_IR[11:8]}};  // Bit_Extender bit_extender_2
  assign bit_extender_3_out = {{12{ID_IR[31]}}, {ID_IR[31], ID_IR[19:12], ID_IR[20], ID_IR[30:21]}};  // Bit_Extender bit_extender_3
  not not_6 (not_6_out, nor_2_out);
  // Probe on WB_PC[11:0]
  Comparator #(.width(13), .mode("twosComplement")) comparator_6 (
    .a(CNT_num), .b(13'h373), .eq(comparator_6_eq), .lt(comparator_6_lt));  // open: gt
  Clock #(.highDuration(1), .lowDuration(1)) clock_1 (.out(clock_1_out));
  Demultiplexer #(.select(2), .width(1), .tristate("false"), .disabled("Z"), .enable("false")) demultiplexer_1 (
    .out1(CLRA), .out2(CLRB), .out3(CLRC), .in(URET), .sel(CUR_INT));  // open: out0
  Register #(.width(1), .trigger("rising"), .Select("low")) register_3 (
    .D(multiplexer_6_out), .en(not_6_out), .Q(CSRRSI), .clk(not_6_out));  // open: clr
  Register #(.width(1), .trigger("rising"), .Select("low")) register_4 (
    .D(multiplexer_7_out), .en(not_6_out), .Q(CSRRCI), .clk(CLK));  // open: clr
  nand nand_1 (nand_1_out, d_ff_1_q, comparator_6_eq);
  Counter #(.width(13), .max('h1fff), .ongoal("stay"), .trigger("rising"), .behavior("old")) counter_3 (
    .count(comparator_6_lt), .Q(CNT_num), .clk(clock_1_out));  // open: load, D, carry, clr, preset
  Comparator #(.width(32), .mode("twosComplement")) comparator_7 (
    .a({32{1'b0}}), .b(ID_IR), .gt(comparator_7_gt), .eq(comparator_7_eq));  // open: lt
  Regifile4Bubble regifile4bubble_1 (
    .Din(RDin), .Clk(CLK), .R1(regifile4bubble_1_r1), .R2(regifile4bubble_1_r2), .WE(RegWrite),
    .W_num(RegWriteDest), .R1_num(multiplexer_3_out), .R2_num(multiplexer_4_out));
  not not_7 (not_7_out, halt);
  assign CLK = nand_1_out ? clock_1_out : 1'bz;  // Controlled_Buffer controlled_buffer_1
  Comparator #(.width(2), .mode("unsigned")) comparator_8 (
    .a(priority_encoder_1_out), .b(CUR_INT), .gt(comparator_8_gt));  // open: eq, lt
  and and_2 (and_2_out, \单周期硬布线控制器_1_regwrite , not_8_out);
  not not_8 (not_8_out, comparator_7_eq);
  nor nor_2 (nor_2_out, Go, not_7_out);
  Pull_Resistor #(.pull(1)) pull_resistor_4 (.node(CLK));
  and and_3 (INTR, comparator_8_gt, IE);
  ID_EX id_ex_1 (
    .JAL(\单周期硬布线控制器_1_jal ), .BLT(\单周期硬布线控制器_1_blt ), .JALR(\单周期硬布线控制器_1_jalr ), .LB(\单周期硬布线控制器_1_lb ),
    .URET(\单周期硬布线控制器_1_uret ), .BEQ(\单周期硬布线控制器_1_beq ), .BNE(\单周期硬布线控制器_1_bne ),
    .MemToReg(\单周期硬布线控制器_1_memtoreg ), .MemWrite(\单周期硬布线控制器_1_memwrite ), .AluOP(\单周期硬布线控制器_1_alu_op ),
    .AluSrcB(\单周期硬布线控制器_1_alu_src ), .RegWrite(and_2_out), .R1(regifile4bubble_1_r1),
    .R2(regifile4bubble_1_r2), .Imm(bit_extender_1_out), .IR(ID_IR), .PC(ID_PC), .bubble(or_7_out),
    .EN(nor_2_out), .CLK(CLK), .JALout(JAL), .BLTout(BLT), .JALRout(JALR), .LBout(id_ex_1_lbout),
    .URETout(URET), .BEQout(BEQ), .BNEout(BNE), .MemToRegout(EX_MemToReg), .MemWriteout(id_ex_1_memwriteout),
    .AluOPout(id_ex_1_aluopout), .AluSrcBout(id_ex_1_alusrcbout), .RegWriteout(EX_RegWrite), .R1out(EX_R1),
    .R2out(EX_R2), .Immout(id_ex_1_immout), .IRout(EX_IR), .PCout(EX_PC), .RESET(RST), .ecallout(ecall),
    .ecall(IR_ecall), .ImmB(bit_extender_2_out), .ImmJ(bit_extender_3_out), .ImmBout(id_ex_1_immbout),
    .ImmJout(id_ex_1_immjout), .WriteDest_num(ID_IR[11:7]), .WriteDest_out(EX_RegWriteDest_num),
    .R1_Forword(R1_Forword), .R2_Forword(R2_Forword), .R1_Forwordout(EX_R1Forword),
    .R2_Forwordout(EX_R2Forword));  // open: PREDICT_JUMP, PREDICT_JUMPout
  or or_7 (or_7_out, InBranch, load_use);
  not not_9 (not_9_out, ALU_EQU);
  and and_4 (and_4_out, BNE, not_9_out);
  and and_5 (and_5_out, ALU_EQU, BEQ);
  and and_6 (and_6_out, BLT, ALU_LESS);
  or or_8 (or_8_out, INTR, URET);
  Multiplexer #(.select(1), .width(2), .disabled("Z"), .enable("false")) multiplexer_9 (
    .in0(priority_encoder_1_out), .in1(register_7_q), .out(multiplexer_9_out), .sel(URET));
  Multiplexer #(.select(1), .width(32), .disabled("Z"), .enable("false")) multiplexer_10 (
    .in0(IR_PC), .in1(register_8_q), .out(multiplexer_10_out), .sel(URET));
  Multiplexer #(.select(1), .width(32), .disabled("Z"), .enable("false")) multiplexer_11 (
    .in0(R2), .in1(id_ex_1_immout), .out(multiplexer_11_out), .sel(id_ex_1_alusrcbout));
  Shifter #(.width(32), .shift("ll")) shifter_1 (.in(id_ex_1_immbout), .\dist (5'b00001), .out(shifter_1_out));
  Shifter #(.width(32), .shift("ll")) shifter_2 (.in(id_ex_1_immjout), .\dist (5'b00001), .out(shifter_2_out));
  Register #(.width(2), .trigger("rising"), .Select("low")) register_5 (
    .D(multiplexer_9_out), .en(or_8_out), .Q(CUR_INT), .clk(CLK));  // open: clr
  Register #(.width(32), .trigger("rising"), .Select("low")) register_6 (
    .D(multiplexer_10_out), .en(or_8_out), .Q(EPC), .clk(CLK));  // open: clr
  Adder #(.width(32)) adder_1 (.a(shifter_1_out), .b(EX_PC), .out(adder_1_out));  // open: cin, cout
  Adder #(.width(32)) adder_2 (.a(shifter_2_out), .b(EX_PC), .out(adder_2_out));  // open: cin, cout
  Adder #(.width(32)) adder_3 (.a(IF_PC), .b(32'h4), .out(adder_3_out));  // open: cin, cout
  Priority_Encoder #(.select(3), .disabled("Z")) priority_encoder_2 (
    .in0(1'b1), .in1(and_4_out), .in2(and_5_out), .in3(JAL), .in4(JALR), .in5(and_6_out), .out(PC_SRC));  // open: in6, in7, gs, en_out, en_in
  or or_9 (InBranch, INTR, JAL, JALR, Branch_Success, URET);
  Multiplexer #(.select(1), .width(2), .disabled("Z"), .enable("false")) multiplexer_12 (
    .in0(CUR_INT), .in1(register_9_q), .out(multiplexer_12_out), .sel(URET));
  Multiplexer #(.select(1), .width(32), .disabled("Z"), .enable("false")) multiplexer_13 (
    .in0(EPC), .in1(register_10_q), .out(multiplexer_13_out), .sel(URET));
  or or_10 (or_10_out, JALR, JAL);
  ALU alu_1 (
    .X(R1), .Y(multiplexer_11_out), .AluOP(id_ex_1_aluopout), .Equal(ALU_EQU), .Result(alu_1_result),
    .out_6(ALU_LESS));  // open: Result_2, out_4
  or or_11 (Branch_Success, and_5_out, and_4_out, and_6_out);
  Register #(.width(2), .trigger("rising"), .Select("low")) register_7 (
    .D(multiplexer_12_out), .en(or_8_out), .Q(register_7_q), .clk(CLK));  // open: clr
  Register #(.width(32), .trigger("rising"), .Select("low")) register_8 (
    .D(multiplexer_13_out), .en(or_8_out), .Q(register_8_q), .clk(CLK));  // open: clr
  Counter #(.width(16), .max('hffff), .ongoal("wrap"), .trigger("rising"), .behavior("new")) counter_4 (
    .count(or_10_out), .Q(\无条件分支数 ), .clk(CLK), .clr(RST));  // open: load, D, carry, preset, down
  assign and_7_out = alu_1_result & 32'hfffffffe;  // AND_Gate and_7, 32 bits wide
  Multiplexer #(.select(1), .width(2), .disabled("Z"), .enable("false")) multiplexer_14 (
    .in0(register_7_q), .in1(2'b00), .out(multiplexer_14_out), .sel(URET));
  Multiplexer #(.select(1), .width(32), .disabled("Z"), .enable("false")) multiplexer_15 (
    .in0(register_8_q), .in1({32{1'b0}}), .out(multiplexer_15_out), .sel(URET));
  EX_MEM ex_mem_1 (
    .JAL(JAL), .JALR(JALR), .LB(id_ex_1_lbout), .MemToReg(EX_MemToReg), .MemWrite(id_ex_1_memwriteout),
    .RegWrite(EX_RegWrite), .ALUResult(alu_1_result), .R2(R2), .RegWriteDest(EX_RegWriteDest_num),
    .IR(EX_IR), .PC(EX_PC), .JALout(ex_mem_1_jalout), .JALRout(ex_mem_1_jalrout), .LBout(ex_mem_1_lbout),
    .MemToRegout(ex_mem_1_memtoregout), .MemWriteout(MemWrite), .RegWriteout(MEM_RegWrite),
    .ALUResultout({ex_mem_1_aluresultout, MEM_ALUHIGH}), .R2out(MDin),
    .RegWriteDestout(MEM_RegWriteDest_num), .IRout(MEM_IR), .PCout(M_PC), .RESET(RST), .bubble(1'b0),
    .EN(nor_3_out), .CLK(CLK), .BLT(BLT), .BLTout(ex_mem_1_bltout), .halt(haltsign),
    .haltout(ex_mem_1_haltout));
  Multiplexer #(.select(3), .width(32), .disabled("Z"), .enable("false")) multiplexer_16 (
    .in0(adder_3_out), .in1(adder_1_out), .in2(adder_1_out), .in3(adder_2_out), .in4(and_7_out),
    .in5(adder_1_out), .out(IR_PC), .sel(PC_SRC));  // open: in6, in7
  Register #(.width(2), .trigger("rising"), .Select("low")) register_9 (
    .D(multiplexer_14_out), .en(or_8_out), .Q(register_9_q), .clk(CLK));  // open: clr
  Register #(.width(32), .trigger("rising"), .Select("low")) register_10 (
    .D(multiplexer_15_out), .en(or_8_out), .Q(register_10_q), .clk(CLK));  // open: clr
  Multiplexer #(.select(2), .width(8), .disabled("Z"), .enable("false")) multiplexer_17 (
    .in0(MEM_ReadData[7:0]), .in1(MEM_ReadData[15:8]), .in2(MEM_ReadData[23:16]), .in3(MEM_ReadData[31:24]),
    .out(multiplexer_17_out), .sel(MEM_ALUHIGH));
  assign bit_extender_4_out = {{24{multiplexer_17_out[7]}}, multiplexer_17_out};  // Bit_Extender bit_extender_4
  Counter #(.width(16), .max('hffff), .ongoal("wrap"), .trigger("rising"), .behavior("new")) counter_5 (
    .count(Branch_Success), .Q(\条件分支成功数 ), .clk(CLK), .clr(RST));  // open: load, D, carry, preset, down
  Multiplexer #(.select(1), .width(32), .disabled("Z"), .enable("false")) multiplexer_18 (
    .in0(MEM_ReadData), .in1(bit_extender_4_out), .out(multiplexer_18_out), .sel(ex_mem_1_lbout));
  or or_12 (or_12_out, ex_mem_1_jalrout, ex_mem_1_jalout);
  Multiplexer #(.select(1), .width(32), .disabled("Z"), .enable("false")) multiplexer_19 (
    .in0({ex_mem_1_aluresultout, MEM_ALUHIGH}), .in1(multiplexer_18_out), .out(multiplexer_19_out),
    .sel(ex_mem_1_memtoregout));
  Multiplexer #(.select(1), .width(32), .disabled("Z"), .enable("false")) multiplexer_20 (
    .in0(multiplexer_19_out), .in1(adder_4_out), .out(MEM_DATAOUT), .sel(or_12_out));
  Adder #(.width(32)) adder_4 (.a(32'h4), .b(M_PC), .out(adder_4_out));  // open: cin, cout
  RAM #(.addrWidth(10), .dataWidth(32), .bus("separate"), .Select("high")) ram_1 (
    .addr(ex_mem_1_aluresultout[11:2]), .din(MDin), .data(MEM_ReadData), .str(MemWrite), .clk(CLK));  // open: sel, ld, clr
  not not_10 (not_10_out, halt);
  nor nor_3 (nor_3_out, Go, not_10_out);
  Multiplexer #(.select(2), .width(32), .disabled("Z"), .enable("false")) multiplexer_21 (
    .in0(IR_PC), .in1(INTR_PC), .in2(EPC), .out(NEXT_PC), .sel(priority_encoder_3_out));  // open: in3
  Priority_Encoder #(.select(2), .disabled("Z")) priority_encoder_3 (
    .in0(1'b1), .in1(INTR), .in2(URET), .in3(1'b0), .out(priority_encoder_3_out));  // open: gs, en_out, en_in
  MEM_WB mem_wb_1 (
    .JAL(ex_mem_1_jalout), .JALR(ex_mem_1_jalrout), .LB(ex_mem_1_lbout), .MemToReg(ex_mem_1_memtoregout),
    .RegWrite(MEM_RegWrite), .ALUResult({ex_mem_1_aluresultout, MEM_ALUHIGH}),
    .RegWriteDest(MEM_RegWriteDest_num), .IR(MEM_IR), .PC(M_PC), .JALout(mem_wb_1_jalout),
    .JALRout(mem_wb_1_jalrout), .LBout(mem_wb_1_lbout), .MemToRegout(mem_wb_1_memtoregout),
    .RegWriteout(RegWrite), .ALUResultout(mem_wb_1_aluresultout), .RegWriteDestout(RegWriteDest),
    .MemDataout(mem_wb_1_memdataout), .IRout(WB_IR), .PCout(WB_PC), .RESET(RST), .bubble(1'b0),
    .EN(nor_3_out), .CLK(CLK), .BLT(ex_mem_1_bltout), .ALUResultHigh(MEM_ALUHIGH),
    .ALUResultHighout(mem_wb_1_aluresulthighout), .MemData(MEM_ReadData), .halt(ex_mem_1_haltout),
    .haltout(halt));  // open: BLTout
  Register #(.width(1), .trigger("rising"), .Select("low")) register_11 (
    .D(1'b1), .Q(register_11_q), .clk(IRA), .clr(INTRA));  // open: en
  or or_13 (W1, INTRA, register_11_q);
  Register #(.width(1), .trigger("rising"), .Select("low")) register_12 (
    .D(1'b1), .Q(register_12_q), .clk(IRB), .clr(INTRB));  // open: en
  or or_14 (W2, INTRB, register_12_q);
  Register #(.width(1), .trigger("rising"), .Select("low")) register_13 (
    .D(1'b1), .Q(register_13_q), .clk(IRC), .clr(INTRC));  // open: en
  or or_15 (W3, INTRC, register_13_q);
  Comparator #(.width(32), .mode("twosComplement")) comparator_9 (
    .a(R2), .b(32'h22), .eq(comparator_9_eq));  // open: gt, lt
  Multiplexer #(.select(2), .width(8), .disabled("Z"), .enable("false")) multiplexer_22 (
    .in0(mem_wb_1_memdataout[7:0]), .in1(mem_wb_1_memdataout[15:8]), .in2(mem_wb_1_memdataout[23:16]),
    .in3(mem_wb_1_memdataout[31:24]), .out(multiplexer_22_out), .sel(mem_wb_1_aluresulthighout));
  or or_16 (or_16_out, register_11_q, INTRA);
  or or_17 (or_17_out, register_13_q, INTRC);
  and and_8 (and_8_out, ecall, comparator_9_eq);
  assign bit_extender_5_out = {{24{multiplexer_22_out[7]}}, multiplexer_22_out};  // Bit_Extender bit_extender_5
  and and_9 (and_9_out, or_16_out, ~CLRA);  // AND_Gate
  and and_10 (and_10_out, or_18_out, ~CLRB);  // AND_Gate
  or or_18 (or_18_out, register_12_q, INTRB);
  and and_11 (and_11_out, or_17_out, ~CLRC);  // AND_Gate
  Register #(.width(32), .trigger("rising"), .Select("low")) register_14 (
    .D(R1), .en(and_8_out), .Q(LedData), .clk(CLK), .clr(RST));
  Multiplexer #(.select(1), .width(32), .disabled("Z"), .enable("false")) multiplexer_23 (
    .in0(mem_wb_1_memdataout), .in1(bit_extender_5_out), .out(multiplexer_23_out), .sel(mem_wb_1_lbout));
  Register #(.width(1), .trigger("rising"), .Select("low")) register_15 (
    .D(and_9_out), .Q(INTRA), .clk(CLK));  // open: en, clr
  Register #(.width(1), .trigger("rising"), .Select("low")) register_16 (
    .D(and_10_out), .Q(INTRB), .clk(CLK));  // open: en, clr
  Register #(.width(1), .trigger("rising"), .Select("low")) register_17 (
    .D(and_11_out), .Q(INTRC), .clk(CLK));  // open: en, clr
  not not_11 (not_11_out, comparator_9_eq);
  Multiplexer #(.select(1), .width(32), .disabled("Z"), .enable("false")) multiplexer_24 (
    .in0(mem_wb_1_aluresultout), .in1(multiplexer_23_out), .out(multiplexer_24_out),
    .sel(mem_wb_1_memtoregout));
  and and_12 (haltsign, ecall, not_11_out);
  or or_19 (or_19_out, mem_wb_1_jalout, mem_wb_1_jalrout);
  Adder #(.width(32)) adder_5 (.a(WB_PC), .b(32'h4), .out(adder_5_out));  // open: cin, cout
  Multiplexer #(.select(1), .width(32), .disabled("Z"), .enable("false")) multiplexer_25 (
    .in0(multiplexer_24_out), .in1(adder_5_out), .out(RDin), .sel(or_19_out));

  // Other names for the same wires on the sheet: MEM_PC[31:0] = M_PC; 插入气泡数[15:0] = \LoadUse次数 

  // Notes on the sheet:
  //   中断源
  //   时空图监测，可删除
  //   中断等待指示
  //   多级中断测试信号模拟器
  //   数码管输出
  //   戳工具置1进入计数暂停模式，ctrl+k时钟自动运行到对应节拍暂停
  //   ctrl+k关闭时钟连续运行，将控制位置零，进入单步调试模式调试
  //   有险象,延迟一拍
  //   contents of rom_1 (hex, n*v repeats v):
  //   7d000113 100413 1f41993 41f9d993 433 c00913 800b13 140413 f47413 800293 100313 499993 89e9b3 1300533
  //   2200893 73 406282b3 fe0294e3 140413 f00f93 1f47433 1c41413 800293 100313 49d993 89e9b3 1300533
  //   2200893 73 406282b3 fe0294e3 1c45413 406b0b33 b0463 f95ff06f 2b3 fff2c293 1029293 fff2e293 500533
  //   2200893 73 f5dff06f 1112023 410113 a12023 410113 812023 410113 1312023 410113 1412023 410113 1512023
  //   410113 1612023 410113 40e073 100b13 300a13 100a93 1600433 441413 14469b3 1300533 2200893 73 fe0416e3
  //   415a0a33 fe0a10e3 40f073 ffc10113 12b03 ffc10113 12a83 ffc10113 12a03 ffc10113 12983 ffc10113 12403
  //   ffc10113 12503 ffc10113 12883 200073 1112023 410113 a12023 410113 812023 410113 1312023 410113
  //   1412023 410113 1512023 410113 1612023 410113 40e073 200b13 300a13 100a93 1600433 441413 14469b3
  //   1300533 2200893 73 fe0416e3 415a0a33 fe0a10e3 40f073 ffc10113 12b03 ffc10113 12a83 ffc10113 12a03
  //   ffc10113 12983 ffc10113 12403 ffc10113 12503 ffc10113 12883 200073 1112023 410113 a12023 410113
  //   812023 410113 1312023 410113 1412023 410113 1512023 410113 1612023 410113 40e073 300b13 300a13
  //   100a93 1600433 441413 14469b3 1300533 2200893 73 fe0416e3 415a0a33 fe0a10e3 40f073 ffc10113 12b03
  //   ffc10113 12a83 ffc10113 12a03 ffc10113 12983 ffc10113 12403 ffc10113 12503 ffc10113 12883 200073
  //   MEM段写寄存器，将写回数据先返回
  //   EX段写寄存器，将MEM段数据提前返回
  //   中断响应
  //   R1
  //   R2
  //   WriteReg#
  //   I
  //   S
  //   B
  //   J
  //   流水调试日志用
  //   暂停节拍，不能为0
  //   中断识别
  //   懒得改流水接口了，直接在外面模拟
  //   中断清除
  //   可计数暂停的时钟源
  //   用这个时钟源需要去掉电路中的其他时钟源
  //   为方便自动评测，需要输出流水线各段保存的PC值，注意是PC不是PC+4，另外ID段寄存器写入信息，Mem段内存写入信息也要输出
  //   中断排队
  //   需要锁存中断号
endmodule

module \流水线_动态分支预测  (
  output RegWrite,
  output MemWrite,
  output [31:0] IF_PC,
  output [31:0] ID_PC,
  output [31:0] EX_PC,
  output [31:0] M_PC,
  output [31:0] WB_PC,
  output [31:0] RDin,
  output [31:0] MDin,
  output [31:0] LedData
);

  wire ALU_EQU, ALU_LESS, and_1_out, and_2_out, and_3_out, and_4_out, and_5_out, and_7_out, BEQ, BLT, BNE,
       Branch_Success, CLK, clock_1_out, comparator_1_eq, comparator_1_lt, comparator_2_eq, comparator_2_gt,
       comparator_3_eq, comparator_4_eq, d_ff_1_q, ecall, ex_mem_1_bltout, ex_mem_1_haltout, ex_mem_1_jalout,
       ex_mem_1_jalrout, ex_mem_1_lbout, ex_mem_1_memtoregout, EX_MemToReg, EX_PREDICT_JUMP, EX_RegWrite, Go,
       halt, haltsign, id_ex_1_alusrcbout, id_ex_1_lbout, id_ex_1_memwriteout, if_id_1_predict_jumpout,
       InBranch, IR1, IR2, IR3, IR_ecall, JAL, JALR, load_use, MEM_RegWrite, mem_wb_1_jalout,
       mem_wb_1_jalrout, mem_wb_1_lbout, mem_wb_1_memtoregout, nand_1_out, nor_1_out, nor_2_out, nor_3_out,
       not_1_out, not_2_out, not_3_out, not_4_out, not_5_out, not_6_out, not_7_out, not_8_out, not_9_out,
       or_1_out, or_2_out, or_3_out, or_5_out, or_7_out, or_8_out, PREDICT_ERROR, PREDICT_JUMP, RST, W1, W2,
       W3, \单周期硬布线控制器_1_alu_src , \单周期硬布线控制器_1_beq , \单周期硬布线控制器_1_blt , \单周期硬布线控制器_1_bne , \单周期硬布线控制器_1_jal ,
       \单周期硬布线控制器_1_jalr , \单周期硬布线控制器_1_lb , \单周期硬布线控制器_1_memtoreg , \单周期硬布线控制器_1_memwrite ,
       \单周期硬布线控制器_1_regwrite , \单周期硬布线控制器_1_s_type , \单周期硬布线控制器_1_uret ;
  wire [1:0] EX_R1Forword, EX_R2Forword, MEM_ALUHIGH, mem_wb_1_aluresulthighout, R1_Forword, R2_Forword;
  wire [2:0] PC_SRC;
  wire [3:0] id_ex_1_aluopout, \单周期硬布线控制器_1_alu_op ;
  wire [4:0] EX_RegWriteDest_num, MEM_RegWriteDest_num, multiplexer_3_out, multiplexer_4_out, RegWriteDest;
  wire [7:0] multiplexer_8_out, multiplexer_15_out;
  wire [11:0] multiplexer_5_out;
  wire [12:0] CNT_num;
  wire [15:0] \LoadUse次数 , \总周期数 , \无条件分支数 , \条件分支成功数 ;
  wire [31:0] adder_1_out, adder_2_out, adder_3_out, adder_4_out, adder_5_out, adder_6_out, alu_1_result,
       and_6_out, bit_extender_1_out, bit_extender_2_out, bit_extender_3_out, bit_extender_4_out,
       bit_extender_5_out, controlled_buffer_2_out, EX_IR, EX_R1, EX_R2, id_ex_1_immbout, id_ex_1_immjout,
       id_ex_1_immout, ID_IR, IF_IR, JUMP_ADDR, MEM_DATAOUT, MEM_IR, MEM_ReadData, mem_wb_1_aluresultout,
       mem_wb_1_memdataout, multiplexer_6_out, multiplexer_7_out, multiplexer_9_out, multiplexer_10_out,
       multiplexer_11_out, multiplexer_13_out, multiplexer_16_out, multiplexer_17_out, NEXT_PC, R1, R2,
       regifile4bubble_1_r1, regifile4bubble_1_r2, shifter_1_out, shifter_2_out, WB_IR;
  wire [31:2] ex_mem_1_aluresultout;

  Button \u_总复位  (.out(RST));
  Button _1 (.out(IR1));
  Button _2 (.out(IR2));
  Button _3 (.out(IR3));
  // Probe on \总周期数 
  // Probe on \总周期数 
  Button \u_继续运行  (.out(Go));
  LED #(.active("true")) led_1 (.in(W1));
  LED #(.active("true")) led_2 (.in(W2));
  LED #(.active("true")) led_3 (.in(W3));
  or or_1 (or_1_out, Go, not_1_out);
  not not_1 (not_1_out, halt);
  Hex_Digit_Display hex_digit_display_1 (.value(LedData[31:28]));  // open: dp
  // Probe on IF_PC[19:0]
  // RiscV_Probe riscv_probe_1: pin names not known; wires that end beside it: IF_IR
  Counter #(.width(16), .max('hffff), .ongoal("wrap"), .trigger("rising"), .behavior("new")) counter_1 (
    .count(or_1_out), .Q(\总周期数 ), .clk(CLK), .clr(RST));  // open: load, D, carry, preset, down
  and and_1 (and_1_out, or_1_out, not_2_out);
  not not_2 (not_2_out, load_use);
  Hex_Digit_Display hex_digit_display_2 (.value(LedData[27:24]));  // open: dp
  Hex_Digit_Display hex_digit_display_3 (.value(LedData[23:20]));  // open: dp
  // Probe on ID_PC[19:0]
  // RiscV_Probe riscv_probe_2: pin names not known; wires that end beside it: ID_IR
  Register #(.width(32), .trigger("rising"), .Select("low")) PC (
    .D(NEXT_PC), .en(and_1_out), .Q(IF_PC), .clk(CLK), .clr(RST));
  Hex_Digit_Display hex_digit_display_4 (.value(LedData[15:12]));  // open: dp
  Hex_Digit_Display hex_digit_display_5 (.value(LedData[19:16]));  // open: dp
  not not_3 (not_3_out, halt);
  Hex_Digit_Display hex_digit_display_6 (.value(LedData[7:4]));  // open: dp
  Hex_Digit_Display hex_digit_display_7 (.value(LedData[11:8]));  // open: dp
  // Probe on EX_PC[19:0]
  // RiscV_Probe riscv_probe_3: pin names not known; wires that end beside it: EX_IR
  nor nor_1 (nor_1_out, Go, not_3_out);
  Hex_Digit_Display hex_digit_display_8 (.value(LedData[3:0]));  // open: dp
  ROM #(.addrWidth(10), .dataWidth(32), .Select("low")) rom_1 (.addr(IF_PC[11:2]), .data(IF_IR));
  // Probe on \总周期数 
  // Probe on M_PC[19:0]
  // RiscV_Probe riscv_probe_4: pin names not known; wires that end beside it: MEM_IR
  IF_ID if_id_1 (
    .IR(IF_IR), .PC(IF_PC), .IRout(ID_IR), .PCout(ID_PC), .bubble(PREDICT_ERROR), .EN(or_2_out), .CLK(CLK),
    .RESET(RST), .PREDICT_JUMP(PREDICT_JUMP), .PREDICT_JUMPout(if_id_1_predict_jumpout));
  // Probe on \总周期数 
  // Probe on \无条件分支数 
  // Probe on \条件分支成功数 
  // Probe on \LoadUse次数 
  // Probe on \LoadUse次数 
  Counter #(.width(16), .max('hffff), .ongoal("wrap"), .trigger("rising"), .behavior("new")) counter_2 (
    .count(load_use), .Q(\LoadUse次数 ), .clk(CLK), .clr(RST));  // open: load, D, carry, preset, down
  or or_2 (or_2_out, nor_1_out, load_use);
  // Probe on IF_PC[11:0]
  // Probe on WB_PC[19:0]
  // RiscV_Probe riscv_probe_5: pin names not known; wires that end beside it: WB_IR
  \流水冲突检测器4重定向  \u_流水冲突检测器4重定向_1  (
    .EX_RegWrite(EX_RegWrite), .MEM_RegWrite(MEM_RegWrite), .EX_RegWriteDest_num(EX_RegWriteDest_num),
    .MEM_RegWriteDest_num(MEM_RegWriteDest_num), .IR(ID_IR), .ecall(IR_ecall), .load_use(load_use),
    .EX_MEMToReg(EX_MemToReg), .R1_Forword(R1_Forword), .R2_Forword(R2_Forword));
  Multiplexer #(.select(2), .width(32), .disabled("Z"), .enable("false")) multiplexer_1 (
    .in0(EX_R1), .in1(RDin), .in2(MEM_DATAOUT), .in3(MEM_DATAOUT), .out(R1), .sel(EX_R1Forword));
  Multiplexer #(.select(2), .width(32), .disabled("Z"), .enable("false")) multiplexer_2 (
    .in0(EX_R2), .in1(RDin), .in2(MEM_DATAOUT), .in3(MEM_DATAOUT), .out(R2), .sel(EX_R2Forword));
  // Probe on EX_PC[11:0]
  // Probe on ID_PC[11:0]
  \单周期硬布线控制器  \u_单周期硬布线控制器_1  (
    .Funct({ID_IR[30], ID_IR[25], ID_IR[14:12]}), .OP(ID_IR[6:2]), .ALU_OP(\单周期硬布线控制器_1_alu_op ),
    .MemToReg(\单周期硬布线控制器_1_memtoreg ), .MemWrite(\单周期硬布线控制器_1_memwrite ), .ALU_SRC(\单周期硬布线控制器_1_alu_src ),
    .RegWrite(\单周期硬布线控制器_1_regwrite ), .ecall(IR_ecall), .S_type(\单周期硬布线控制器_1_s_type ),
    .Jalr(\单周期硬布线控制器_1_jalr ), .Beq(\单周期硬布线控制器_1_beq ), .JAL(\单周期硬布线控制器_1_jal ), .Bne(\单周期硬布线控制器_1_bne ),
    .in_3(ID_IR[21]), .uret(\单周期硬布线控制器_1_uret ), .BLT(\单周期硬布线控制器_1_blt ), .LB(\单周期硬布线控制器_1_lb ));  // open: CSRRSI, CSRRCI
  Multiplexer #(.select(1), .width(5), .disabled("Z"), .enable("false")) multiplexer_3 (
    .in0(ID_IR[19:15]), .in1(5'b01010), .out(multiplexer_3_out), .sel(IR_ecall));
  Multiplexer #(.select(1), .width(5), .disabled("Z"), .enable("false")) multiplexer_4 (
    .in0(ID_IR[24:20]), .in1(5'b10001), .out(multiplexer_4_out), .sel(IR_ecall));
  Multiplexer #(.select(1), .width(12), .disabled("Z"), .enable("false")) multiplexer_5 (
    .in0(ID_IR[31:20]), .in1({ID_IR[31:25], ID_IR[11:7]}), .out(multiplexer_5_out), .sel(\单周期硬布线控制器_1_s_type ));
  // Probe on M_PC[11:0]
  D_Flip_Flop #(.trigger("high"), .Pre_Clr_Positions("LEGACY"), .NegatePresetClear("false"), .enable("true"), .NewFFLayout("false")) d_ff_1 (.Q(d_ff_1_q));  // open: clk, D, Qn, preset, en, reset
  // Probe on 13'h373
  assign bit_extender_1_out = {{20{multiplexer_5_out[11]}}, multiplexer_5_out};  // Bit_Extender bit_extender_1
  assign bit_extender_2_out = {{20{ID_IR[31]}}, {ID_IR[31], ID_IR[7], ID_IR[30:25], ID_IR[11:8]}};  // Bit_Extender bit_extender_2
  assign bit_extender_3_out = {{12{ID_IR[31]}}, {ID_IR[31], ID_IR[19:12], ID_IR[20], ID_IR[30:21]}};  // Bit_Extender bit_extender_3
  // Probe on WB_PC[11:0]
  Comparator #(.width(13), .mode("twosComplement")) comparator_1 (
    .a(CNT_num), .b(13'h373), .eq(comparator_1_eq), .lt(comparator_1_lt));  // open: gt
  Clock #(.highDuration(1), .lowDuration(1)) clock_1 (.out(clock_1_out));
  nand nand_1 (nand_1_out, d_ff_1_q, comparator_1_eq);
  Counter #(.width(13), .max('h1fff), .ongoal("stay"), .trigger("rising"), .behavior("old")) counter_3 (
    .count(comparator_1_lt), .Q(CNT_num), .clk(clock_1_out));  // open: load, D, carry, clr, preset
  Comparator #(.width(32), .mode("twosComplement")) comparator_2 (
    .a({32{1'b0}}), .b(ID_IR), .gt(comparator_2_gt), .eq(comparator_2_eq));  // open: lt
  Regifile4Bubble regifile4bubble_1 (
    .Din(RDin), .Clk(CLK), .R1(regifile4bubble_1_r1), .R2(regifile4bubble_1_r2), .WE(RegWrite),
    .W_num(RegWriteDest), .R1_num(multiplexer_3_out), .R2_num(multiplexer_4_out));
  not not_4 (not_4_out, halt);
  assign CLK = nand_1_out ? clock_1_out : 1'bz;  // Controlled_Buffer controlled_buffer_1
  and and_2 (and_2_out, \单周期硬布线控制器_1_regwrite , not_5_out);
  not not_5 (not_5_out, comparator_2_eq);
  nor nor_2 (nor_2_out, Go, not_4_out);
  Pull_Resistor #(.pull(1)) pull_resistor_1 (.node(CLK));
  ID_EX id_ex_1 (
    .JAL(\单周期硬布线控制器_1_jal ), .BLT(\单周期硬布线控制器_1_blt ), .JALR(\单周期硬布线控制器_1_jalr ), .LB(\单周期硬布线控制器_1_lb ),
    .URET(\单周期硬布线控制器_1_uret ), .BEQ(\单周期硬布线控制器_1_beq ), .BNE(\单周期硬布线控制器_1_bne ),
    .MemToReg(\单周期硬布线控制器_1_memtoreg ), .MemWrite(\单周期硬布线控制器_1_memwrite ), .AluOP(\单周期硬布线控制器_1_alu_op ),
    .AluSrcB(\单周期硬布线控制器_1_alu_src ), .RegWrite(and_2_out), .R1(regifile4bubble_1_r1),
    .R2(regifile4bubble_1_r2), .Imm(bit_extender_1_out), .IR(ID_IR), .PC(ID_PC), .bubble(or_3_out),
    .EN(nor_2_out), .CLK(CLK), .JALout(JAL), .BLTout(BLT), .JALRout(JALR), .LBout(id_ex_1_lbout),
    .BEQout(BEQ), .BNEout(BNE), .MemToRegout(EX_MemToReg), .MemWriteout(id_ex_1_memwriteout),
    .AluOPout(id_ex_1_aluopout), .AluSrcBout(id_ex_1_alusrcbout), .RegWriteout(EX_RegWrite), .R1out(EX_R1),
    .R2out(EX_R2), .Immout(id_ex_1_immout), .IRout(EX_IR), .PCout(EX_PC), .RESET(RST), .ecallout(ecall),
    .ecall(IR_ecall), .ImmB(bit_extender_2_out), .ImmJ(bit_extender_3_out), .ImmBout(id_ex_1_immbout),
    .ImmJout(id_ex_1_immjout), .WriteDest_num(ID_IR[11:7]), .WriteDest_out(EX_RegWriteDest_num),
    .R1_Forword(R1_Forword), .R2_Forword(R2_Forword), .R1_Forwordout(EX_R1Forword),
    .R2_Forwordout(EX_R2Forword), .PREDICT_JUMP(if_id_1_predict_jumpout), .PREDICT_JUMPout(EX_PREDICT_JUMP));  // open: URETout
  or or_3 (or_3_out, PREDICT_ERROR, load_use);
  not not_6 (not_6_out, ALU_EQU);
  and and_3 (and_3_out, BNE, not_6_out);
  and and_4 (and_4_out, ALU_EQU, BEQ);
  and and_5 (and_5_out, BLT, ALU_LESS);
  Multiplexer #(.select(1), .width(32), .disabled("Z"), .enable("false")) multiplexer_6 (
    .in0(R2), .in1(id_ex_1_immout), .out(multiplexer_6_out), .sel(id_ex_1_alusrcbout));
  Shifter #(.width(32), .shift("ll")) shifter_1 (.in(id_ex_1_immbout), .\dist (5'b00001), .out(shifter_1_out));
  Shifter #(.width(32), .shift("ll")) shifter_2 (.in(id_ex_1_immjout), .\dist (5'b00001), .out(shifter_2_out));
  Adder #(.width(32)) adder_1 (.a(shifter_1_out), .b(EX_PC), .out(adder_1_out));  // open: cin, cout
  Adder #(.width(32)) adder_2 (.a(shifter_2_out), .b(EX_PC), .out(adder_2_out));  // open: cin, cout
  Adder #(.width(32)) adder_3 (.a(IF_PC), .b(32'h4), .out(adder_3_out));  // open: cin, cout
  Priority_Encoder #(.select(3), .disabled("Z")) priority_encoder_1 (
    .in0(1'b1), .in1(and_3_out), .in2(and_4_out), .in3(JAL), .in4(JALR), .in5(and_5_out), .out(PC_SRC));  // open: in6, in7, gs, en_out, en_in
  or or_4 (InBranch, JAL, JALR, Branch_Success);
  or or_5 (or_5_out, JALR, JAL);
  ALU alu_1 (
    .X(R1), .Y(multiplexer_6_out), .AluOP(id_ex_1_aluopout), .Equal(ALU_EQU), .Result(alu_1_result),
    .out_6(ALU_LESS));  // open: Result_2, out_4
  or or_6 (Branch_Success, and_4_out, and_3_out, and_5_out);
  Counter #(.width(16), .max('hffff), .ongoal("wrap"), .trigger("rising"), .behavior("new")) counter_4 (
    .count(or_5_out), .Q(\无条件分支数 ), .clk(CLK), .clr(RST));  // open: load, D, carry, preset, down
  assign and_6_out = alu_1_result & 32'hfffffffe;  // AND_Gate and_6, 32 bits wide
  xor xor_1 (PREDICT_ERROR, InBranch, EX_PREDICT_JUMP);
  EX_MEM ex_mem_1 (
    .JAL(JAL), .JALR(JALR), .LB(id_ex_1_lbout), .MemToReg(EX_MemToReg), .MemWrite(id_ex_1_memwriteout),
    .RegWrite(EX_RegWrite), .ALUResult(alu_1_result), .R2(R2), .RegWriteDest(EX_RegWriteDest_num),
    .IR(EX_IR), .PC(EX_PC), .JALout(ex_mem_1_jalout), .JALRout(ex_mem_1_jalrout), .LBout(ex_mem_1_lbout),
    .MemToRegout(ex_mem_1_memtoregout), .MemWriteout(MemWrite), .RegWriteout(MEM_RegWrite),
    .ALUResultout({ex_mem_1_aluresultout, MEM_ALUHIGH}), .R2out(MDin),
    .RegWriteDestout(MEM_RegWriteDest_num), .IRout(MEM_IR), .PCout(M_PC), .RESET(RST), .bubble(1'b0),
    .EN(nor_3_out), .CLK(CLK), .BLT(BLT), .BLTout(ex_mem_1_bltout), .halt(haltsign),
    .haltout(ex_mem_1_haltout));
  Multiplexer #(.select(3), .width(32), .disabled("Z"), .enable("false")) multiplexer_7 (
    .in0(adder_3_out), .in1(adder_1_out), .in2(adder_1_out), .in3(adder_2_out), .in4(and_6_out),
    .in5(adder_1_out), .out(multiplexer_7_out), .sel(PC_SRC));  // open: in6, in7
  Comparator #(.width(3), .mode("unsigned")) comparator_3 (
    .a(PC_SRC), .b(3'b000), .eq(comparator_3_eq));  // open: gt, lt
  Multiplexer #(.select(2), .width(8), .disabled("Z"), .enable("false")) multiplexer_8 (
    .in0(MEM_ReadData[7:0]), .in1(MEM_ReadData[15:8]), .in2(MEM_ReadData[23:16]), .in3(MEM_ReadData[31:24]),
    .out(multiplexer_8_out), .sel(MEM_ALUHIGH));
  assign controlled_buffer_2_out = not_7_out ? multiplexer_7_out : 32'bz;  // Controlled_Buffer controlled_buffer_2
  not not_7 (not_7_out, comparator_3_eq);
  assign bit_extender_4_out = {{24{multiplexer_8_out[7]}}, multiplexer_8_out};  // Bit_Extender bit_extender_4
  BHT bht_1 (
    .CLK(CLK), .IF_PC(IF_PC), .EX_PC(EX_PC), .BRANCH_ADDR(controlled_buffer_2_out),
    .Branch_Success(InBranch), .PREDICT_JUMP(PREDICT_JUMP), .JUMP_ADDR(JUMP_ADDR), .EX_BRANCH(not_7_out));
  Counter #(.width(16), .max('hffff), .ongoal("wrap"), .trigger("rising"), .behavior("new")) counter_5 (
    .count(Branch_Success), .Q(\条件分支成功数 ), .clk(CLK), .clr(RST));  // open: load, D, carry, preset, down
  Multiplexer #(.select(1), .width(32), .disabled("Z"), .enable("false")) multiplexer_9 (
    .in0(MEM_ReadData), .in1(bit_extender_4_out), .out(multiplexer_9_out), .sel(ex_mem_1_lbout));
  Multiplexer #(.select(1), .width(32), .disabled("Z"), .enable("false")) multiplexer_10 (
    .in0(adder_3_out), .in1(JUMP_ADDR), .out(multiplexer_10_out), .sel(PREDICT_JUMP));
  Adder #(.width(32)) adder_4 (.a(EX_PC), .b(32'h4), .out(adder_4_out));  // open: cin, cout
  or or_7 (or_7_out, ex_mem_1_jalrout, ex_mem_1_jalout);
  Multiplexer #(.select(1), .width(32), .disabled("Z"), .enable("false")) multiplexer_11 (
    .in0({ex_mem_1_aluresultout, MEM_ALUHIGH}), .in1(multiplexer_9_out), .out(multiplexer_11_out),
    .sel(ex_mem_1_memtoregout));
  Multiplexer #(.select(1), .width(32), .disabled("Z"), .enable("false")) multiplexer_12 (
    .in0(multiplexer_11_out), .in1(adder_5_out), .out(MEM_DATAOUT), .sel(or_7_out));
  Adder #(.width(32)) adder_5 (.a(32'h4), .b(M_PC), .out(adder_5_out));  // open: cin, cout
  RAM #(.addrWidth(10), .dataWidth(32), .bus("separate"), .Select("high")) ram_1 (
    .addr(ex_mem_1_aluresultout[11:2]), .din(MDin), .data(MEM_ReadData), .str(MemWrite), .clk(CLK));  // open: sel, ld, clr
  Multiplexer #(.select(1), .width(32), .disabled("Z"), .enable("false")) multiplexer_13 (
    .in0(adder_4_out), .in1(multiplexer_7_out), .out(multiplexer_13_out), .sel(InBranch));
  not not_8 (not_8_out, halt);
  Multiplexer #(.select(1), .width(32), .disabled("Z"), .enable("false")) multiplexer_14 (
    .in0(multiplexer_10_out), .in1(multiplexer_13_out), .out(NEXT_PC), .sel(PREDICT_ERROR));
  MEM_WB mem_wb_1 (
    .JAL(ex_mem_1_jalout), .JALR(ex_mem_1_jalrout), .LB(ex_mem_1_lbout), .MemToReg(ex_mem_1_memtoregout),
    .RegWrite(MEM_RegWrite), .ALUResult({ex_mem_1_aluresultout, MEM_ALUHIGH}),
    .RegWriteDest(MEM_RegWriteDest_num), .IR(MEM_IR), .PC(M_PC), .JALout(mem_wb_1_jalout),
    .JALRout(mem_wb_1_jalrout), .LBout(mem_wb_1_lbout), .MemToRegout(mem_wb_1_memtoregout),
    .RegWriteout(RegWrite), .ALUResultout(mem_wb_1_aluresultout), .RegWriteDestout(RegWriteDest),
    .MemDataout(mem_wb_1_memdataout), .IRout(WB_IR), .PCout(WB_PC), .RESET(RST), .bubble(1'b0),
    .EN(nor_3_out), .CLK(CLK), .BLT(ex_mem_1_bltout), .ALUResultHigh(MEM_ALUHIGH),
    .ALUResultHighout(mem_wb_1_aluresulthighout), .MemData(MEM_ReadData), .halt(ex_mem_1_haltout),
    .haltout(halt));  // open: BLTout
  nor nor_3 (nor_3_out, Go, not_8_out);
  Comparator #(.width(32), .mode("twosComplement")) comparator_4 (
    .a(R2), .b(32'h22), .eq(comparator_4_eq));  // open: gt, lt
  Multiplexer #(.select(2), .width(8), .disabled("Z"), .enable("false")) multiplexer_15 (
    .in0(mem_wb_1_memdataout[7:0]), .in1(mem_wb_1_memdataout[15:8]), .in2(mem_wb_1_memdataout[23:16]),
    .in3(mem_wb_1_memdataout[31:24]), .out(multiplexer_15_out), .sel(mem_wb_1_aluresulthighout));
  and and_7 (and_7_out, ecall, comparator_4_eq);
  assign bit_extender_5_out = {{24{multiplexer_15_out[7]}}, multiplexer_15_out};  // Bit_Extender bit_extender_5
  Register #(.width(32), .trigger("rising"), .Select("low")) register_1 (
    .D(R1), .en(and_7_out), .Q(LedData), .clk(CLK), .clr(RST));
  Multiplexer #(.select(1), .width(32), .disabled("Z"), .enable("false")) multiplexer_16 (
    .in0(mem_wb_1_memdataout), .in1(bit_extender_5_out), .out(multiplexer_16_out), .sel(mem_wb_1_lbout));
  not not_9 (not_9_out, comparator_4_eq);
  Multiplexer #(.select(1), .width(32), .disabled("Z"), .enable("false")) multiplexer_17 (
    .in0(mem_wb_1_aluresultout), .in1(multiplexer_16_out), .out(multiplexer_17_out),
    .sel(mem_wb_1_memtoregout));
  and and_8 (haltsign, ecall, not_9_out);
  or or_8 (or_8_out, mem_wb_1_jalout, mem_wb_1_jalrout);
  Adder #(.width(32)) adder_6 (.a(WB_PC), .b(32'h4), .out(adder_6_out));  // open: cin, cout
  Multiplexer #(.select(1), .width(32), .disabled("Z"), .enable("false")) multiplexer_18 (
    .in0(multiplexer_17_out), .in1(adder_6_out), .out(RDin), .sel(or_8_out));

  // Other names for the same wires on the sheet: MEM_PC[31:0] = M_PC; 插入气泡数[15:0] = \LoadUse次数 

  // Notes on the sheet:
  //   中断源
  //   时空图监测，可删除
  //   中断等待指示
  //   数码管输出
  //   contents of rom_1 (hex, n*v repeats v):
  //   100493 100006f 100493 200913 300993 100006f 100493 200913 300993 100006f 100493 200913 300993
  //   100006f 100493 200913 300993 3cc000ef 100413 100493 1f49493 900533 2200893 73 24d493 48463 fedff06f
  //   900533 2200893 73 100493 249493 900533 2200893 73 48463 fedff06f 100493 1f49493 900533 2200893 73
  //   4034d493 900533 2200893 73 4044d493 900533 2200893 73 4044d493 900533 2200893 73 4044d493 900533
  //   2200893 73 4044d493 900533 2200893 73 4044d493 900533 2200893 73 4044d493 900533 2200893 73 4044d493
  //   900533 2200893 73 100413 1f41993 41f9d993 433 c00913 300b13 140413 f47413 800293 100313 499993
  //   89e9b3 1300533 2200893 73 406282b3 fe0294e3 140413 f00f93 1f47433 1c41413 800293 100313 49d993
  //   89e9b3 1300533 2200893 73 406282b3 fe0294e3 1c45413 406b0b33 b0463 f95ff06f 2b3 fff2c293 829293
  //   ff2e293 500533 2200893 73 fff00413 493 84a023 140413 448493 84a023 140413 448493 84a023 140413
  //   448493 84a023 140413 448493 84a023 140413 448493 84a023 140413 448493 84a023 140413 448493 84a023
  //   140413 448493 84a023 140413 448493 84a023 140413 448493 84a023 140413 448493 84a023 140413 448493
  //   84a023 140413 448493 84a023 140413 448493 84a023 140413 448493 84a023 140413 448493 140413 433
  //   3c00493 42983 4aa03 149a2b3 28663 134a023 1442023 ffc48493 fe9412e3 800533 2200893 73 440413 3c00493
  //   fc9416e3 3200893 73 100293 300313 800493 849493 7648493 1449493 900533 2200893 73 800e13 4054d4b3
  //   4064d4b3 900533 2200893 73 fffe0e13 fe0e14e3 a00893 73 fff00293 7700493 849493 7748493 900533
  //   2200893 73 1000e13 54c4b3 900533 2200893 73 fffe0e13 fe0e16e3 a00893 73 313 1000e13 13 8400493
  //   849493 8348493 400913 891913 490913 849493 8248493 849493 8148493 891913 490913 891913 490913 932023
  //   12484b3 430313 fffe0e13 fe0e18e3 2000e13 313 30483 900533 2200893 73 130313 fffe0e13 fe0e14e3 a00893
  //   73 ff100493 900533 2200893 73 148493 fe04c8e3 a00893 73 413 140413 800533 2200893 73 240413 800533
  //   2200893 73 340413 800533 2200893 73 440413 800533 2200893 73 540413 800533 2200893 73 640413 800533
  //   2200893 73 740413 800533 2200893 73 840413 800533 2200893 2200893 73 8067
  //   MEM段写寄存器，将写回数据先返回
  //   EX段写寄存器，将MEM段数据提前返回
  //   R1
  //   R2
  //   WriteReg#
  //   I
  //   S
  //   B
  //   J
  //   流水调试日志用
  //   暂停节拍，不能为0
  //   戳工具置1进入计数暂停模式，ctrl+k时钟自动运行到对应节拍暂停
  //   ctrl+k关闭时钟连续运行，将控制位置零，进入单步调试模式调试
  //   用这个时钟源需要去掉电路中的其他时钟源
  //   可计数暂停的时钟源
  //   为方便自动评测，需要输出流水线各段保存的PC值，注意是PC不是PC+4，另外ID段寄存器写入信息，Mem段内存写入信息也要输出
  //   没有预测信号默认不跳转
  //   预测错误，则将跳转指令的后一条指令载入
  //   当要跳转时，只可能预测成功使用预测值或者失败使用跳转真实值
endmodule

// 动态分支预测器
module BHT (
  input  [31:0] IF_PC,
  input  [31:0] BRANCH_ADDR,
  input  Branch_Success,
  input  EX_BRANCH,
  input  [31:0] EX_PC,
  input  CLK,
  output [31:0] JUMP_ADDR,
  output PREDICT_JUMP
);

  wire and_9_out, and_10_out, and_11_out, and_12_out, and_13_out, and_14_out, and_15_out, and_16_out,
       comparator_1_eq, comparator_2_eq, comparator_3_eq, comparator_4_eq, comparator_5_eq, comparator_6_eq,
       comparator_7_eq, comparator_8_eq, comparator_9_eq, comparator_10_eq, comparator_11_eq,
       comparator_12_eq, comparator_13_eq, comparator_14_eq, comparator_15_eq, comparator_16_eq, d_ff_1_q,
       d_ff_2_q, d_ff_3_q, d_ff_4_q, d_ff_5_q, d_ff_6_q, d_ff_7_q, d_ff_8_q, demultiplexer_1_out0,
       demultiplexer_1_out1, demultiplexer_1_out2, demultiplexer_1_out3, demultiplexer_1_out4,
       demultiplexer_1_out5, demultiplexer_1_out6, demultiplexer_1_out7, demultiplexer_2_out0,
       demultiplexer_2_out1, demultiplexer_2_out2, demultiplexer_2_out3, demultiplexer_2_out4,
       demultiplexer_2_out5, demultiplexer_2_out6, demultiplexer_2_out7, full, hit0, hit1, hit2, hit3, hit4,
       hit5, hit6, hit7, l0, l1, l2, l3, l4, l5, l6, l7, MISS, multiplexer_13_out, not_1_out, not_2_out,
       not_3_out, not_4_out, not_5_out, not_6_out, not_7_out, not_8_out, or_1_out, or_2_out, or_3_out,
       or_4_out, or_5_out, or_6_out, or_7_out, or_8_out, or_9_out, or_10_out, or_11_out, or_12_out,
       or_13_out, or_14_out, or_15_out, or_16_out, or_17_out, or_18_out, or_19_out, or_20_out, or_21_out,
       or_22_out, or_23_out, or_24_out, priority_encoder_1_gs, priority_encoder_3_en_out, v0, v1, v2, v3, v4,
       v5, v6, v7, w0, w1, w2, w3, w4, w5, w6, w7;
  wire [1:0] multiplexer_1_out, multiplexer_2_out, multiplexer_3_out, multiplexer_4_out, multiplexer_5_out,
       multiplexer_6_out, multiplexer_7_out, multiplexer_8_out, multiplexer_9_out, multiplexer_11_out,
       next_status, p0, p1, p2, p3, p4, p5, p6, p7;
  wire [2:0] max2_1_max_num, max2_2_max_num, max2_3_max_num, max2_4_max_num, max2_5_max_num, max2_6_max_num,
       max2_7_max_num, multiplexer_12_out, priority_encoder_1_out, priority_encoder_2_out, select;
  wire [15:0] c0, c1, c2, c3, c4, c5, c6, c7, max2_1_max, max2_2_max, max2_3_max, max2_4_max, max2_5_max,
       max2_6_max;
  wire [31:0] add0, add1, add2, add3, add4, add5, add6, add7, EXPC0, EXPC1, EXPC2, EXPC3, EXPC4, EXPC5,
       EXPC6, EXPC7, multiplexer_14_out;

  Register #(.width(1), .trigger("rising"), .Select("low")) valid (.D(1'b1), .en(w0), .Q(v0), .clk(CLK));  // open: clr
  Register #(.width(1), .trigger("rising"), .Select("low")) valid_2 (
    .D(1'b1), .en(w1), .Q(v1), .clk(CLK));  // open: clr
  Register #(.width(1), .trigger("rising"), .Select("low")) valid_3 (
    .D(1'b1), .en(w2), .Q(v2), .clk(CLK));  // open: clr
  Register #(.width(1), .trigger("rising"), .Select("low")) valid_4 (
    .D(1'b1), .en(w3), .Q(v3), .clk(CLK));  // open: clr
  Register #(.width(1), .trigger("rising"), .Select("low")) valid_5 (
    .D(1'b1), .en(w4), .Q(v4), .clk(CLK));  // open: clr
  Register #(.width(1), .trigger("rising"), .Select("low")) valid_6 (
    .D(1'b1), .en(w5), .Q(v5), .clk(CLK));  // open: clr
  Register #(.width(1), .trigger("rising"), .Select("low")) valid_7 (
    .D(1'b1), .en(w6), .Q(v6), .clk(CLK));  // open: clr
  Register #(.width(1), .trigger("rising"), .Select("low")) valid_8 (
    .D(1'b1), .en(w7), .Q(v7), .clk(CLK));  // open: clr
  Register #(.width(32), .trigger("rising"), .Select("low")) u_EX_PC (
    .D(EX_PC), .en(w0), .Q(EXPC0), .clk(CLK));  // open: clr
  Register #(.width(32), .trigger("rising"), .Select("low")) EX_PC_2 (
    .D(EX_PC), .en(w1), .Q(EXPC1), .clk(CLK));  // open: clr
  Register #(.width(32), .trigger("rising"), .Select("low")) EX_PC_3 (
    .D(EX_PC), .en(w2), .Q(EXPC2), .clk(CLK));  // open: clr
  Register #(.width(32), .trigger("rising"), .Select("low")) EX_PC_4 (
    .D(EX_PC), .en(w3), .Q(EXPC3), .clk(CLK));  // open: clr
  Register #(.width(32), .trigger("rising"), .Select("low")) EX_PC_5 (
    .D(EX_PC), .en(w4), .Q(EXPC4), .clk(CLK));  // open: clr
  Register #(.width(32), .trigger("rising"), .Select("low")) EX_PC_6 (
    .D(EX_PC), .en(w5), .Q(EXPC5), .clk(CLK));  // open: clr
  Register #(.width(32), .trigger("rising"), .Select("low")) EX_PC_7 (
    .D(EX_PC), .en(w6), .Q(EXPC6), .clk(CLK));  // open: clr
  Register #(.width(32), .trigger("rising"), .Select("low")) EX_PC_8 (
    .D(EX_PC), .en(w7), .Q(EXPC7), .clk(CLK));  // open: clr
  Counter #(.width(16), .max('hffff), .ongoal("wrap"), .trigger("rising"), .behavior("new")) count (
    .D({16{1'b0}}), .Q(c0), .clk(CLK), .clr(d_ff_1_q));  // open: load, count, carry, preset, down
  Counter #(.width(16), .max('hffff), .ongoal("wrap"), .trigger("rising"), .behavior("new")) count_2 (
    .D({16{1'b0}}), .Q(c1), .clk(CLK), .clr(d_ff_2_q));  // open: load, count, carry, preset, down
  Counter #(.width(16), .max('hffff), .ongoal("wrap"), .trigger("rising"), .behavior("new")) count_3 (
    .D({16{1'b0}}), .Q(c2), .clk(CLK), .clr(d_ff_3_q));  // open: load, count, carry, preset, down
  Counter #(.width(16), .max('hffff), .ongoal("wrap"), .trigger("rising"), .behavior("new")) count_4 (
    .D({16{1'b0}}), .Q(c3), .clk(CLK), .clr(d_ff_4_q));  // open: load, count, carry, preset, down
  Counter #(.width(16), .max('hffff), .ongoal("wrap"), .trigger("rising"), .behavior("new")) count_5 (
    .D({16{1'b0}}), .Q(c4), .clk(CLK), .clr(d_ff_5_q));  // open: load, count, carry, preset, down
  Counter #(.width(16), .max('hffff), .ongoal("wrap"), .trigger("rising"), .behavior("new")) count_6 (
    .D({16{1'b0}}), .Q(c5), .clk(CLK), .clr(d_ff_6_q));  // open: load, count, carry, preset, down
  Counter #(.width(16), .max('hffff), .ongoal("wrap"), .trigger("rising"), .behavior("new")) count_7 (
    .D({16{1'b0}}), .Q(c6), .clk(CLK), .clr(d_ff_7_q));  // open: load, count, carry, preset, down
  Counter #(.width(16), .max('hffff), .ongoal("wrap"), .trigger("rising"), .behavior("new")) count_8 (
    .D({16{1'b0}}), .Q(c7), .clk(CLK), .clr(d_ff_8_q));  // open: load, count, carry, preset, down
  Register #(.width(32), .trigger("rising"), .Select("low")) data (
    .D(BRANCH_ADDR), .en(w0), .Q(add0), .clk(CLK));  // open: clr
  Register #(.width(32), .trigger("rising"), .Select("low")) data_2 (
    .D(BRANCH_ADDR), .en(w1), .Q(add1), .clk(CLK));  // open: clr
  Register #(.width(32), .trigger("rising"), .Select("low")) data_3 (
    .D(BRANCH_ADDR), .en(w2), .Q(add2), .clk(CLK));  // open: clr
  Register #(.width(32), .trigger("rising"), .Select("low")) data_4 (
    .D(BRANCH_ADDR), .en(w3), .Q(add3), .clk(CLK));  // open: clr
  Register #(.width(32), .trigger("rising"), .Select("low")) data_5 (
    .D(BRANCH_ADDR), .en(w4), .Q(add4), .clk(CLK));  // open: clr
  Register #(.width(32), .trigger("rising"), .Select("low")) data_6 (
    .D(BRANCH_ADDR), .en(w5), .Q(add5), .clk(CLK));  // open: clr
  Register #(.width(32), .trigger("rising"), .Select("low")) data_7 (
    .D(BRANCH_ADDR), .en(w6), .Q(add6), .clk(CLK));  // open: clr
  Register #(.width(32), .trigger("rising"), .Select("low")) data_8 (
    .D(BRANCH_ADDR), .en(w7), .Q(add7), .clk(CLK));  // open: clr
  Comparator #(.width(32), .mode("twosComplement")) comparator_1 (
    .a(EX_PC), .b(EXPC0), .eq(comparator_1_eq));  // open: gt, lt
  Comparator #(.width(32), .mode("twosComplement")) comparator_2 (
    .a(EX_PC), .b(EXPC1), .eq(comparator_2_eq));  // open: gt, lt
  Comparator #(.width(32), .mode("twosComplement")) comparator_3 (
    .a(EX_PC), .b(EXPC2), .eq(comparator_3_eq));  // open: gt, lt
  Comparator #(.width(32), .mode("twosComplement")) comparator_4 (
    .a(EX_PC), .b(EXPC3), .eq(comparator_4_eq));  // open: gt, lt
  Comparator #(.width(32), .mode("twosComplement")) comparator_5 (
    .a(EX_PC), .b(EXPC4), .eq(comparator_5_eq));  // open: gt, lt
  Comparator #(.width(32), .mode("twosComplement")) comparator_6 (
    .a(EX_PC), .b(EXPC5), .eq(comparator_6_eq));  // open: gt, lt
  Comparator #(.width(32), .mode("twosComplement")) comparator_7 (
    .a(EX_PC), .b(EXPC6), .eq(comparator_7_eq));  // open: gt, lt
  Comparator #(.width(32), .mode("twosComplement")) comparator_8 (
    .a(EX_PC), .b(EXPC7), .eq(comparator_8_eq));  // open: gt, lt
  and and_1 (hit0, comparator_1_eq, v0);
  and and_2 (hit1, comparator_2_eq, v1);
  and and_3 (hit2, comparator_3_eq, v2);
  and and_4 (hit3, comparator_4_eq, v3);
  and and_5 (hit4, comparator_5_eq, v4);
  and and_6 (hit5, comparator_6_eq, v5);
  and and_7 (hit6, comparator_7_eq, v6);
  and and_8 (hit7, comparator_8_eq, v7);
  and and_9 (and_9_out, EX_BRANCH, hit0);
  and and_10 (and_10_out, EX_BRANCH, hit1);
  and and_11 (and_11_out, EX_BRANCH, hit2);
  and and_12 (and_12_out, EX_BRANCH, hit3);
  and and_13 (and_13_out, EX_BRANCH, hit4);
  and and_14 (and_14_out, EX_BRANCH, hit5);
  and and_15 (and_15_out, EX_BRANCH, hit6);
  and and_16 (and_16_out, EX_BRANCH, hit7);
  Comparator #(.width(32), .mode("twosComplement")) comparator_9 (
    .a(IF_PC), .b(EXPC0), .eq(comparator_9_eq));  // open: gt, lt
  and and_17 (l0, comparator_9_eq, v0);
  Comparator #(.width(32), .mode("twosComplement")) comparator_10 (
    .a(IF_PC), .b(EXPC1), .eq(comparator_10_eq));  // open: gt, lt
  Comparator #(.width(32), .mode("twosComplement")) comparator_11 (
    .a(IF_PC), .b(EXPC2), .eq(comparator_11_eq));  // open: gt, lt
  Comparator #(.width(32), .mode("twosComplement")) comparator_12 (
    .a(IF_PC), .b(EXPC3), .eq(comparator_12_eq));  // open: gt, lt
  Comparator #(.width(32), .mode("twosComplement")) comparator_13 (
    .a(IF_PC), .b(EXPC4), .eq(comparator_13_eq));  // open: gt, lt
  Comparator #(.width(32), .mode("twosComplement")) comparator_14 (
    .a(IF_PC), .b(EXPC5), .eq(comparator_14_eq));  // open: gt, lt
  Comparator #(.width(32), .mode("twosComplement")) comparator_15 (
    .a(IF_PC), .b(EXPC6), .eq(comparator_15_eq));  // open: gt, lt
  Comparator #(.width(32), .mode("twosComplement")) comparator_16 (
    .a(IF_PC), .b(EXPC7), .eq(comparator_16_eq));  // open: gt, lt
  Multiplexer #(.select(1), .width(2), .disabled("Z"), .enable("false")) multiplexer_1 (
    .in0(2'b01), .in1(2'b10), .out(multiplexer_1_out), .sel(Branch_Success));
  and and_18 (l1, comparator_10_eq, v1);
  and and_19 (l2, comparator_11_eq, v2);
  and and_20 (l3, comparator_12_eq, v3);
  and and_21 (l4, comparator_13_eq, v4);
  and and_22 (l5, comparator_14_eq, v5);
  and and_23 (l6, comparator_15_eq, v6);
  and and_24 (l7, comparator_16_eq, v7);
  Multiplexer #(.select(1), .width(2), .disabled("Z"), .enable("false")) multiplexer_2 (
    .in0(next_status), .in1(multiplexer_1_out), .out(multiplexer_2_out), .sel(w0));
  or or_1 (or_1_out, and_9_out, w0);
  Multiplexer #(.select(1), .width(2), .disabled("Z"), .enable("false")) multiplexer_3 (
    .in0(next_status), .in1(multiplexer_1_out), .out(multiplexer_3_out), .sel(w1));
  or or_2 (or_2_out, and_10_out, w1);
  Multiplexer #(.select(1), .width(2), .disabled("Z"), .enable("false")) multiplexer_4 (
    .in0(next_status), .in1(multiplexer_1_out), .out(multiplexer_4_out), .sel(w2));
  or or_3 (or_3_out, and_11_out, w2);
  Multiplexer #(.select(1), .width(2), .disabled("Z"), .enable("false")) multiplexer_5 (
    .in0(next_status), .in1(multiplexer_1_out), .out(multiplexer_5_out), .sel(w3));
  or or_4 (or_4_out, and_12_out, w3);
  Multiplexer #(.select(1), .width(2), .disabled("Z"), .enable("false")) multiplexer_6 (
    .in0(next_status), .in1(multiplexer_1_out), .out(multiplexer_6_out), .sel(w4));
  or or_5 (or_5_out, and_13_out, w4);
  Multiplexer #(.select(1), .width(2), .disabled("Z"), .enable("false")) multiplexer_7 (
    .in0(next_status), .in1(multiplexer_1_out), .out(multiplexer_7_out), .sel(w5));
  or or_6 (or_6_out, and_14_out, w5);
  Multiplexer #(.select(1), .width(2), .disabled("Z"), .enable("false")) multiplexer_8 (
    .in0(next_status), .in1(multiplexer_1_out), .out(multiplexer_8_out), .sel(w6));
  or or_7 (or_7_out, and_15_out, w6);
  Multiplexer #(.select(1), .width(2), .disabled("Z"), .enable("false")) multiplexer_9 (
    .in0(next_status), .in1(multiplexer_1_out), .out(multiplexer_9_out), .sel(w7));
  or or_8 (or_8_out, w7, and_16_out);
  Register #(.width(2), .trigger("falling"), .Select("low")) history (
    .D(multiplexer_2_out), .en(or_1_out), .Q(p0), .clk(CLK));  // open: clr
  Register #(.width(2), .trigger("falling"), .Select("low")) history_2 (
    .D(multiplexer_3_out), .en(or_2_out), .Q(p1), .clk(CLK));  // open: clr
  Register #(.width(2), .trigger("falling"), .Select("low")) history_3 (
    .D(multiplexer_4_out), .en(or_3_out), .Q(p2), .clk(CLK));  // open: clr
  Register #(.width(2), .trigger("falling"), .Select("low")) history_4 (
    .D(multiplexer_5_out), .en(or_4_out), .Q(p3), .clk(CLK));  // open: clr
  Register #(.width(2), .trigger("falling"), .Select("low")) history_5 (
    .D(multiplexer_6_out), .en(or_5_out), .Q(p4), .clk(CLK));  // open: clr
  Register #(.width(2), .trigger("falling"), .Select("low")) history_6 (
    .D(multiplexer_7_out), .en(or_6_out), .Q(p5), .clk(CLK));  // open: clr
  Register #(.width(2), .trigger("falling"), .Select("low")) history_7 (
    .D(multiplexer_8_out), .en(or_7_out), .Q(p6), .clk(CLK));  // open: clr
  Register #(.width(2), .trigger("falling"), .Select("low")) history_8 (
    .D(multiplexer_9_out), .en(or_8_out), .Q(p7), .clk(CLK));  // open: clr
  or or_9 (or_9_out, l0, w0);
  or or_10 (or_10_out, l1, w1);
  or or_11 (or_11_out, l2, w2);
  or or_12 (or_12_out, l3, w3);
  or or_13 (or_13_out, l4, w4);
  or or_14 (or_14_out, l5, w5);
  or or_15 (or_15_out, l6, w6);
  or or_16 (or_16_out, l7, w7);
  D_Flip_Flop #(.trigger("rising"), .Pre_Clr_Positions("LEGACY"), .NegatePresetClear("false"), .enable("false"), .NewFFLayout("true")) d_ff_1 (
    .clk(CLK), .D(or_9_out), .Q(d_ff_1_q));  // open: Qn, preset, reset
  D_Flip_Flop #(.trigger("rising"), .Pre_Clr_Positions("LEGACY"), .NegatePresetClear("false"), .enable("false"), .NewFFLayout("true")) d_ff_2 (
    .clk(CLK), .D(or_10_out), .Q(d_ff_2_q));  // open: Qn, preset, reset
  D_Flip_Flop #(.trigger("rising"), .Pre_Clr_Positions("LEGACY"), .NegatePresetClear("false"), .enable("false"), .NewFFLayout("true")) d_ff_3 (
    .clk(CLK), .D(or_11_out), .Q(d_ff_3_q));  // open: Qn, preset, reset
  D_Flip_Flop #(.trigger("rising"), .Pre_Clr_Positions("LEGACY"), .NegatePresetClear("false"), .enable("false"), .NewFFLayout("true")) d_ff_4 (
    .clk(CLK), .D(or_12_out), .Q(d_ff_4_q));  // open: Qn, preset, reset
  D_Flip_Flop #(.trigger("rising"), .Pre_Clr_Positions("LEGACY"), .NegatePresetClear("false"), .enable("false"), .NewFFLayout("true")) d_ff_5 (
    .clk(CLK), .D(or_13_out), .Q(d_ff_5_q));  // open: Qn, preset, reset
  D_Flip_Flop #(.trigger("rising"), .Pre_Clr_Positions("LEGACY"), .NegatePresetClear("false"), .enable("false"), .NewFFLayout("true")) d_ff_6 (
    .clk(CLK), .D(or_14_out), .Q(d_ff_6_q));  // open: Qn, preset, reset
  D_Flip_Flop #(.trigger("rising"), .Pre_Clr_Positions("LEGACY"), .NegatePresetClear("false"), .enable("false"), .NewFFLayout("true")) d_ff_7 (
    .clk(CLK), .D(or_15_out), .Q(d_ff_7_q));  // open: Qn, preset, reset
  D_Flip_Flop #(.trigger("rising"), .Pre_Clr_Positions("LEGACY"), .NegatePresetClear("false"), .enable("false"), .NewFFLayout("true")) d_ff_8 (
    .clk(CLK), .D(or_16_out), .Q(d_ff_8_q));  // open: Qn, preset, reset
  not not_1 (not_1_out, v0);
  not not_2 (not_2_out, v1);
  not not_3 (not_3_out, v2);
  not not_4 (not_4_out, v3);
  not not_5 (not_5_out, v4);
  not not_6 (not_6_out, v5);
  not not_7 (not_7_out, v6);
  not not_8 (not_8_out, v7);
  Max2 max2_1 (.Y(c1), .MAX(max2_1_max), .X(c0), .Y_num(3'b001), .Max_num(max2_1_max_num), .X_num(3'b000));
  Max2 max2_2 (.Y(c3), .MAX(max2_2_max), .X(c2), .Y_num(3'b011), .Max_num(max2_2_max_num), .X_num(3'b010));
  Max2 max2_3 (.Y(c5), .MAX(max2_3_max), .X(c4), .Y_num(3'b101), .Max_num(max2_3_max_num), .X_num(3'b100));
  Max2 max2_4 (.Y(c7), .MAX(max2_4_max), .X(c6), .Y_num(3'b111), .Max_num(max2_4_max_num), .X_num(3'b110));
  nor nor_1 (MISS, hit0, hit1, hit2, hit3, hit4, hit5, hit6, hit7);
  Max2 max2_5 (
    .Y(max2_2_max), .MAX(max2_5_max), .X(max2_1_max), .Y_num(max2_2_max_num), .Max_num(max2_5_max_num),
    .X_num(max2_1_max_num));
  Max2 max2_6 (
    .Y(max2_4_max), .MAX(max2_6_max), .X(max2_3_max), .Y_num(max2_4_max_num), .Max_num(max2_6_max_num),
    .X_num(max2_3_max_num));
  Multiplexer #(.select(3), .width(2), .disabled("Z"), .enable("false")) multiplexer_10 (
    .in0(2'b00), .in1(2'b00), .in2(2'b11), .in3(2'b00), .in4(2'b01), .in5(2'b10), .in6(2'b10), .in7(2'b10),
    .out(next_status), .sel({Branch_Success, multiplexer_11_out}));
  Priority_Encoder #(.select(3), .disabled("Z")) priority_encoder_1 (
    .in0(not_1_out), .in1(not_2_out), .in2(not_3_out), .in3(not_4_out), .in4(not_5_out), .in5(not_6_out),
    .in6(not_7_out), .in7(not_8_out), .out(priority_encoder_1_out), .gs(priority_encoder_1_gs),
    .en_out(full), .en_in(1'b1));
  Max2 max2_7 (
    .Y(max2_6_max), .X(max2_5_max), .Y_num(max2_6_max_num), .Max_num(max2_7_max_num), .X_num(max2_5_max_num));  // open: MAX
  Priority_Encoder #(.select(3), .disabled("Z")) priority_encoder_2 (
    .in0(hit0), .in1(hit1), .in2(hit2), .in3(hit3), .in4(hit4), .in5(hit5), .in6(hit6), .in7(hit7),
    .out(priority_encoder_2_out));  // open: gs, en_out, en_in
  Demultiplexer #(.select(3), .width(1), .tristate("false"), .disabled("Z"), .enable("false")) demultiplexer_1 (
    .out0(demultiplexer_1_out0), .out1(demultiplexer_1_out1), .out2(demultiplexer_1_out2),
    .out3(demultiplexer_1_out3), .out4(demultiplexer_1_out4), .out5(demultiplexer_1_out5),
    .out6(demultiplexer_1_out6), .out7(demultiplexer_1_out7), .in(full), .sel(max2_7_max_num));
  Multiplexer #(.select(3), .width(2), .disabled("Z"), .enable("false")) multiplexer_11 (
    .in0(p0), .in1(p1), .in2(p2), .in3(p3), .in4(p4), .in5(p5), .in6(p6), .in7(p7), .out(multiplexer_11_out),
    .sel(priority_encoder_2_out));
  Demultiplexer #(.select(3), .width(1), .tristate("false"), .disabled("Z"), .enable("false")) demultiplexer_2 (
    .out0(demultiplexer_2_out0), .out1(demultiplexer_2_out1), .out2(demultiplexer_2_out2),
    .out3(demultiplexer_2_out3), .out4(demultiplexer_2_out4), .out5(demultiplexer_2_out5),
    .out6(demultiplexer_2_out6), .out7(demultiplexer_2_out7), .in(priority_encoder_1_gs),
    .sel(multiplexer_12_out));
  Multiplexer #(.select(1), .width(3), .disabled("Z"), .enable("false")) multiplexer_12 (
    .in0(priority_encoder_1_out), .in1(3'b000), .out(multiplexer_12_out), .sel(full));
  or or_17 (or_17_out, demultiplexer_2_out0, demultiplexer_1_out0);
  or or_18 (or_18_out, demultiplexer_2_out1, demultiplexer_1_out1);
  or or_19 (or_19_out, demultiplexer_2_out2, demultiplexer_1_out2);
  or or_20 (or_20_out, demultiplexer_2_out3, demultiplexer_1_out3);
  or or_21 (or_21_out, demultiplexer_2_out4, demultiplexer_1_out4);
  or or_22 (or_22_out, demultiplexer_2_out5, demultiplexer_1_out5);
  or or_23 (or_23_out, demultiplexer_2_out6, demultiplexer_1_out6);
  or or_24 (or_24_out, demultiplexer_2_out7, demultiplexer_1_out7);
  and and_25 (w0, MISS, EX_BRANCH, or_17_out);
  and and_26 (w1, MISS, EX_BRANCH, or_18_out);
  and and_27 (w2, MISS, EX_BRANCH, or_19_out);
  and and_28 (w3, MISS, EX_BRANCH, or_20_out);
  and and_29 (w4, MISS, EX_BRANCH, or_21_out);
  and and_30 (w5, MISS, EX_BRANCH, or_22_out);
  and and_31 (w6, MISS, EX_BRANCH, or_23_out);
  and and_32 (w7, MISS, EX_BRANCH, or_24_out);
  Priority_Encoder #(.select(3), .disabled("Z")) priority_encoder_3 (
    .in0(l0), .in1(l1), .in2(l2), .in3(l3), .in4(l4), .in5(l5), .in6(l6), .in7(l7), .out(select),
    .en_out(priority_encoder_3_en_out));  // open: gs, en_in
  Multiplexer #(.select(3), .width(1), .disabled("Z"), .enable("false")) multiplexer_13 (
    .in0(p0[1]), .in1(p1[1]), .in2(p2[1]), .in3(p3[1]), .in4(p4[1]), .in5(p5[1]), .in6(p6[1]), .in7(p7[1]),
    .out(multiplexer_13_out), .sel(select));
  Multiplexer #(.select(3), .width(32), .disabled("Z"), .enable("false")) multiplexer_14 (
    .in0(add0), .in1(add1), .in2(add2), .in3(add3), .in4(add4), .in5(add5), .in6(add6), .in7(add7),
    .out(multiplexer_14_out), .sel(select));
  Multiplexer #(.select(1), .width(1), .disabled("Z"), .enable("false")) multiplexer_15 (
    .in0(multiplexer_13_out), .in1(1'b0), .out(PREDICT_JUMP), .sel(priority_encoder_3_en_out));
  Multiplexer #(.select(1), .width(32), .disabled("Z"), .enable("false")) multiplexer_16 (
    .in0(multiplexer_14_out), .in1({32{1'b0}}), .out(JUMP_ADDR), .sel(priority_encoder_3_en_out));

  // Notes on the sheet:
  //   保存EX段PC
  //   淘汰计数
  //   保存EX段PC对应跳转地址
  //   有跳转就要记录
  //   预测跳转
  //   跳转成功记录
  //   10
  //   ^分支成功
  //   01
  //   历史预测情况
  //   分支失败-->
  //   <--分支成功
  //   分支失败-->
  //   <--分支成功
  //   11
  //   分支失败\/
  //   00
  //   找出最久未被使用的行
  //   还有空行
  //   防止行满后出现不确定值
  //   行已满
  //   行替换
  //   更新预测历史
endmodule

module Max2 (
  input  [15:0] Y,
  input  [15:0] X,
  input  [2:0] Y_num,
  input  [2:0] X_num,
  output [15:0] MAX,
  output [2:0] Max_num
);

  wire comparator_1_eq, comparator_1_gt, or_1_out;

  Multiplexer #(.select(1), .width(16), .disabled("Z"), .enable("false")) multiplexer_1 (
    .in0(Y), .in1(X), .out(MAX), .sel(or_1_out));
  Comparator #(.width(16), .mode("unsigned")) comparator_1 (
    .a(X), .b(Y), .gt(comparator_1_gt), .eq(comparator_1_eq));  // open: lt
  or or_1 (or_1_out, comparator_1_gt, comparator_1_eq);
  Multiplexer #(.select(1), .width(3), .disabled("Z"), .enable("false")) multiplexer_2 (
    .in0(Y_num), .in1(X_num), .out(Max_num), .sel(or_1_out));

  // Notes on the sheet:
  //   输出两个输入中的较大值，并输出较大值的3位编号
endmodule
